# Fritzing sketch Dual GPS Rev A (saved by Fritzing 0.9.3b)
circuit board: 13cm x 7.2cm
breadboards: 1

parts:
  LM358 = LM 358 Dual Op-Amp [package="DIP8 [THT]"]
  R1 = Resistor [tolerance=±5% resistance=1k package=THT]
  R2 = Resistor [tolerance=±5% resistance=1k package=THT]
  R3 = Resistor [tolerance=±5% resistance=1k package=THT]
  Ntrip = RGB LED - (4 legs) [package="5 mm [THT]"]
  NAV-PVT_right = ZED-F9P
  RelPosNED_left = ZED-F9P
  C1 = Electrolytic Capacitor [capacitance=0.1mF voltage=20V package="100 mil [THT, electrolytic]"]
  C2 = Electrolytic Capacitor [capacitance=0.47mF package="100 mil [THT, electrolytic]"]
  NMEA = LED - 5mm [color="Yellow (595nm)" package="5 mm [THT]"]
  RTCM = LED - 5mm [color="Green (555nm)" package="5 mm [THT]"]
  C3 = Ceramic Capacitor [capacitance=100nF package="100 mil [THT, multilayer]"]
  R4 = Resistor [tolerance=±5% resistance=100 package=THT]
  R5 = Resistor [tolerance=±5% resistance=100 package=THT]
  Ntrip_ESP32 = ESP32 Huzzah Breakout [part_number="Adafruit #4172"]
  WiFi = LED - 5mm [color="Blue (470nm)" package="5 mm [THT]"]
  R6 = Resistor [tolerance=±5% resistance=4.7k package=THT]
  Dual_GPS_ESP32 = ESP32-38PinWide [part_number=ESP32-38PinWide]
  7805 = Voltage Regulator - 5V [package="TO220 [THT]"]
  C4 = Ceramic Capacitor [capacitance=100nF package="100 mil [THT, multilayer]"]
  br = Bridge Rectifier
  J7 = DTM13-4P [package=THT]
  CNY17 = mystery part, 6 pins [chip_label=?]
  R7 = Resistor [tolerance=±5% resistance=220 package=THT]
  F1 = Fuse PCB mount [package=THT]

nets:
  N1: LM358.connector0, LM358.connector1, R4.Pin_1
  N2: LM358.connector2, NAV-PVT_right.TX, Ntrip_ESP32.RXD_5V, Dual_GPS_ESP32.GPIO27
  GND: LM358.connector3, NAV-PVT_right.GND, RelPosNED_left.GND, C1.-, C2.-, C3.1, Ntrip_ESP32.GND, Dual_GPS_ESP32.GND, 7805.GND, C4.0, br.-, CNY17.pin2
  N3: LM358.connector4, NAV-PVT_right.RX2, Ntrip_ESP32.TXD, Dual_GPS_ESP32.GPIO16
  N4: LM358.connector5, LM358.connector6, R5.Pin_1
  5V: LM358.connector7, NAV-PVT_right.5V, RelPosNED_left.5V, C2.+, NMEA.anode, RTCM.anode, C3.0, Ntrip_ESP32.VBAT, Dual_GPS_ESP32.VIN, 7805.output_voltage, C4.1
  N5: R1.Pin_0, Ntrip_ESP32.GPIO22
  N6: R1.Pin_1, Ntrip.blue_cathode
  N7: R2.Pin_0, Ntrip_ESP32.GPIO23
  N8: R2.Pin_1, Ntrip.green_cathode
  N9: R3.Pin_0, Ntrip_ESP32.GPIO21
  N10: R3.Pin_1, Ntrip.red_cathode
  N11: Ntrip.common_anode, Ntrip_ESP32.3.3V
  N12: NAV-PVT_right.TX2, RelPosNED_left.RX2
  N13: RelPosNED_left.TX, Dual_GPS_ESP32.GPIO25
  N14: C1.+, 7805.input_voltage, br.+
  N15: NMEA.cathode, R4.Pin_0
  N16: RTCM.cathode, R5.Pin_0
  N17: WiFi.cathode, R6.Pin_1
  N18: WiFi.anode, Dual_GPS_ESP32.3.3
  N19: R6.Pin_0, Dual_GPS_ESP32.GPIO32
  N20: Dual_GPS_ESP32.GPIO15, R7.Pin_1
  N21: br.~#1, J7.pin_4
  N22: br.~#3, J7.pin_2
  N23: J7.pin_1, CNY17.pin4
  N24: J7.pin_3, F1.pin2
  N25: CNY17.pin1, R7.Pin_0
  N26: CNY17.pin5, F1.pin1

notes:
  Rev B
  Copyright Silicon Reparation 2021
  License GPLv3 PCB design
  Gnd
  Antenna
  ____________

custom parts:
  ZED-F9P: A breakout board made by Sparkfun with the Ublox ZED-F9P, in the vein of Qwiic boards.
  ZED-F9P: A breakout board made by Sparkfun with the Ublox ZED-F9P, in the vein of Qwiic boards.
  ESP32 Huzzah Breakout: Squeeeeze down your next ESP32 project to its bare-bones essential with the Adafruit HUZZAH32 Breakout. This breakout is basically the 'big sister' of our HUZZAH 8266, but instead of an ESP8266 it has the '32! We've pared down our popular Feather ESP32, removing the battery charger and USB-serial converter. You just get a regulator, some protection diodes, two buttons and an LED. For some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
  ESP32-38PinWide: Generic 38-Pin ESP32 with wide format (only access to one side of pins on a breadboard) based on Stephen Lilley's HiLetgo ESP-WROOM-32 ESP32 ESP-32S Development Board.
  DTM13-4P: DTM13-4P connector.
  Fuse PCB mount: A PCB mount fuse with 200 mil spacing.
