# Fritzing sketch Dual GPS Rev C (saved by Fritzing 0.9.9b)
circuit board: 13cm x 7.09999cm
breadboards: 1

parts:
  J0 = Resistor [tolerance=±5% resistance=0 power=0.25 package=THT]
  J8 = DTM13-4P [package=THT]
  CNY17 = mystery part, 6 pins [chip_label=?]
  R10 = Resistor [tolerance=±5% resistance=220 power=0.25 package=THT]
  78E05 = Voltage Regulator - 5V [package="TO220 [THT]"]
  F9P_RelPosNED_left_orange = ZED-F9P
  br = Bridge Rectifier
  R11 = Resistor [tolerance=±5% resistance=4.7k power=0.25 package=THT]
  Dual_GPS_ESP32 = ESP32-38PinWide [part_number=ESP32-38PinWide]
  F9P_NAV-PVT_right_purple = ZED-F9P
  C4 = Electrolytic Capacitor [capacitance=0.1mF voltage=20V package="100 mil [THT, electrolytic]"]
  C5 = Electrolytic Capacitor [capacitance=0.47mF voltage=35V package="100 mil [THT, electrolytic]"]
  RTCM = LED - 5mm [color="Green (555nm)" current=0.030 package="5 mm [THT]"]
  WiFi = LED - 5mm [color="Blue (470nm)" current=0.030 package="5 mm [THT]"]
  NMEA = LED - 5mm [color="Yellow (595nm)" current=0.030 package="5 mm [THT]"]
  C6 = Ceramic Capacitor [capacitance=100nF package="100 mil [THT, multilayer]"]
  R1 = Resistor [tolerance=±5% resistance=100 power=0.25 package=THT]
  R2 = Resistor [tolerance=±5% resistance=100 power=0.25 package=THT]
  Ntrip_ESP32 = ESP32 Huzzah Breakout [part_number="Adafruit #4172"]
  R14 = Resistor [tolerance=±5% resistance=2.2k power=0.25 package=THT]
  R15 = Resistor [tolerance=±5% resistance=1k power=0.25 package=THT]
  R16 = Resistor [tolerance=±5% resistance=1k power=0.25 package=THT]
  Ntrip = RGB LED - (4 legs) [package="5 mm [THT]"]
  LM358 = LM 358 Dual Op-Amp [package="DIP8 [THT]"]
  R17 = Resistor [tolerance=±5% resistance=680 power=0.25 package=THT]
  sourcing_/_sinking = mystery part, 3 pins [chip_label=?]
  LM358_2 = LM 358 Dual Op-Amp [package="DIP8 [THT]"]
  RX = LED - 5mm [color="Green (555nm)" current=0.030 package="5 mm [THT]"]
  R3 = Resistor [tolerance=±5% resistance=100 power=0.25 package=THT]
  TX = LED - 5mm [color="Yellow (595nm)" current=0.030 package="5 mm [THT]"]
  R4 = Resistor [tolerance=±5% resistance=100 power=0.25 package=THT]
  F2 = Fuse PCB mount [package=THT]
  F1 = Fuse PCB mount [package=THT]

nets:
  N1: J0.Pin_0, F9P_NAV-PVT_right_purple.RX2, Ntrip_ESP32.TXD, LM358.connector4
  N2: J0.Pin_1, Dual_GPS_ESP32.GPIO16
  N3: J8.pin_1, F2.pin1
  N4: J8.pin_2, br.~#3
  N5: J8.pin_3, CNY17.pin5
  N6: J8.pin_4, F1.pin2
  N7: CNY17.pin1, R10.Pin_0
  GND: CNY17.pin2, 78E05.GND, F9P_RelPosNED_left_orange.GND, br.-, Dual_GPS_ESP32.GND, F9P_NAV-PVT_right_purple.GND, C4.-, C5.-, C6.1, Ntrip_ESP32.GND, LM358.connector3, LM358_2.connector3
  N8: CNY17.pin4, sourcing_/_sinking.pin2, F2.pin2
  N9: R10.Pin_1, Dual_GPS_ESP32.GPIO15
  N10: 78E05.input_voltage, br.+, C4.+, R17.Pin_1
  5V: 78E05.output_voltage, F9P_RelPosNED_left_orange.5V, Dual_GPS_ESP32.VIN, F9P_NAV-PVT_right_purple.5V, C5.+, RTCM.anode, NMEA.anode, C6.0, Ntrip_ESP32.VBAT, LM358.connector7, LM358_2.connector7, RX.anode, TX.anode
  N11: F9P_RelPosNED_left_orange.TX, Dual_GPS_ESP32.GPIO25, LM358_2.connector4
  N12: F9P_RelPosNED_left_orange.RX2, F9P_NAV-PVT_right_purple.TX2, LM358_2.connector2
  N13: br.~#1, F1.pin1
  N14: R11.Pin_0, Dual_GPS_ESP32.GPIO32
  N15: R11.Pin_1, WiFi.cathode
  N16: Dual_GPS_ESP32.3.3, WiFi.anode
  N17: Dual_GPS_ESP32.GPIO27, F9P_NAV-PVT_right_purple.TX, Ntrip_ESP32.RXD_5V, LM358.connector2
  N18: RTCM.cathode, R1.Pin_0
  N19: NMEA.cathode, R2.Pin_0
  N20: R1.Pin_1, LM358.connector5, LM358.connector6
  N21: R2.Pin_1, LM358.connector0, LM358.connector1
  N22: Ntrip_ESP32.3.3V, Ntrip.common_anode
  N23: Ntrip_ESP32.GPIO23, R15.Pin_0
  N24: Ntrip_ESP32.GPIO22, R16.Pin_0
  N25: Ntrip_ESP32.GPIO21, R14.Pin_0
  N26: R14.Pin_1, Ntrip.red_cathode
  N27: R15.Pin_1, Ntrip.green_cathode
  N28: R16.Pin_1, Ntrip.blue_cathode
  N29: R17.Pin_0, sourcing_/_sinking.pin1
  N30: LM358_2.connector0, LM358_2.connector1, R4.Pin_0
  N31: LM358_2.connector5, LM358_2.connector6, R3.Pin_0
  N32: RX.cathode, R4.Pin_1
  N33: R3.Pin_1, TX.cathode

notes:
  License GPLv3 PCB design
  Copyright Reuben Rissler 2022
  ___________
  Antenna
  Rev C
  Heading
  Roll

custom parts:
  DTM13-4P: DTM13-4P connector.
  Voltage Regulator - 5V: 5V DC Voltage Regulator
  ZED-F9P: A breakout board made by Sparkfun with the Ublox ZED-F9P, in the vein of Qwiic boards.
  ESP32-38PinWide: Generic 38-Pin ESP32 with wide format (only access to one side of pins on a breadboard) based on Stephen Lilley's HiLetgo ESP-WROOM-32 ESP32 ESP-32S Development Board.
  ZED-F9P: A breakout board made by Sparkfun with the Ublox ZED-F9P, in the vein of Qwiic boards.
  ESP32 Huzzah Breakout: Squeeeeze down your next ESP32 project to its bare-bones essential with the Adafruit HUZZAH32 Breakout. This breakout is basically the 'big sister' of our HUZZAH 8266, but instead of an ESP8266 it has the '32! We've pared down our popular Feather ESP32, removing the battery charger and USB-serial converter. You just get a regulator, some protection diodes, two buttons and an LED. For some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
  Fuse PCB mount: A PCB mount PTC fuse with 5mm spacing.
