# Fritzing sketch Dual GPS Rev G (saved by Fritzing 1.0.1rc)
circuit board: 13cm x 7.09999cm
breadboards: 1

parts:
  J8 = DTM13-4P [package=THT]
  CNY17 = mystery part, 6 pins [chip_label=?]
  R12 = Resistor [tolerance=±5% resistance=10 power=0.25 package=THT]
  F9P_RelPosNED_left_orange = ZED-F9P
  R15 = Resistor [tolerance=±5% resistance=470 power=0.25 package=THT]
  Dual_GPS_ESP32 = ESP32-38PinWide [part_number=ESP32-38PinWide]
  F9P_NAV-PVT_right_purple = ZED-F9P
  WiFi = LED - 5mm [color="Yellow (595nm)" current=0.030 package="5 mm [THT]"]
  C1 = Ceramic Capacitor [capacitance=100nF voltage=35V package="100 mil [THT, multilayer]"]
  LM358 = LM 358 Dual Op-Amp [package="DIP8 [THT]"]
  LM358_2 = LM 358 Dual Op-Amp [package="DIP8 [THT]"]
  RX = LED - 5mm [color="Green (555nm)" current=0.030 package="5 mm [THT]"]
  R3 = Resistor [tolerance=±5% resistance=100 power=0.25 package=THT]
  TX = LED - 5mm [color="Yellow (595nm)" current=0.030 package="5 mm [THT]"]
  R4 = Resistor [tolerance=±5% resistance=100 power=0.25 package=THT]
  F2 = Fuse PCB mount [package=THT]
  Speed = LED - 5mm [color="Yellow (595nm)" current=0.030 package="5 mm [THT]"]
  J1 = female pin header, 6 pins [form="♀ (female)"]
  MAX700 = mystery part, 8 pins [chip_label=?]
  R6 = Resistor [tolerance=±1% power=0.25W resistance=10k package=THT]
  R8 = Resistor [tolerance=±1% power=0.25W resistance=1k package=THT]
  R10 = Resistor [tolerance=±5% power=0.25W resistance=7.32k package=THT]
  D1 = Rectifier Diode [part_number=1N4001 package="300 mil [THT]"]
  D2 = Rectifier Diode [part_number=1N4001 package="300 mil [THT]"]
  C3 = Ceramic Capacitor [capacitance=100nF voltage=35V package="100 mil [THT, multilayer]"]
  C4 = Ceramic Capacitor [capacitance=100nF voltage=35V package="100 mil [THT, multilayer]"]
  F1 = Fuse PCB mount [package=THT]
  78E05 = Voltage Regulator - 5V [package="TO220 [THT]"]
  C6 = Electrolytic Capacitor [capacitance=47µF voltage=25V package="100 mil [THT, electrolytic]"]
  C7 = Electrolytic Capacitor [capacitance=0.1mF voltage=6.3V package="100 mil [THT, electrolytic]"]
  NTRIP_ESP33 = ESP32 Huzzah Breakout [part_number="Adafruit #4172"]
  RTCM = LED - 5mm [color="Green (555nm)" current=0.030 package="5 mm [THT]"]
  NMEA = LED - 5mm [color="Yellow (595nm)" current=0.030 package="5 mm [THT]"]
  R1 = Resistor [tolerance=±5% resistance=100 power=0.25 package=THT]
  R2 = Resistor [tolerance=±5% resistance=100 power=0.25 package=THT]
  R26 = Resistor [tolerance=±5% resistance=2.2k power=0.25 package=THT]
  R23 = Resistor [tolerance=±5% resistance=1k power=0.25 package=THT]
  R22 = Resistor [tolerance=±5% resistance=1k power=0.25 package=THT]
  R20 = Resistor [tolerance=±5% resistance=10k power=0.25 package=THT]
  R17 = Resistor [tolerance=±5% power=0.25W resistance=330 package=THT]
  DC_good = LED - 5mm [color="Red (633nm)" current=0.030A package="5 mm [THT]"]
  R14 = Resistor [tolerance=±5% power=0.25W resistance=470 package=THT]
  Ntrip = RGB LED - (4 legs) [color="Red (633nm)" current=0.030A package="5 mm [THT]"]
  R24 = Resistor [tolerance=±5% power=0.25W resistance=1k package=THT]
  Speed_output = LED - 5mm [color="Yellow (595nm)" current=0.030 package="5 mm [THT]"]
  C2 = Ceramic Capacitor [capacitance=100nF voltage=35V package="100 mil [THT, multilayer]"]

nets:
  N1: J8.pin_1, F2.pin1, Speed_output.cathode
  N2: J8.pin_2, D1.anode
  N3: J8.pin_3, CNY17.pin5
  GND: J8.pin_4, CNY17.pin2, F9P_RelPosNED_left_orange.GND, Dual_GPS_ESP32.GND, F9P_NAV-PVT_right_purple.GND, C1.1, LM358.connector3, LM358_2.connector3, MAX700.pin4, R8.Pin_1, C3.1, C4.1, 78E05.GND, C6.-, C7.-, NTRIP_ESP33.GND, R17.Pin_0, R14.Pin_0, C2.1
  N4: CNY17.pin1, R12.Pin_0
  N5: CNY17.pin4, F2.pin2
  N6: R12.Pin_1, Speed.cathode
  N7: F9P_RelPosNED_left_orange.RST, F9P_NAV-PVT_right_purple.RST, D2.anode, R20.Pin_0
  N8: F9P_RelPosNED_left_orange.TX, Dual_GPS_ESP32.GPIO25, LM358_2.connector4
  N9: F9P_RelPosNED_left_orange.RX2, F9P_NAV-PVT_right_purple.TX2, LM358_2.connector2, J1.pin5
  5V: F9P_RelPosNED_left_orange.5V, Dual_GPS_ESP32.VIN, F9P_NAV-PVT_right_purple.5V, C1.0, LM358.connector7, LM358_2.connector7, RX.anode, TX.anode, MAX700.pin7, MAX700.pin8, C3.0, 78E05.output_voltage, C7.+, NTRIP_ESP33.VBAT, RTCM.anode, NMEA.anode, C2.0
  N10: R15.Pin_0, Dual_GPS_ESP32.GPIO32
  N11: R15.Pin_1, WiFi.cathode
  N12: Dual_GPS_ESP32.3.3, WiFi.anode
  N13: Dual_GPS_ESP32.GPIO27, F9P_NAV-PVT_right_purple.TX, LM358.connector2, J1.pin1, NTRIP_ESP33.RXD_5V
  N14: Dual_GPS_ESP32.GPIO15, Speed.anode
  N15: Dual_GPS_ESP32.GPIO5, R20.Pin_1
  N16: F9P_NAV-PVT_right_purple.RX, LM358.connector4, J1.pin2, NTRIP_ESP33.TXD
  N17: F9P_NAV-PVT_right_purple.CS, J1.pin3
  N18: F9P_NAV-PVT_right_purple.RX2, J1.pin4
  N19: F9P_NAV-PVT_right_purple.3V3, J1.pin6
  N20: LM358.connector0, LM358.connector1, R2.Pin_1
  N21: LM358.connector5, LM358.connector6, R1.Pin_1
  N22: LM358_2.connector0, LM358_2.connector1, R4.Pin_0
  N23: LM358_2.connector5, LM358_2.connector6, R3.Pin_0
  N24: RX.cathode, R4.Pin_1
  N25: R3.Pin_1, TX.cathode
  N26: MAX700.pin2, R6.Pin_0, R8.Pin_0, R10.Pin_1, C4.0
  N27: MAX700.pin3, R6.Pin_1
  N28: MAX700.pin5, D2.cathode, DC_good.anode, R14.Pin_1
  N29: R10.Pin_0, F1.pin2, 78E05.input_voltage, C6.+
  N30: D1.cathode, F1.pin1, R24.Pin_0
  N31: NTRIP_ESP33.3.3V, Ntrip.common_anode
  N32: NTRIP_ESP33.GPIO23, R23.Pin_0
  N33: NTRIP_ESP33.GPIO22, R22.Pin_0
  N34: NTRIP_ESP33.GPIO21, R26.Pin_0
  N35: RTCM.cathode, R1.Pin_0
  N36: NMEA.cathode, R2.Pin_0
  N37: R26.Pin_1, Ntrip.red_cathode
  N38: R23.Pin_1, Ntrip.green_cathode
  N39: R22.Pin_1, Ntrip.blue_cathode
  N40: R17.Pin_1, DC_good.cathode
  N41: R24.Pin_1, Speed_output.anode

notes:
  License GPLv3 PCB design
  Copyright Reuben Rissler 2024
  ___________
  Antenna
  Rev G
  Heading
  Roll

custom parts:
  DTM13-4P: DTM13-4P connector.
  ZED-F9P: A breakout board made by Sparkfun with the Ublox ZED-F9P, in the vein of Qwiic boards.
  ESP32-38PinWide: Generic 38-Pin ESP32 with wide format (only access to one side of pins on a breadboard) based on Stephen Lilley's HiLetgo ESP-WROOM-32 ESP32 ESP-32S Development Board.
  ZED-F9P: A breakout board made by Sparkfun with the Ublox ZED-F9P, in the vein of Qwiic boards.
  Fuse PCB mount: A PCB mount PTC fuse with 5mm spacing.
  Voltage Regulator - 5V: 5V DC Voltage Regulator
  ESP32 Huzzah Breakout: Squeeeeze down your next ESP32 project to its bare-bones essential with the Adafruit HUZZAH32 Breakout. This breakout is basically the 'big sister' of our HUZZAH 8266, but instead of an ESP8266 it has the '32! We've pared down our popular Feather ESP32, removing the battery charger and USB-serial converter. You just get a regulator, some protection diodes, two buttons and an LED. For some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
