# Fritzing sketch Dual GPS Serial Rev B (saved by Fritzing 0.9.9b)
circuit board: 13cm x 7.09999cm
breadboards: 1

parts:
  CNY17 = mystery part, 6 pins [chip_label=?]
  R7 = Resistor [tolerance=±5% resistance=10 power=0.25 package=THT]
  78E05 = Voltage Regulator - 5V [package="TO220 [THT]"]
  F9P_RelPosNED_left_orange = ZED-F9P
  br = Bridge Rectifier
  R10 = Resistor [tolerance=±5% resistance=470 power=0.25 package=THT]
  Dual_GPS_ESP32 = ESP32-38PinWide [part_number=ESP32-38PinWide]
  F9P_NAV-PVT_right_purple = ZED-F9P
  C4 = Electrolytic Capacitor [capacitance=47µF voltage=25V package="100 mil [THT, electrolytic]"]
  C5 = Electrolytic Capacitor [capacitance=0.1mF voltage=6.3V package="100 mil [THT, electrolytic]"]
  RTCM = LED - 5mm [color="Green (555nm)" current=0.030 package="5 mm [THT]"]
  WiFi = LED - 5mm [color="Blue (470nm)" current=0.030 package="5 mm [THT]"]
  NMEA = LED - 5mm [color="Yellow (595nm)" current=0.030 package="5 mm [THT]"]
  C6 = Ceramic Capacitor [capacitance=100nF voltage=35V package="100 mil [THT, multilayer]"]
  R1 = Resistor [tolerance=±5% resistance=100 power=0.25 package=THT]
  R2 = Resistor [tolerance=±5% resistance=100 power=0.25 package=THT]
  Ntrip_ESP32 = ESP32 Huzzah Breakout [part_number="Adafruit #4172"]
  R14 = Resistor [tolerance=±5% resistance=2.2k power=0.25 package=THT]
  R15 = Resistor [tolerance=±5% resistance=1k power=0.25 package=THT]
  R16 = Resistor [tolerance=±5% resistance=1k power=0.25 package=THT]
  Ntrip = RGB LED - (4 legs) [package="5 mm [THT]"]
  LM358 = LM 358 Dual Op-Amp [package="DIP8 [THT]"]
  R20 = Resistor [tolerance=±5% resistance=680 power=0.25 package=THT]
  source/sink = mystery part, 3 pins [chip_label=?]
  LM358_2 = LM 358 Dual Op-Amp [package="DIP8 [THT]"]
  RX = LED - 5mm [color="Green (555nm)" current=0.030 package="5 mm [THT]"]
  R3 = Resistor [tolerance=±5% resistance=100 power=0.25 package=THT]
  TX = LED - 5mm [color="Yellow (595nm)" current=0.030 package="5 mm [THT]"]
  R4 = Resistor [tolerance=±5% resistance=100 power=0.25 package=THT]
  F2 = Fuse PCB mount [package=THT]
  F1 = Fuse PCB mount [package=THT]
  6N137 = 6n137 Optocoupler [chip_label=6n137 package="DIP (Dual Inline) [THT]"]
  R11 = Resistor [tolerance=±5% power=0.25 resistance=470 package=THT]
  C8 = Ceramic Capacitor [capacitance=100nF voltage=35V package="100 mil [THT, multilayer]"]
  2N3906 = PNP-Transistor [package="TO92 [THT]"]
  R23 = Resistor [tolerance=±5% power=0.25 resistance=330 package=THT]
  R19 = Resistor [tolerance=±5% power=0.25 resistance=220 package=THT]
  P1 = DTM13-6P [package=THT]
  J1 = female pin header, 6 pins [form="♀ (female)"]
  -3_3+ = female pin header, 2 pins [form="♀ (female)"]
  RO-0505S = Isolated regulator [part_number=RO-0505S package=THT]
  Speed_out = LED - 5mm [color="Yellow (595nm)" current=0.030 package="5 mm [THT]"]
  RS-232 = LED - 5mm [color="Yellow (595nm)" current=0.030 package="5 mm [THT]"]
  MAX202 = mystery part, 16 pins [chip_label=Max202]
  C9 = Ceramic Capacitor [capacitance=100nF voltage=35V package="100 mil [THT, multilayer]"]
  C11 = Ceramic Capacitor [capacitance=100nF voltage=35V package="100 mil [THT, multilayer]"]
  C12 = Ceramic Capacitor [capacitance=100nF voltage=35V package="100 mil [THT, multilayer]"]
  C10 = Ceramic Capacitor [capacitance=100nF voltage=35V package="100 mil [THT, multilayer]"]
  C13 = Ceramic Capacitor [capacitance=100nF voltage=35V package="100 mil [THT, multilayer]"]
  C14 = Ceramic Capacitor [capacitance=100nF voltage=35V package="100 mil [THT, multilayer]"]
  R5 = Resistor [tolerance=±5% power=0.25 resistance=100 package=THT]

nets:
  N1: CNY17.pin1, R7.Pin_0
  GND: CNY17.pin2, 78E05.GND, F9P_RelPosNED_left_orange.GND, br.-, Dual_GPS_ESP32.GND, F9P_NAV-PVT_right_purple.GND, C4.-, C5.-, C6.1, Ntrip_ESP32.GND, LM358.connector3, LM358_2.connector3, 6N137.Vf-, -3_3+.pin1, RO-0505S.-VIN, C14.0
  N2: CNY17.pin4, source/sink.pin2, F2.pin2
  N3: CNY17.pin5, P1.pin_3
  N4: R7.Pin_1, Speed_out.cathode
  N5: 78E05.input_voltage, br.+, C4.+, R20.Pin_1
  5V: 78E05.output_voltage, F9P_RelPosNED_left_orange.5V, Dual_GPS_ESP32.VIN, F9P_NAV-PVT_right_purple.5V, C5.+, RTCM.anode, NMEA.anode, C6.0, Ntrip_ESP32.VBAT, LM358.connector7, LM358_2.connector7, RX.anode, TX.anode, RO-0505S.+VIN, C14.1
  N6: F9P_RelPosNED_left_orange.TX, Dual_GPS_ESP32.GPIO25, LM358_2.connector4
  N7: F9P_RelPosNED_left_orange.RX2, F9P_NAV-PVT_right_purple.TX2, LM358_2.connector2, J1.pin5
  N8: br.~#1, F1.pin1
  N9: br.~#3, P1.pin_2
  N10: R10.Pin_0, Dual_GPS_ESP32.GPIO32
  N11: R10.Pin_1, WiFi.cathode
  N12: Dual_GPS_ESP32.3.3, WiFi.anode, 2N3906.E
  N13: Dual_GPS_ESP32.GPIO27, F9P_NAV-PVT_right_purple.TX, Ntrip_ESP32.RXD_5V, LM358.connector2, J1.pin1
  N14: Dual_GPS_ESP32.GPIO15, Speed_out.anode
  N15: Dual_GPS_ESP32.GPIO19, R11.Pin_0
  N16: F9P_NAV-PVT_right_purple.RX, Ntrip_ESP32.TXD, LM358.connector4, J1.pin2
  N17: F9P_NAV-PVT_right_purple.CS, J1.pin3
  N18: F9P_NAV-PVT_right_purple.RX2, J1.pin4
  N19: F9P_NAV-PVT_right_purple.3V3, J1.pin6
  N20: RTCM.cathode, R1.Pin_0
  N21: NMEA.cathode, R2.Pin_0
  N22: R1.Pin_1, LM358.connector5, LM358.connector6
  N23: R2.Pin_1, LM358.connector0, LM358.connector1
  N24: Ntrip_ESP32.3.3V, Ntrip.common_anode, -3_3+.pin2
  N25: Ntrip_ESP32.GPIO23, R15.Pin_0
  N26: Ntrip_ESP32.GPIO22, R16.Pin_0
  N27: Ntrip_ESP32.GPIO21, R14.Pin_0
  N28: R14.Pin_1, Ntrip.red_cathode
  N29: R15.Pin_1, Ntrip.green_cathode
  N30: R16.Pin_1, Ntrip.blue_cathode
  N31: R20.Pin_0, source/sink.pin1
  N32: LM358_2.connector0, LM358_2.connector1, R4.Pin_0
  N33: LM358_2.connector5, LM358_2.connector6, R3.Pin_0
  N34: RX.cathode, R4.Pin_1
  N35: R3.Pin_1, TX.cathode
  N36: F2.pin1, P1.pin_1
  N37: F1.pin2, P1.pin_4
  N38: 6N137.Vf+, R23.Pin_0
  N39: 6N137.GND, C8.0, P1.pin_5, RO-0505S.-VOUT, MAX202.pin15, C10.0, C13.0
  N40: 6N137.Vo, R19.Pin_0, RS-232.cathode, MAX202.pin10
  N41: 6N137.Vcc, C8.1, R19.Pin_1, RO-0505S.+VOUT, MAX202.pin16, C9.1, C10.1, R5.Pin_1
  N42: R11.Pin_1, 2N3906.B
  N43: 2N3906.C, R23.Pin_1
  N44: P1.pin_6, MAX202.pin7
  N45: RS-232.anode, R5.Pin_0
  N46: MAX202.pin1, C11.1
  N47: MAX202.pin2, C9.0
  N48: MAX202.pin3, C11.0
  N49: MAX202.pin4, C12.1
  N50: MAX202.pin5, C12.0
  N51: MAX202.pin6, C13.1

notes:
  License GPLv3 PCB design
  Copyright Reuben Rissler 2023
  ___________
  Antenna
  Rev B
  Heading
  Roll

custom parts:
  Voltage Regulator - 5V: 5V DC Voltage Regulator
  ZED-F9P: A breakout board made by Sparkfun with the Ublox ZED-F9P, in the vein of Qwiic boards.
  ESP32-38PinWide: Generic 38-Pin ESP32 with wide format (only access to one side of pins on a breadboard) based on Stephen Lilley's HiLetgo ESP-WROOM-32 ESP32 ESP-32S Development Board.
  ZED-F9P: A breakout board made by Sparkfun with the Ublox ZED-F9P, in the vein of Qwiic boards.
  ESP32 Huzzah Breakout: Squeeeeze down your next ESP32 project to its bare-bones essential with the Adafruit HUZZAH32 Breakout. This breakout is basically the 'big sister' of our HUZZAH 8266, but instead of an ESP8266 it has the '32! We've pared down our popular Feather ESP32, removing the battery charger and USB-serial converter. You just get a regulator, some protection diodes, two buttons and an LED. For some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
  Fuse PCB mount: A PCB mount PTC fuse with 5mm spacing.
  6n137 Optocoupler: 6n137 fast Optocoupler. With 8 pins on a 300mil dual inline package (DIP) footprint. Ve is strobe input. Output is inverting.
  DTM13-6P: DTM13-6P connector.
  Isolated regulator: An isolated DC/DC regulator made by Recom.
