# Fritzing sketch Dual GPS Serial Rev E (saved by Fritzing 1.0.1rc)
circuit board: 13cm x 7.09999cm
breadboards: 1

parts:
  CNY17 = mystery part, 6 pins [chip_label=?]
  R7 = Resistor [tolerance=±5% resistance=10 power=0.25 package=THT]
  78E05 = Voltage Regulator - 5V [package="TO220 [THT]"]
  F9P_RelPosNED_left_orange = ZED-F9P
  R10 = Resistor [tolerance=±5% resistance=470 power=0.25 package=THT]
  Dual_GPS_ESP32 = ESP32-38PinWide [part_number=ESP32-38PinWide]
  F9P_NAV-PVT_right_purple = ZED-F9P
  C4 = Electrolytic Capacitor [capacitance=47µF voltage=25V package="100 mil [THT, electrolytic]"]
  C5 = Electrolytic Capacitor [capacitance=0.1mF voltage=6.3V package="100 mil [THT, electrolytic]"]
  RTCM = LED - 5mm [color="Green (555nm)" current=0.030 package="5 mm [THT]"]
  WiFi = LED - 5mm [color="Blue (470nm)" current=0.030 package="5 mm [THT]"]
  NMEA = LED - 5mm [color="Yellow (595nm)" current=0.030 package="5 mm [THT]"]
  C6 = Ceramic Capacitor [capacitance=100nF voltage=35V package="100 mil [THT, multilayer]"]
  R1 = Resistor [tolerance=±5% resistance=100 power=0.25 package=THT]
  R2 = Resistor [tolerance=±5% resistance=100 power=0.25 package=THT]
  R14 = Resistor [tolerance=±5% resistance=2.2k power=0.25 package=THT]
  R15 = Resistor [tolerance=±5% resistance=1k power=0.25 package=THT]
  R16 = Resistor [tolerance=±5% resistance=1k power=0.25 package=THT]
  LM358 = LM 358 Dual Op-Amp [package="DIP8 [THT]"]
  LM358_2 = LM 358 Dual Op-Amp [package="DIP8 [THT]"]
  RX = LED - 5mm [color="Green (555nm)" current=0.030 package="5 mm [THT]"]
  R3 = Resistor [tolerance=±5% resistance=100 power=0.25 package=THT]
  TX = LED - 5mm [color="Yellow (595nm)" current=0.030 package="5 mm [THT]"]
  R4 = Resistor [tolerance=±5% resistance=100 power=0.25 package=THT]
  F2 = Fuse PCB mount [package=THT]
  F1 = Fuse PCB mount [package=THT]
  6N137 = 6n137 Optocoupler [chip_label=6n137 package="DIP (Dual Inline) [THT]"]
  R11 = Resistor [tolerance=±5% power=0.25 resistance=470 package=THT]
  C8 = Ceramic Capacitor [capacitance=100nF voltage=35V package="100 mil [THT, multilayer]"]
  2N3906 = PNP-Transistor [package="TO92 [THT]"]
  R23 = Resistor [tolerance=±5% power=0.25 resistance=330 package=THT]
  R19 = Resistor [tolerance=±5% power=0.25 resistance=220 package=THT]
  P1 = DTM13-6P [package=THT]
  J1 = female pin header, 6 pins [form="♀ (female)"]
  RO-0505S = Isolated regulator [part_number=RO-0505S package=THT]
  Speed_out = LED - 5mm [color="Yellow (595nm)" current=0.030 package="5 mm [THT]"]
  RS-232 = LED - 5mm [color="Yellow (595nm)" current=0.030 package="5 mm [THT]"]
  MAX202 = mystery part, 16 pins [chip_label=Max202]
  C9 = Ceramic Capacitor [capacitance=100nF voltage=35V package="100 mil [THT, multilayer]"]
  C11 = Ceramic Capacitor [capacitance=100nF voltage=35V package="100 mil [THT, multilayer]"]
  C12 = Ceramic Capacitor [capacitance=100nF voltage=35V package="100 mil [THT, multilayer]"]
  C10 = Ceramic Capacitor [capacitance=100nF voltage=35V package="100 mil [THT, multilayer]"]
  C13 = Ceramic Capacitor [capacitance=100nF voltage=35V package="100 mil [THT, multilayer]"]
  R5 = Resistor [tolerance=±5% power=0.25 resistance=100 package=THT]
  Ntrip = RGB LED - (4 legs) [color="Red (633nm)" current=0.030A package="5 mm [THT]"]
  MAX700 = mystery part, 8 pins [chip_label=?]
  NTRIP_ESP32 = ESP32 Huzzah Breakout [part_number="Adafruit #4172"]
  D1 = Rectifier Diode [part_number=1N4001 package="300 mil [THT]"]
  C18 = Ceramic Capacitor [capacitance=100nF voltage=35V package="100 mil [THT, multilayer]"]
  3_3 = mystery part, 2 pins [chip_label=?]
  R17 = Resistor [tolerance=±1% power=0.25W resistance=1k package=THT]
  R25 = Resistor [tolerance=±1% power=0.25W resistance=10k package=THT]
  R26 = Resistor [tolerance=±5% power=0.25W resistance=7.32k package=THT]
  C19 = Ceramic Capacitor [capacitance=100nF voltage=35V package="100 mil [THT, multilayer]"]
  D2 = Rectifier Diode [part_number=1N4001 package="300 mil [THT]"]
  DC_good = LED - 5mm [color="Green (565nm)" current=0.030A package="5 mm [THT]"]
  R12 = Resistor [tolerance=±5% power=0.25W resistance=470 package=THT]
  R22 = Resistor [tolerance=±5% power=0.25W resistance=330 package=THT]
  R29 = Resistor [tolerance=±5% resistance=10k power=0.25 package=THT]
  232 = mystery part, 3 pins [chip_label=?]

nets:
  N1: CNY17.pin1, R7.Pin_0
  GND: CNY17.pin2, 78E05.GND, F9P_RelPosNED_left_orange.GND, Dual_GPS_ESP32.GND, F9P_NAV-PVT_right_purple.GND, C4.-, C5.-, C6.1, LM358.connector3, LM358_2.connector3, 6N137.Vf-, P1.pin_4, RO-0505S.-VIN, MAX700.pin4, NTRIP_ESP32.GND, C18.1, R17.Pin_1, C19.1, R12.Pin_0, R22.Pin_0
  N2: CNY17.pin4, F2.pin2
  N3: CNY17.pin5, P1.pin_3
  N4: R7.Pin_1, Speed_out.cathode
  N5: 78E05.input_voltage, C4.+, F1.pin2, R26.Pin_0
  5V: 78E05.output_voltage, F9P_RelPosNED_left_orange.5V, Dual_GPS_ESP32.VIN, F9P_NAV-PVT_right_purple.5V, C5.+, RTCM.anode, NMEA.anode, C6.0, LM358.connector7, LM358_2.connector7, RX.anode, TX.anode, RO-0505S.+VIN, MAX700.pin7, MAX700.pin8, NTRIP_ESP32.VBAT, C18.0
  N6: F9P_RelPosNED_left_orange.RST, F9P_NAV-PVT_right_purple.RST, D2.anode, R29.Pin_0
  N7: F9P_RelPosNED_left_orange.TX, Dual_GPS_ESP32.GPIO25, LM358_2.connector4
  N8: F9P_RelPosNED_left_orange.RX2, F9P_NAV-PVT_right_purple.TX2, LM358_2.connector2, J1.pin5, 232.pin3
  N9: R10.Pin_0, Dual_GPS_ESP32.GPIO32
  N10: R10.Pin_1, WiFi.cathode
  N11: Dual_GPS_ESP32.3.3, WiFi.anode, 2N3906.E, 3_3.pin1
  N12: Dual_GPS_ESP32.GPIO27, F9P_NAV-PVT_right_purple.TX, LM358.connector2, J1.pin1, NTRIP_ESP32.RXD_5V
  N13: Dual_GPS_ESP32.GPIO15, Speed_out.anode
  N14: Dual_GPS_ESP32.GPIO5, R29.Pin_1
  N15: Dual_GPS_ESP32.GPIO19, 232.pin1
  N16: F9P_NAV-PVT_right_purple.RX, LM358.connector4, J1.pin2, NTRIP_ESP32.TXD
  N17: F9P_NAV-PVT_right_purple.CS, J1.pin3
  N18: F9P_NAV-PVT_right_purple.RX2, J1.pin4
  N19: F9P_NAV-PVT_right_purple.3V3, J1.pin6, 3_3.pin2
  N20: RTCM.cathode, R1.Pin_0
  N21: NMEA.cathode, R2.Pin_0
  N22: R1.Pin_1, LM358.connector5, LM358.connector6
  N23: R2.Pin_1, LM358.connector0, LM358.connector1
  N24: R14.Pin_0, NTRIP_ESP32.GPIO21
  N25: R14.Pin_1, Ntrip.red_cathode
  N26: R15.Pin_0, NTRIP_ESP32.GPIO23
  N27: R15.Pin_1, Ntrip.green_cathode
  N28: R16.Pin_0, NTRIP_ESP32.GPIO22
  N29: R16.Pin_1, Ntrip.blue_cathode
  N30: LM358_2.connector0, LM358_2.connector1, R4.Pin_0
  N31: LM358_2.connector5, LM358_2.connector6, R3.Pin_0
  N32: RX.cathode, R4.Pin_1
  N33: R3.Pin_1, TX.cathode
  N34: F2.pin1, P1.pin_1
  N35: F1.pin1, D1.cathode
  N36: 6N137.Vf+, R23.Pin_0
  N37: 6N137.GND, C8.0, P1.pin_5, RO-0505S.-VOUT, MAX202.pin15, C10.0, C13.0
  N38: 6N137.Vo, R19.Pin_0, RS-232.cathode, MAX202.pin10
  N39: 6N137.Vcc, C8.1, R19.Pin_1, RO-0505S.+VOUT, MAX202.pin16, C9.1, C10.1, R5.Pin_1
  N40: R11.Pin_0, 232.pin2
  N41: R11.Pin_1, 2N3906.B
  N42: 2N3906.C, R23.Pin_1
  N43: P1.pin_2, D1.anode
  N44: P1.pin_6, MAX202.pin7
  N45: RS-232.anode, R5.Pin_0
  N46: MAX202.pin1, C11.1
  N47: MAX202.pin2, C9.0
  N48: MAX202.pin3, C11.0
  N49: MAX202.pin4, C12.1
  N50: MAX202.pin5, C12.0
  N51: MAX202.pin6, C13.1
  N52: Ntrip.common_anode, NTRIP_ESP32.3.3V
  N53: MAX700.pin2, R17.Pin_0, R25.Pin_0, R26.Pin_1, C19.0
  N54: MAX700.pin3, R25.Pin_1
  N55: MAX700.pin5, D2.cathode, DC_good.anode, R12.Pin_1
  N56: DC_good.cathode, R22.Pin_1

notes:
  License GPLv3 PCB design
  Copyright Reuben Rissler 2024
  ___________
  Antenna
  Rev E
  Heading
  Roll

custom parts:
  Voltage Regulator - 5V: 5V DC Voltage Regulator
  ZED-F9P: A breakout board made by Sparkfun with the Ublox ZED-F9P, in the vein of Qwiic boards.
  ESP32-38PinWide: Generic 38-Pin ESP32 with wide format (only access to one side of pins on a breadboard) based on Stephen Lilley's HiLetgo ESP-WROOM-32 ESP32 ESP-32S Development Board.
  ZED-F9P: A breakout board made by Sparkfun with the Ublox ZED-F9P, in the vein of Qwiic boards.
  Fuse PCB mount: A PCB mount PTC fuse with 5mm spacing.
  6n137 Optocoupler: 6n137 fast Optocoupler. With 8 pins on a 300mil dual inline package (DIP) footprint. Ve is strobe input. Output is inverting.
  DTM13-6P: DTM13-6P connector.
  Isolated regulator: An isolated DC/DC regulator made by Recom.
  ESP32 Huzzah Breakout: Squeeeeze down your next ESP32 project to its bare-bones essential with the Adafruit HUZZAH32 Breakout. This breakout is basically the 'big sister' of our HUZZAH 8266, but instead of an ESP8266 it has the '32! We've pared down our popular Feather ESP32, removing the battery charger and USB-serial converter. You just get a regulator, some protection diodes, two buttons and an LED. For some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
