# Fritzing sketch Dual GPS REV B (saved by Fritzing 0.9.3b)
circuit board: 9.3cm x 5.64444cm
breadboards: 1

parts:
  LM358 = LM 358 Dual Op-Amp [package="DIP8 [THT]"]
  12V = screw terminal, 2 pins
  R1 = Resistor [tolerance=±5% resistance=560 package=THT]
  R2 = Resistor [tolerance=±5% resistance=560 package=THT]
  R3 = Resistor [tolerance=±5% resistance=560 package=THT]
  Ntrip = RGB LED - (4 legs) [package="5 mm [THT]"]
  NAV-PVT_right = ZED-F9P
  RelPosNED_left = ZED-F9P
  NMEA = LED - 5mm [color="Orange (605nm)" package="5 mm [THT]"]
  RTCM = LED - 5mm [color="Red (635nm)" package="5 mm [THT]"]
  C3 = Ceramic Capacitor [capacitance=100nF package="100 mil [THT, multilayer]"]
  R4 = Resistor [tolerance=±5% resistance=1k package=THT]
  R5 = Resistor [tolerance=±5% resistance=1k package=THT]
  Ntrip_ESP32 = ESP32 Huzzah Breakout [part_number="Adafruit #4172"]
  ESP_Wifi = LED - 5mm [color="Blue (470nm)" package="5 mm [THT]"]
  R6 = Resistor [tolerance=±5% resistance=4.7k package=THT]
  Dual_GPS_ESP32 = ESP32-38PinWide [part_number=ESP32-38PinWide]
  br = Bridge Rectifier
  F1 = Fuse PCB mount [package=THT]
  U1 = Voltage Regulator - 5V [package="TO220 [THT]"]
  C1 = Electrolytic Capacitor Axial leads [package="800 mil [THT, electrolytic]"]
  C2 = Electrolytic Capacitor Axial leads [package="800 mil [THT, electrolytic]"]

nets:
  N1: LM358.connector0, LM358.connector1, R4.Pin_1
  N2: LM358.connector2, NAV-PVT_right.TX, Ntrip_ESP32.RXD_5V, Dual_GPS_ESP32.GPIO27
  GND: LM358.connector3, NAV-PVT_right.GND, RelPosNED_left.GND, C3.1, Ntrip_ESP32.GND, Dual_GPS_ESP32.GND, br.-, U1.GND, C1.-, C2.-
  N3: LM358.connector4, NAV-PVT_right.RX2, Ntrip_ESP32.TXD
  N4: LM358.connector5, LM358.connector6, R5.Pin_1
  5V: LM358.connector7, NAV-PVT_right.5V, RelPosNED_left.5V, NMEA.anode, RTCM.anode, C3.0, Ntrip_ESP32.VBAT, Dual_GPS_ESP32.VIN, U1.output_voltage, C1.+
  N5: 12V.pin1, br.~#3
  N6: 12V.pin2, F1.pin2
  N7: R1.Pin_0, Ntrip_ESP32.GPIO23
  N8: R1.Pin_1, Ntrip.blue_cathode
  N9: R2.Pin_0, Ntrip_ESP32.GPIO22
  N10: R2.Pin_1, Ntrip.green_cathode
  N11: R3.Pin_0, Ntrip_ESP32.GPIO21
  N12: R3.Pin_1, Ntrip.red_cathode
  N13: Ntrip.common_anode, Ntrip_ESP32.3.3V
  N14: NAV-PVT_right.TX2, RelPosNED_left.RX2
  N15: RelPosNED_left.TX, Dual_GPS_ESP32.GPIO25
  N16: NMEA.cathode, R4.Pin_0
  N17: RTCM.cathode, R5.Pin_0
  N18: ESP_Wifi.cathode, R6.Pin_1
  N19: ESP_Wifi.anode, Dual_GPS_ESP32.3.3
  N20: R6.Pin_0, Dual_GPS_ESP32.GPIO32
  N21: br.+, U1.input_voltage, C2.+
  N22: br.~#1, F1.pin1

custom parts:
  ZED-F9P: A breakout board made by Sparkfun with the Ublox ZED-F9P, in the vein of Qwiic boards.
  ZED-F9P: A breakout board made by Sparkfun with the Ublox ZED-F9P, in the vein of Qwiic boards.
  ESP32 Huzzah Breakout: Squeeeeze down your next ESP32 project to its bare-bones essential with the Adafruit HUZZAH32 Breakout. This breakout is basically the 'big sister' of our HUZZAH 8266, but instead of an ESP8266 it has the '32! We've pared down our popular Feather ESP32, removing the battery charger and USB-serial converter. You just get a regulator, some protection diodes, two buttons and an LED. For some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
  ESP32-38PinWide: Generic 38-Pin ESP32 with wide format (only access to one side of pins on a breadboard) based on Stephen Lilley's HiLetgo ESP-WROOM-32 ESP32 ESP-32S Development Board.
  Fuse PCB mount: A PCB mount fuse with 200 mil spacing.
  Voltage Regulator - 5V: 5V DC Voltage Regulator
  Electrolytic Capacitor Axial leads: An electrolytic capacitor with axial leads
