# Fritzing sketch CanBus breakout Rev A (saved by Fritzing 1.0.1rc)
circuit board: 3.5cm x 2cm
breadboards: 1

parts:
  U3 = mystery part, 5 pins [chip_label=?]
  U4 = mystery part, 5 pins [chip_label=?]
  MCP2515 = SOIC18-W [chip_label=SOIC18-W package=SO(w)]
  MCP2562 = SO08-EIAJ [chip_label=SOIC18-W package=SO]
  C1 = Ceramic Capacitor [capacitance=100nF voltage=35V package="100 mil [THT, multilayer]"]
  C2 = Ceramic Capacitor [capacitance=100nF voltage=35V package="100 mil [THT, multilayer]"]
  C3 = Ceramic Capacitor [capacitance=100nF voltage=35V package="100 mil [THT, multilayer]"]
  XTAL = Crystal [frequency="16 Mhz" package=THT]
  C4 = Ceramic Capacitor [capacitance=100nF voltage=35V package="100 mil [THT, multilayer]"]
  Tx = smd LED [color="Red (633nm)" current=30mA package="1206 [SMD]"]
  Rx = smd LED [color="Red (633nm)" current=30mA package="1206 [SMD]"]
  R10 = Resistor [tolerance=±5% resistance=220 power=0.25W package="1206 [SMD]"]
  R11 = Resistor [tolerance=±5% resistance=220 power=0.25W package="1206 [SMD]"]

nets:
  N1: U3.pin1, MCP2515.13
  N2: U3.pin2, MCP2515.14
  N3: U3.pin3, MCP2515.15
  N4: U3.pin4, MCP2515.16
  N5: U3.pin5, MCP2515.18, MCP2562.5, C4.0, Tx.anode, Rx.anode
  N6: U4.pin1, MCP2515.9, MCP2562.2, MCP2562.8, C1.1, C2.0, C3.0, C4.1
  N7: U4.pin2, MCP2562.3, C3.1
  N8: U4.pin4, MCP2562.7
  N9: U4.pin5, MCP2562.6
  N10: MCP2515.1, MCP2562.1, R10.Pin_1
  N11: MCP2515.2, MCP2562.4, R11.Pin_1
  N12: MCP2515.7, C2.1, XTAL.pin_0
  N13: MCP2515.8, C1.0, XTAL.pin_1
  N14: Tx.cathode, R10.Pin_0
  N15: Rx.cathode, R11.Pin_0

notes:
  Rev A
  Gnd
  Sck
  Cs
  Si
  So
