# Fritzing sketch Lightbar Rev A (saved by Fritzing 1.0.1rc)
circuit board: 4.2cm x 2.9cm
breadboards: 1

parts:
  Esp32 = seeeduino-xiao
  78E05 = Voltage Regulator - 5V [package="TO220 [THT]"]
  D1 = Rectifier Diode [part_number=1N4001 package="300 mil [THT]"]
  C2 = Electrolytic Capacitor [capacitance=1µF voltage=35V package="100 mil [THT, electrolytic]"]
  R1 = Resistor [tolerance=±5% power=0.25W resistance=1k package=THT]
  R2 = Resistor [tolerance=±5% power=0.25W resistance=1k package=THT]
  C3 = Electrolytic Capacitor [capacitance=1µF voltage=35V package="100 mil [THT, electrolytic]"]
  R3 = Resistor [tolerance=±5% power=0.25W resistance=680 package=THT]
  R4 = Resistor [tolerance=±5% power=0.25W resistance=680 package=THT]
  R5 = Resistor [tolerance=±5% power=0.25W resistance=10k package=THT]
  R6 = PHOTOCELL [package=photocell]
  D2 = BAV99 [package=sot23]
  R7 = Resistor [tolerance=±0.1% power=0.25W resistance=4.7k package=THT]
  Q3 = MOSFET-NCHANNEL [package=to-92]
  R8 = 12mm Trimmer Potentiometer (Large) [package=THT]

nets:
  N1: Esp32.D3, R6.P$1, R7.Pin_1
  N2: Esp32.D5, R5.Pin_0, D2.COM
  N3: Esp32.D6, R8.wiper
  N4: Esp32.D10, R1.Pin_0, Q3.S
  N5: Esp32.3V3, R1.Pin_1, R6.P$2, D2.C2, Q3.G, R8.leg2
  GND: Esp32.GND, 78E05.GND, C2.-, C3.-, R4.Pin_0, D2.A1, R7.Pin_0, R8.leg1
  N6: Esp32.5V, 78E05.output_voltage, R2.Pin_1, C3.+
  N7: 78E05.input_voltage, D1.cathode, C2.+
  N8: R2.Pin_0, Q3.D
  N9: R3.Pin_1, R4.Pin_1, R5.Pin_1

notes:
  +
  -
  steer
  5v+
  Gnd
  D
  Rev A

custom parts:
  seeeduino-xiao: Seeeduino XIAO processor board.
  Voltage Regulator - 5V: 5V DC Voltage Regulator
  MOSFET-NCHANNEL: Generic NMOS footprint
  12mm Trimmer Potentiometer (Large): A standard adjustable resistor (potentiometer).
