# Fritzing sketch Machine control Rev A (saved by Fritzing 0.9.3b)
circuit board: 9.8cm x 5.64444cm
breadboards: 1

parts:
  ADS1115 = Adafruit ADS1115 16Bit I2C ADC [part_number="Adafruit #1085"]
  7805 = Voltage Regulator - 5V [package="DPak [SMD]"]
  D14 = Rectifier Diode [part_number=1N4001 package="300 mil [THT]"]
  C1 = Electrolytic Capacitor [capacitance=47µF voltage=20V package="100 mil [THT, electrolytic]"]
  C2 = Electrolytic Capacitor [capacitance=0.47mF package="100 mil [THT, electrolytic]"]
  R1 = Resistor [tolerance=±5% resistance=1.5k package=THT]
  R2 = Resistor [tolerance=±5% resistance=1.5k package=THT]
  3_3 = Voltage Regulator - 5V [part_number=497-14661-1-ND package="DPak [SMD]"]
  WAS_V+ = female pin header, 3 pins [form="♀ (female)"]
  R3 = Resistor [tolerance=±5% resistance=1k package=THT]
  R4 = Resistor [tolerance=±5% resistance=1k package=THT]
  D4 = Zener Diode [part_number=1N4732A breakdown_voltage=3.6V package="300 mil [THT]"]
  D3 = Zener Diode [part_number=1N4732A breakdown_voltage=3.6V package="300 mil [THT]"]
  R5 = Resistor [tolerance=±5% resistance=1k package=THT]
  R6 = Resistor [tolerance=±5% resistance=1k package=THT]
  C1_2 = Ceramic Capacitor [capacitance=100nF package="100 mil [THT, multilayer]"]
  D11 = Rectifier Diode [part_number=1N4001 package="300 mil [THT]"]
  F3 = Fuse PCB mount [package=THT]
  C4 = Electrolytic Capacitor [capacitance=0.1mF voltage=20V package="100 mil [THT, electrolytic]"]
  C3 = Ceramic Capacitor [capacitance=100nF package="100 mil [THT, multilayer]"]
  C2_2 = Ceramic Capacitor [capacitance=100nF package="100 mil [THT, multilayer]"]
  C3_2 = Electrolytic Capacitor [capacitance=0.1mF package="100 mil [THT, electrolytic]"]
  18_17_16 = female pin header, 3 pins [form="♀ (female)"]
  D12 = Rectifier Diode [part_number=1N4001 package="300 mil [THT]"]
  D13 = Rectifier Diode [part_number=1N4001 package="300 mil [THT]"]
  R7 = Resistor [tolerance=±5% resistance=220 package=THT]
  R8 = Resistor [tolerance=±5% resistance=220 package=THT]
  D1 = Zener Diode [part_number=1N4732A breakdown_voltage=3.6V package="300 mil [THT]"]
  D2 = Zener Diode [part_number=1N4732A breakdown_voltage=3.6V package="300 mil [THT]"]
  Q6 = N-channel mosfet [part_number=ZVN4206AVSTZ package="TO92 [THT]"]
  F5305 = Basic FET P-Channel [package="DPak [SMD]"]
  Q7 = N-channel mosfet [part_number=ZVN4206AVSTZ package="TO92 [THT]"]
  F5305_2 = Basic FET P-Channel [package="DPak [SMD]"]
  R9 = Resistor [tolerance=±5% resistance=1k package=THT]
  R10 = Resistor [tolerance=±5% resistance=1k package=THT]
  R11 = Resistor [tolerance=±5% resistance=220 package=THT]
  R12 = Resistor [tolerance=±5% resistance=220 package=THT]
  R13 = Resistor [tolerance=±5% resistance=1k package=THT]
  R14 = Resistor [tolerance=±5% resistance=1k package=THT]
  ESP32 = ESP32-38PinWide [part_number=ESP32-38PinWide]
  Steer = LED - 5mm [color="Red (633nm)" package="5 mm [THT]"]
  R15 = Resistor [tolerance=±5% resistance=330 package=THT]
  R16 = Resistor [tolerance=±5% resistance=330 package=THT]
  Status = LED - 5mm [color="Green (565nm)" package="5 mm [THT]"]
  R17 = Resistor [tolerance=±5% resistance=10 package=THT]
  Power = LED - 5mm [color="Red (633nm)" package="5 mm [THT]"]
  R18 = Resistor [tolerance=±5% resistance=330 package=THT]
  +5V- = double row female pin header, 4 pins [form="♀ (female)"]
  C5 = Ceramic Capacitor [capacitance=100nF package="100 mil [THT, multilayer]"]
  +3V- = double row female pin header, 2 pins [form="♀ (female)"]
  +_str_sns_- = screw terminal, 4 pins
  Wheel_angle = screw terminal, 3 pins
  steer_work = screw terminal, 5 pins
  +_12V_- = screw terminal, 2 pins
  Gnd_IO16_IO17 = screw terminal, 3 pins

nets:
  N1: ADS1115.AIN0, C1_2.0, Wheel_angle.pin2
  N2: ADS1115.SDA, R2.Pin_0, ESP32.GPIO21
  N3: ADS1115.SCL, R1.Pin_0, ESP32.GPIO22
  GND: ADS1115.GND, 7805.GND, C1.-, C2.-, 3_3.GND, D4.anode, D3.anode, R5.Pin_0, R6.Pin_0, C1_2.1, C4.-, C3.1, C2_2.0, C3_2.-, D12.anode, D13.anode, D1.anode, D2.anode, Q6.S, Q7.S, R11.Pin_1, R12.Pin_1, R13.Pin_1, R14.Pin_1, ESP32.GND, Steer.cathode, Status.cathode, R18.Pin_0, +5V-.pin2, +5V-.pin3, C5.0, +3V-.pin1, +_str_sns_-.pin4, Wheel_angle.pin3, +_12V_-.pin1, Gnd_IO16_IO17.pin3
  N4: ADS1115.VDD, WAS_V+.pin2, C5.1, +_str_sns_-.pin1, Wheel_angle.pin1
  N5: 7805.input_voltage, D14.cathode, C1.+
  N6: 7805.output_voltage, C2.+, 3_3.input_voltage, WAS_V+.pin1, ESP32.VIN, Power.anode, +5V-.pin1, +5V-.pin4
  N7: D14.anode, D11.anode, +_12V_-.pin2
  N8: R1.Pin_1, R2.Pin_1, ESP32.3.3
  N9: 3_3.output_voltage, WAS_V+.pin3, C3_2.+, R17.Pin_1, +3V-.pin2
  N10: R3.Pin_0, D4.cathode, R5.Pin_1, C3.0, ESP32.GPIO15, steer_work.pin4
  N11: R3.Pin_1, steer_work.pin3
  N12: R4.Pin_0, D3.cathode, R6.Pin_1, C2_2.1, ESP32.GPIO2, steer_work.pin2
  N13: R4.Pin_1, steer_work.pin1
  N14: D11.cathode, F3.pin1, C4.+
  N15: F3.pin2, F5305.source, F5305_2.source, R9.Pin_0, R10.Pin_1
  N16: 18_17_16.pin1, ESP32.GPIO18
  N17: 18_17_16.pin2, Q6.G, R11.Pin_0, ESP32.GPIO17
  N18: 18_17_16.pin3, Q7.G, R12.Pin_0, ESP32.GPIO16
  N19: D12.cathode, F5305_2.drain, Gnd_IO16_IO17.pin2
  N20: D13.cathode, F5305.drain, Gnd_IO16_IO17.pin1
  N21: R7.Pin_0, D1.cathode, R13.Pin_0, ESP32.GPIO34
  N22: R7.Pin_1, +_str_sns_-.pin3
  N23: R8.Pin_0, D2.cathode, R14.Pin_0, ESP32.GPIO35
  N24: R8.Pin_1, +_str_sns_-.pin2
  N25: Q6.D, F5305.Gate, R9.Pin_1
  N26: Q7.D, F5305_2.Gate, R10.Pin_0
  N27: ESP32.GPIO5, R15.Pin_1
  N28: ESP32.GPIO19, R16.Pin_1
  N29: Steer.anode, R15.Pin_0
  N30: R16.Pin_0, Status.anode
  N31: R17.Pin_0, steer_work.pin5
  N32: Power.cathode, R18.Pin_1

notes:
  5V
  3V3
  + sense -
  12V
  3V3+
  ------
  Valve
  Copyright Reuben Rissler 2020
  License GPLv3 for PCB
  Rev A

custom parts:
  Adafruit ADS1115 16Bit I2C ADC: For microcontrollers without an analog-to-digital converter or when you want a higher-precision ADC, the ADS1115 provides 16-bit precision at 860 samples/second over I2C. The chip can be configured as 4 single-ended input channels, or two differential channels. As a nice bonus, it even includes a programmable gain amplifier, up to x16, to help boost up smaller single/differential signals to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
  Fuse PCB mount: A PCB mount fuse with 200 mil spacing.
  N-channel mosfet: A TO-92 N-channel mosfet
  ESP32-38PinWide: Generic 38-Pin ESP32 with wide format (only access to one side of pins on a breadboard) based on Stephen Lilley's HiLetgo ESP-WROOM-32 ESP32 ESP-32S Development Board.
