# Fritzing sketch Machine control Rev B (saved by Fritzing 0.9.3b)
circuit board: 10.1cm x 8.25cm
breadboards: 1

parts:
  ADS1115 = Adafruit ADS1115 16Bit I2C ADC [part_number="Adafruit #1085"]
  D4 = Rectifier Diode [part_number=1N4001 package="300 mil [THT]"]
  C1 = Electrolytic Capacitor [capacitance=47µF voltage=20V package="100 mil [THT, electrolytic]"]
  C2 = Electrolytic Capacitor [capacitance=0.47mF package="100 mil [THT, electrolytic]"]
  R28 = Resistor [tolerance=±5% resistance=1.2k package=THT]
  R29 = Resistor [tolerance=±5% resistance=1.2k package=THT]
  R13 = Resistor [tolerance=±5% resistance=270 package=THT]
  D4_2 = Zener Diode [part_number=1N4732A breakdown_voltage=3.6V package="300 mil [THT]"]
  R6 = Resistor [tolerance=±5% resistance=1k package=THT]
  C1_2 = Ceramic Capacitor [capacitance=100nF package="100 mil [THT, multilayer]"]
  F1 = Fuse PCB mount [package=THT]
  C4 = Electrolytic Capacitor [capacitance=0.1mF voltage=20V package="100 mil [THT, electrolytic]"]
  C3 = Ceramic Capacitor [capacitance=100nF package="100 mil [THT, multilayer]"]
  D2 = Rectifier Diode [part_number=1N4001 package="300 mil [THT]"]
  D3 = Rectifier Diode [part_number=1N4001 package="300 mil [THT]"]
  R15 = Resistor [tolerance=±5% resistance=270 package=THT]
  D1 = Zener Diode [part_number=1N4732A breakdown_voltage=3.6V package="300 mil [THT]"]
  Q6 = N-channel mosfet [part_number=ZVN4206AVSTZ package="TO92 [THT]"]
  F5305 = Basic FET P-Channel [package="DPak [SMD]"]
  Q7 = N-channel mosfet [part_number=ZVN4206AVSTZ package="TO92 [THT]"]
  R5 = Resistor [tolerance=±5% resistance=1k package=THT]
  R4 = Resistor [tolerance=±5% resistance=1k package=THT]
  Steer = LED - 5mm [color="Red (633nm)" package="5 mm [THT]"]
  R22 = Resistor [tolerance=±5% resistance=470 package=THT]
  R21 = Resistor [tolerance=±5% resistance=470 package=THT]
  Power = LED - 5mm [color="Green (555nm)" package="5 mm [THT]"]
  R20 = Resistor [tolerance=±5% resistance=470 package=THT]
  C5 = Ceramic Capacitor [capacitance=100nF package="100 mil [THT, multilayer]"]
  Wifi = LED - 5mm [color="Blue (470nm)" package="5 mm [THT]"]
  R32 = Resistor [tolerance=±5% resistance=47 package=THT]
  R31 = Resistor [tolerance=±5% resistance=47 package=THT]
  Q8 = N-channel mosfet [part_number=ZVN4206AVSTZ package="TO92 [THT]"]
  ESP32 = ESP32-38PinWide [part_number=ESP32-38PinWide]
  Work = LED - 5mm [color="Yellow (592nm)" package="5 mm [THT]"]
  R23 = Resistor [tolerance=±5% resistance=470 package=THT]
  Str_Sw = LED - 5mm [color="Red (633nm)" package="5 mm [THT]"]
  Wrk_Sw = LED - 5mm [color="Red (633nm)" package="5 mm [THT]"]
  F5305_2 = Basic FET P-Channel [package="DPak [SMD]"]
  F5305_3 = Basic FET P-Channel [package="DPak [SMD]"]
  D1_2 = Rectifier Diode [part_number=1N4001 package="300 mil [THT]"]
  R3 = Resistor [tolerance=±5% resistance=1k package=THT]
  C4_2 = Ceramic Capacitor [capacitance=100nF package="100 mil [THT, multilayer]"]
  D3_2 = Zener Diode [part_number=1N4732A breakdown_voltage=3.6V package="300 mil [THT]"]
  R7 = Resistor [tolerance=±5% resistance=1k package=THT]
  R25 = Resistor [tolerance=±5% resistance=470 package=THT]
  R24 = Resistor [tolerance=±5% resistance=470 package=THT]
  MCP2562 = IC, DIP package, 8 pins [chip_label=IC]
  C6 = Ceramic Capacitor [capacitance=100nF package="100 mil [THT, multilayer]"]
  R8 = Resistor [tolerance=±5% resistance=1k package=THT]
  R1 = Resistor [tolerance=±5% resistance=1k package=THT]
  R2 = Resistor [tolerance=±5% resistance=1k package=THT]
  D10 = Rectifier Diode 600mil [part_number=1N5400 package="600 mil [THT]"]
  Str_Whl_Sw = LED - 5mm [color="Red (633nm)" package="5 mm [THT]"]
  R26 = Resistor [tolerance=±5% resistance=470 package=THT]
  J3 = DTM13-12PA-12PB-R008 [package=THT]
  7805 = Voltage Regulator - 5V [package="DPak [SMD]"]
  R9 = Resistor [tolerance=±5% resistance=220 package=THT]
  R10 = Resistor [tolerance=±5% resistance=220 package=THT]
  R11 = Resistor [tolerance=±5% resistance=220 package=THT]
  R14 = Resistor [tolerance=±5% resistance=270 package=THT]

nets:
  N1: ADS1115.AIN0, C1_2.0, J3.pin_21
  N2: ADS1115.SDA, R29.Pin_0, ESP32.GPIO21
  N3: ADS1115.SCL, R28.Pin_0, ESP32.GPIO22
  GND: ADS1115.GND, C1.-, C2.-, D4_2.anode, R6.Pin_0, C1_2.1, C4.-, C3.1, D2.anode, D3.anode, D1.anode, Q6.S, Q7.S, Steer.cathode, Power.cathode, C5.0, Wifi.cathode, Q8.S, ESP32.GND, Work.cathode, D1_2.anode, C4_2.1, D3_2.anode, R7.Pin_0, R25.Pin_1, R24.Pin_1, MCP2562.pin2, C6.0, R8.Pin_1, R1.Pin_0, R2.Pin_0, J3.pin_3, J3.pin_4, J3.pin_23, J3.pin_24, 7805.GND, R9.Pin_0, R10.Pin_0, R11.Pin_0
  VDD: ADS1115.VDD, C2.+, R20.Pin_1, C5.1, ESP32.VIN, MCP2562.pin3, C6.1, J3.pin_18, J3.pin_19, J3.pin_20, 7805.output_voltage
  N4: D4.cathode, C1.+, 7805.input_voltage
  N5: D4.anode, J3.pin_2
  N6: R28.Pin_1, R29.Pin_1, R15.Pin_1, ESP32.3.3, MCP2562.pin5, R26.Pin_1
  N7: R13.Pin_0, D4_2.cathode, R6.Pin_1, C3.0, R32.Pin_0, ESP32.GPIO15, Str_Sw.anode
  N8: R13.Pin_1, J3.pin_12
  N9: F1.pin1, C4.+, D10.cathode
  N10: F1.pin2, F5305.source, R5.Pin_1, R4.Pin_1, F5305_2.source, F5305_3.source, R3.Pin_1
  N11: D2.cathode, F5305_2.drain, R1.Pin_1, J3.pin_8
  N12: D3.cathode, F5305.drain, J3.pin_7
  N13: R15.Pin_0, D1.cathode, ESP32.GPIO23, Str_Whl_Sw.cathode, J3.pin_22
  N14: Q6.G, ESP32.GPIO27, R9.Pin_1
  N15: Q6.D, F5305.Gate, R5.Pin_0
  N16: Q7.G, ESP32.GPIO26, R10.Pin_1
  N17: Q7.D, R4.Pin_0, F5305_2.Gate
  N18: Steer.anode, R22.Pin_0
  N19: R22.Pin_1, ESP32.GPIO12
  N20: R21.Pin_0, Wifi.anode
  N21: R21.Pin_1, ESP32.GPIO13
  N22: Power.anode, R20.Pin_0
  N23: R32.Pin_1, J3.pin_16
  N24: R31.Pin_0, ESP32.GPIO2, Wrk_Sw.anode, C4_2.0, D3_2.cathode, R7.Pin_1, R14.Pin_0
  N25: R31.Pin_1, J3.pin_17
  N26: Q8.G, ESP32.GPIO25, R11.Pin_1
  N27: Q8.D, F5305_3.Gate, R3.Pin_0
  N28: ESP32.GPIO32, MCP2562.pin1
  N29: ESP32.GPIO33, MCP2562.pin4
  N30: ESP32.GPIO14, R23.Pin_1
  N31: Work.anode, R23.Pin_0
  N32: Str_Sw.cathode, R25.Pin_0
  N33: Wrk_Sw.cathode, R24.Pin_0
  N34: F5305_3.drain, D1_2.cathode, R2.Pin_1, J3.pin_9
  N35: MCP2562.pin6, J3.pin_11
  N36: MCP2562.pin7, J3.pin_10
  N37: MCP2562.pin8, R8.Pin_0
  N38: D10.anode, J3.pin_1
  N39: Str_Whl_Sw.anode, R26.Pin_0
  N40: J3.pin_5, R14.Pin_1

notes:
  Rev B
  Copyright Reuben Rissler 2021
  License GPLv3 - PCB design

custom parts:
  Adafruit ADS1115 16Bit I2C ADC: For microcontrollers without an analog-to-digital converter or when you want a higher-precision ADC, the ADS1115 provides 16-bit precision at 860 samples/second over I2C. The chip can be configured as 4 single-ended input channels, or two differential channels. As a nice bonus, it even includes a programmable gain amplifier, up to x16, to help boost up smaller single/differential signals to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
  Fuse PCB mount: A PCB mount fuse with 200 mil spacing.
  N-channel mosfet: A TO-92 N-channel mosfet
  ESP32-38PinWide: Generic 38-Pin ESP32 with wide format (only access to one side of pins on a breadboard) based on Stephen Lilley's HiLetgo ESP-WROOM-32 ESP32 ESP-32S Development Board.
  Rectifier Diode 600mil: A standard 3amp rectifier diode
  DTM13-12PA-12PB-R008: DTM13-12PA-12PB-R008 connector.
