# Fritzing sketch Machine control Rev F (saved by Fritzing 0.9.9b)
circuit board: 10.1cm x 8.25cm
breadboards: 1

parts:
  ADS1115 = Adafruit ADS1115 16Bit I2C ADC [part_number="Adafruit #1085"]
  D4 = Rectifier Diode [part_number=1N4001 package="300 mil [THT]"]
  C11 = Electrolytic Capacitor [capacitance=47µF voltage=50V package="100 mil [THT, electrolytic]"]
  C10 = Electrolytic Capacitor [capacitance=0.47mF voltage=35V package="100 mil [THT, electrolytic]"]
  R28 = Resistor [tolerance=±5% resistance=1.2k power=0.25 package=THT]
  R29 = Resistor [tolerance=±5% resistance=1.2k power=0.25 package=THT]
  R13 = Resistor [tolerance=±5% resistance=680 power=0.25 package=THT]
  C1 = Ceramic Capacitor [capacitance=100nF voltage=35V package="100 mil [THT, multilayer]"]
  F1 = Fuse PCB mount [package=THT]
  C12 = Electrolytic Capacitor [capacitance=0.1mF voltage=50V package="100 mil [THT, electrolytic]"]
  Q7 = N-channel mosfet [part_number=ZVN4206AVSTZ package="TO92 [THT]"]
  R6 = Resistor [tolerance=±5% resistance=1k power=0.25 package=THT]
  Steer = LED - 5mm [color="Red (633nm)" current=0.030 package="5 mm [THT]"]
  R22 = Resistor [tolerance=±5% resistance=470 power=0.25 package=THT]
  R21 = Resistor [tolerance=±5% resistance=470 power=0.25 package=THT]
  Power = LED - 5mm [color="Green (555nm)" current=0.030 package="5 mm [THT]"]
  R20 = Resistor [tolerance=±5% resistance=470 power=0.25 package=THT]
  Wifi = LED - 5mm [color="Yellow (595nm)" current=0.030 package="5 mm [THT]"]
  R32 = Resistor [tolerance=±5% resistance=100 power=0.25 package=THT]
  R31 = Resistor [tolerance=±5% resistance=100 power=0.25 package=THT]
  Q8 = N-channel mosfet [part_number=ZVN4206AVSTZ package="TO92 [THT]"]
  ESP32 = ESP32-38PinWide [part_number=ESP32-38PinWide]
  Work = LED - 5mm [color="Blue (525nm)" current=0.030 package="5 mm [THT]"]
  R3 = Resistor [tolerance=±5% resistance=4.7k power=0.25 package=THT]
  Str_Sw = LED - 5mm [color="Yellow (595nm)" current=0.030 package="5 mm [THT]"]
  Wrk_Sw = LED - 5mm [color="Yellow (595nm)" current=0.030 package="5 mm [THT]"]
  F5305 = Basic FET P-Channel [package="DPak [SMD]"]
  F5305_2 = Basic FET P-Channel [package="DPak [SMD]"]
  R7 = Resistor [tolerance=±5% resistance=1k power=0.25 package=THT]
  MCP2562 = IC, DIP package, 8 pins [chip_label=IC]
  C6 = Ceramic Capacitor [capacitance=100nF voltage=35V package="100 mil [THT, multilayer]"]
  R8 = Resistor [tolerance=±5% resistance=1k power=0.25 package=THT]
  D10 = Rectifier Diode 600mil [part_number=1N5400 package="600 mil [THT]"]
  Str_Whl_Sw = LED - 5mm [color="Yellow (595nm)" current=0.030 package="5 mm [THT]"]
  J3 = DTM13-12PA-12PB-R008 [package=THT]
  R9 = Resistor [tolerance=±5% resistance=1k power=0.25 package=THT]
  R10 = Resistor [tolerance=±5% resistance=1k power=0.25 package=THT]
  R11 = Resistor [tolerance=±5% resistance=1k power=0.25 package=THT]
  R14 = Resistor [tolerance=±5% resistance=680 power=0.25 package=THT]
  D5 = Rectifier Diode [part_number=1N4001 package="300 mil [THT]"]
  TC4427 = TC4427 [part_number=TC4427 package="DIP (Dual Inline) [THT]"]
  78E05 = Voltage Regulator - 5V [package="TO220 [THT]"]
  F2 = Fuse PCB mount [package=THT]
  C2 = Ceramic Capacitor [capacitance=100nF voltage=35V package="100 mil [THT, multilayer]"]
  CNY17 = mystery part, 6 pins [chip_label=?]
  CNY17_2 = mystery part, 6 pins [chip_label=?]
  CNY17_3 = mystery part, 6 pins [chip_label=?]
  R33 = Resistor [tolerance=±5% power=0.25 resistance=100 package=THT]
  R1 = Resistor [tolerance=±5% power=0.25 resistance=3.3k package=THT]
  R35 = Resistor [tolerance=±5% power=0.25 resistance=10k package=THT]
  D12 = BAV99 [package=sot23]
  R36 = Resistor [tolerance=±5% power=0.25 resistance=10k package=THT]
  R37 = Resistor [tolerance=±5% power=0.25 resistance=10k package=THT]
  D13 = BAV99 [package=sot23]
  C4 = Ceramic Capacitor [capacitance=100nF voltage=35V package="100 mil [THT, multilayer]"]
  D14 = BAV99 [package=sot23]
  C3 = Ceramic Capacitor [capacitance=100nF voltage=35V package="100 mil [THT, multilayer]"]
  D11 = BAV99 [package=sot23]
  R38 = Resistor [tolerance=±5% power=0.25 resistance=10k package=THT]
  IRF44 = Basic FET N-Channel [package="DPak [SMD]"]
  IRF44_2 = Basic FET N-Channel [package="DPak [SMD]"]
  C13 = Ceramic Capacitor [capacitance=100nF voltage=35V package="100 mil [THT, multilayer]"]
  IC1 = SO08 [chip_label=IC package=SO]
  D15 = Rectifier Diode [part_number=1N4001 package="300 mil [THT]"]
  D16 = Rectifier Diode [part_number=1N4001 package="300 mil [THT]"]

nets:
  N1: ADS1115.AIN3, R1.Pin_0, R35.Pin_1, C4.0, D14.COM
  N2: ADS1115.AIN2, C3.0, IC1.7
  N3: ADS1115.AIN1, J3.pin_20, C2.0
  N4: ADS1115.AIN0, C1.0, J3.pin_21
  N5: ADS1115.SDA, R29.Pin_0, ESP32.GPIO21
  N6: ADS1115.SCL, R28.Pin_0, ESP32.GPIO22
  GND: ADS1115.GND, C11.-, C10.-, C1.1, C12.-, Q7.S, Steer.cathode, Power.cathode, Wifi.cathode, Q8.S, ESP32.GND, Work.cathode, MCP2562.pin2, C6.0, R8.Pin_1, J3.pin_3, J3.pin_4, J3.pin_13, J3.pin_23, J3.pin_24, R9.Pin_0, R10.Pin_0, R11.Pin_0, TC4427.GND, 78E05.GND, C2.1, CNY17.pin2, CNY17.pin4, CNY17_2.pin2, CNY17_2.pin4, CNY17_3.pin4, R1.Pin_1, D12.A1, D13.A1, C4.1, D14.A1, C3.1, D11.A1, IRF44.source, IRF44_2.source, C13.0, IC1.5, D15.anode, D16.anode
  VDD: ADS1115.VDD, C10.+, R20.Pin_1, ESP32.VIN, MCP2562.pin3, C6.1, J3.pin_18, J3.pin_19, 78E05.output_voltage, R33.Pin_1, D14.C2, C13.1, IC1.8
  N7: D4.cathode, C11.+, 78E05.input_voltage
  N8: D4.anode, J3.pin_2
  N9: R28.Pin_1, R29.Pin_1, ESP32.3.3, MCP2562.pin5, D12.C2, D13.C2, D11.C2
  N10: R13.Pin_0, R32.Pin_0, Str_Sw.anode
  N11: R13.Pin_1, J3.pin_12
  N12: F1.pin1, C12.+, D10.cathode, F2.pin2, R35.Pin_0, R38.Pin_1
  N13: F1.pin2, IC1.1, IC1.2
  N14: Q7.G, ESP32.GPIO26, R10.Pin_1
  N15: Q7.D, R6.Pin_0, F5305.Gate, IRF44_2.Gate
  N16: R6.Pin_1, F5305.source, F5305_2.source, R7.Pin_1, R37.Pin_1, IC1.3, IC1.4
  N17: Steer.anode, R22.Pin_0
  N18: R22.Pin_1, ESP32.GPIO12
  N19: R21.Pin_0, Wifi.anode
  N20: R21.Pin_1, ESP32.GPIO13
  N21: Power.anode, R20.Pin_0
  N22: R32.Pin_1, J3.pin_16
  N23: R31.Pin_0, Wrk_Sw.anode, R14.Pin_0
  N24: R31.Pin_1, J3.pin_17
  N25: Q8.G, ESP32.GPIO25, R11.Pin_1
  N26: Q8.D, F5305_2.Gate, R7.Pin_0, IRF44.Gate
  N27: ESP32.GPIO39, D11.COM, R38.Pin_0
  N28: ESP32.GPIO34, D12.COM, R36.Pin_0
  N29: ESP32.GPIO35, R37.Pin_0, D13.COM
  N30: ESP32.GPIO27, R9.Pin_1, TC4427.IN_B
  N31: ESP32.GPIO14, R3.Pin_1
  N32: ESP32.GPIO15, CNY17.pin5
  N33: ESP32.GPIO2, CNY17_2.pin5
  N34: ESP32.GPIO4, TC4427.IN_A
  N35: ESP32.GPIO18, MCP2562.pin4
  N36: ESP32.GPIO19, MCP2562.pin1
  N37: ESP32.GPIO23, CNY17_3.pin5
  N38: Work.anode, R3.Pin_0
  N39: Str_Sw.cathode, CNY17.pin1
  N40: Wrk_Sw.cathode, CNY17_2.pin1
  N41: F5305.drain, J3.pin_8, IRF44_2.drain, D15.cathode
  N42: F5305_2.drain, J3.pin_9, IRF44.drain, D16.cathode
  N43: MCP2562.pin6, J3.pin_14
  N44: MCP2562.pin7, J3.pin_15
  N45: MCP2562.pin8, R8.Pin_0
  N46: D10.anode, J3.pin_1
  N47: Str_Whl_Sw.cathode, D5.anode
  N48: Str_Whl_Sw.anode, CNY17_3.pin2
  N49: J3.pin_5, R14.Pin_1
  N50: J3.pin_6, TC4427.OUT_A
  N51: J3.pin_7, TC4427.OUT_B
  N52: J3.pin_22, D5.cathode
  N53: TC4427.VDD, F2.pin1, R36.Pin_1
  N54: CNY17_3.pin1, R33.Pin_0

notes:
  Rev F
  Copyright Reuben Rissler 2023
  License GPLv3 - PCB design

custom parts:
  Adafruit ADS1115 16Bit I2C ADC: For microcontrollers without an analog-to-digital converter or when you want a higher-precision ADC, the ADS1115 provides 16-bit precision at 860 samples/second over I2C. The chip can be configured as 4 single-ended input channels, or two differential channels. As a nice bonus, it even includes a programmable gain amplifier, up to x16, to help boost up smaller single/differential signals to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
  Fuse PCB mount: A PCB mount fuse with 200 mil spacing.
  N-channel mosfet: A TO-92 N-channel mosfet
  ESP32-38PinWide: Generic 38-Pin ESP32 with wide format (only access to one side of pins on a breadboard) based on Stephen Lilley's HiLetgo ESP-WROOM-32 ESP32 ESP-32S Development Board.
  Rectifier Diode 600mil: A standard 3amp rectifier diode
  DTM13-12PA-12PB-R008: DTM13-12PA-12PB-R008 connector.
  TC4427: A 1.5 amp high side mosfet driver useful for driving positive loads from a microcontroller
  Voltage Regulator - 5V: 5V DC Voltage Regulator
