# Fritzing sketch Machine control Rev H (saved by Fritzing 0.9.9b)
circuit board: 10.1cm x 8.25cm
breadboards: 1

parts:
  D4 = Rectifier Diode [part_number=1N4001 package="300 mil [THT]"]
  C11 = Electrolytic Capacitor [capacitance=47µF voltage=50V package="100 mil [THT, electrolytic]"]
  C10 = Electrolytic Capacitor [capacitance=0.47mF voltage=35V package="100 mil [THT, electrolytic]"]
  R28 = Resistor [tolerance=±5% resistance=1.2k power=0.25 package=THT]
  R29 = Resistor [tolerance=±5% resistance=1.2k power=0.25 package=THT]
  R15 = Resistor [tolerance=±5% resistance=680 power=0.25 package=THT]
  C2 = Ceramic Capacitor [capacitance=100nF voltage=35V package="100 mil [THT, multilayer]"]
  F1 = Fuse PCB mount [package=THT]
  C12 = Electrolytic Capacitor [capacitance=0.1mF voltage=50V package="100 mil [THT, electrolytic]"]
  Q7 = N-channel mosfet [part_number=ZVN4206AVSTZ package="TO92 [THT]"]
  R6 = Resistor [tolerance=±5% resistance=1k power=0.25 package=THT]
  Steer = LED - 5mm [color="Red (633nm)" current=0.030 package="5 mm [THT]"]
  R22 = Resistor [tolerance=±5% resistance=470 power=0.25 package=THT]
  R21 = Resistor [tolerance=±5% resistance=470 power=0.25 package=THT]
  Power = LED - 5mm [color="Green (555nm)" current=0.030 package="5 mm [THT]"]
  R20 = Resistor [tolerance=±5% resistance=470 power=0.25 package=THT]
  Wifi = LED - 5mm [color="Yellow (595nm)" current=0.030 package="5 mm [THT]"]
  R32 = Resistor [tolerance=±5% resistance=100 power=0.25 package=THT]
  R31 = Resistor [tolerance=±5% resistance=100 power=0.25 package=THT]
  Q8 = N-channel mosfet [part_number=ZVN4206AVSTZ package="TO92 [THT]"]
  ESP32 = ESP32-38PinWide [part_number=ESP32-38PinWide]
  Work = LED - 5mm [color="Blue (525nm)" current=0.030 package="5 mm [THT]"]
  R18 = Resistor [tolerance=±5% resistance=4.7k power=0.25 package=THT]
  Str_Sw = LED - 5mm [color="Yellow (595nm)" current=0.030 package="5 mm [THT]"]
  Wrk_Sw = LED - 5mm [color="Yellow (595nm)" current=0.030 package="5 mm [THT]"]
  F5305 = Basic FET P-Channel [package="DPak [SMD]"]
  F5305_2 = Basic FET P-Channel [package="DPak [SMD]"]
  R7 = Resistor [tolerance=±5% resistance=1k power=0.25 package=THT]
  MCP2562 = IC, DIP package, 8 pins [chip_label=IC]
  C5 = Ceramic Capacitor [capacitance=100nF voltage=35V package="100 mil [THT, multilayer]"]
  R8 = Resistor [tolerance=±5% resistance=1k power=0.25 package=THT]
  D7 = Rectifier Diode 600mil [part_number=1N5400 package="600 mil [THT]"]
  Disengage = LED - 5mm [color="Yellow (595nm)" current=0.030 package="5 mm [THT]"]
  H0 = DTM13-12PA-12PB-R008 [package=THT]
  R9 = Resistor [tolerance=±5% resistance=1k power=0.25 package=THT]
  R10 = Resistor [tolerance=±5% resistance=1k power=0.25 package=THT]
  R11 = Resistor [tolerance=±5% resistance=1k power=0.25 package=THT]
  R16 = Resistor [tolerance=±5% resistance=680 power=0.25 package=THT]
  TC4427 = TC4427 [part_number=TC4427 package="DIP (Dual Inline) [THT]"]
  78E05 = Voltage Regulator - 5V [package="TO220 [THT]"]
  F2 = Fuse PCB mount [package=THT]
  C1 = Ceramic Capacitor [capacitance=100nF voltage=35V package="100 mil [THT, multilayer]"]
  R33 = Resistor [tolerance=±5% power=0.25 resistance=100 package=THT]
  R1 = Resistor [tolerance=±5% power=0.25 resistance=2.2k package=THT]
  R35 = Resistor [tolerance=±5% power=0.25 resistance=10k package=THT]
  D12 = BAV99 [package=sot23]
  R36 = Resistor [tolerance=±5% power=0.25 resistance=10k package=THT]
  R37 = Resistor [tolerance=±5% power=0.25 resistance=10k package=THT]
  D13 = BAV99 [package=sot23]
  C4 = Ceramic Capacitor [capacitance=100nF voltage=35V package="100 mil [THT, multilayer]"]
  D16 = BAV99 [package=sot23]
  C3 = Ceramic Capacitor [capacitance=100nF voltage=35V package="100 mil [THT, multilayer]"]
  D11 = BAV99 [package=sot23]
  R38 = Resistor [tolerance=±5% power=0.25 resistance=10k package=THT]
  IRF44 = Basic FET N-Channel [package="DPak [SMD]"]
  IRF44_2 = Basic FET N-Channel [package="DPak [SMD]"]
  C7 = Ceramic Capacitor [capacitance=100nF voltage=35V package="100 mil [THT, multilayer]"]
  IC1 = SO08 [chip_label=IC package=SO]
  D1 = Rectifier Diode [part_number=1N4001 package="300 mil [THT]"]
  D2 = Rectifier Diode [part_number=1N4001 package="300 mil [THT]"]
  F3 = Fuse PCB mount [package=THT]
  R2 = Resistor [tolerance=±0.1% resistance=3.3k power=0.25 package=THT]
  R3 = Resistor [tolerance=±0.1% resistance=3.3k power=0.25 package=THT]
  D15 = BAV99 [package=sot23]
  D14 = BAV99 [package=sot23]
  ADS1115 = Adafruit ADS1115 16-Bit ADC [part_number=1085]
  D10 = BAV99 [package=sot23]
  R39 = Resistor [tolerance=±5% power=0.25 resistance=10k package=THT]
  R25 = Resistor [tolerance=±0.1% power=0.25 resistance=5.6k package=THT]
  R26 = Resistor [tolerance=±0.1% power=0.25 resistance=5.6k package=THT]
  J0 = Resistor [tolerance=±5% power=0.25 resistance=0 package=THT]
  C6 = Ceramic Capacitor [capacitance=100nF voltage=35V package="100 mil [THT, multilayer]"]
  R12 = Resistor [tolerance=±5% resistance=1k power=0.25 package=THT]
  R50 = Resistor [tolerance=±0.1% power=0.25 resistance=270 package=THT]
  R51 = Resistor [tolerance=±0.1% power=0.25 resistance=270 package=THT]
  D17 = BAV99 [package=sot23]
  D18 = BAV99 [package=sot23]
  D19 = BAV99 [package=sot23]
  R42 = Resistor [tolerance=±5% power=0.25 resistance=10k package=THT]
  R41 = Resistor [tolerance=±0.1% power=0.25 resistance=10k package=THT]
  R40 = Resistor [tolerance=±0.1% power=0.25 resistance=10k package=THT]
  R44 = Resistor [tolerance=±0.1% power=0.25 resistance=10k package=THT]
  R43 = Resistor [tolerance=±0.1% power=0.25 resistance=10k package=THT]

nets:
  N1: D4.cathode, C11.+, 78E05.input_voltage
  N2: D4.anode, H0.pin_2
  GND: C11.-, C10.-, C2.0, C12.-, Q7.S, Steer.cathode, Power.cathode, Wifi.cathode, Q8.S, ESP32.GND, Work.cathode, MCP2562.pin2, C5.0, R8.Pin_1, H0.pin_3, H0.pin_4, H0.pin_13, H0.pin_23, H0.pin_24, R9.Pin_0, R10.Pin_0, R11.Pin_0, TC4427.GND, 78E05.GND, C1.0, R1.Pin_1, D12.A1, D13.A1, C4.1, D16.A1, C3.1, D11.A1, IRF44.source, IRF44_2.source, C7.0, IC1.5, D1.anode, D2.anode, D15.A1, D14.A1, ADS1115.GND, D10.A1, R25.Pin_0, R26.Pin_0, C6.0, R50.Pin_0, R51.Pin_0, D17.A1, D18.A1, D19.A1
  N3: C10.+, R20.Pin_1, ESP32.VIN, MCP2562.pin3, C5.1, 78E05.output_voltage, R33.Pin_1, C7.1, IC1.8, F3.pin2
  N4: R28.Pin_0, ESP32.GPIO22, ADS1115.SCL
  N5: R28.Pin_1, R29.Pin_1, ESP32.3.3, MCP2562.pin5, D12.C2, D13.C2, D11.C2, D10.C2, J0.Pin_1
  N6: R29.Pin_0, ESP32.GPIO21, ADS1115.SDA
  N7: R15.Pin_0, R32.Pin_0, Str_Sw.anode
  N8: R15.Pin_1, D7.anode, H0.pin_1
  N9: C2.1, D14.COM, ADS1115.AIN1, R44.Pin_0
  N10: F1.pin1, C12.+, D7.cathode, F2.pin2, R35.Pin_0, R38.Pin_1
  N11: F1.pin2, IC1.1, IC1.2
  N12: Q7.G, ESP32.GPIO26, R10.Pin_1
  N13: Q7.D, R6.Pin_0, F5305.Gate, IRF44_2.Gate
  N14: R6.Pin_1, F5305.source, F5305_2.source, R7.Pin_1, R37.Pin_1, IC1.3, IC1.4
  N15: Steer.anode, R22.Pin_0
  N16: R22.Pin_1, ESP32.GPIO12
  N17: R21.Pin_0, Wifi.anode
  N18: R21.Pin_1, ESP32.GPIO13
  N19: Power.anode, R20.Pin_0
  N20: R32.Pin_1, H0.pin_16
  N21: R31.Pin_0, Wrk_Sw.anode, R16.Pin_0
  N22: R31.Pin_1, H0.pin_17
  N23: Q8.G, ESP32.GPIO25, R11.Pin_1
  N24: Q8.D, F5305_2.Gate, R7.Pin_0, IRF44.Gate
  N25: ESP32.GPIO36, D10.COM, R39.Pin_0
  N26: ESP32.GPIO39, D11.COM, R38.Pin_0
  N27: ESP32.GPIO34, D12.COM, R36.Pin_0
  N28: ESP32.GPIO35, R37.Pin_0, D13.COM
  N29: ESP32.GPIO27, R9.Pin_1, TC4427.IN_B
  N30: ESP32.GPIO14, R18.Pin_1
  N31: ESP32.GPIO15, D18.COM, R40.Pin_1
  N32: ESP32.GPIO2, D17.COM, R41.Pin_1
  N33: ESP32.GPIO4, TC4427.IN_A
  N34: ESP32.GPIO18, MCP2562.pin4
  N35: ESP32.GPIO19, MCP2562.pin1
  N36: ESP32.GPIO23, D19.COM, R42.Pin_1
  N37: Work.anode, R18.Pin_0
  N38: Str_Sw.cathode, R50.Pin_1, R40.Pin_0
  N39: Wrk_Sw.cathode, R51.Pin_1, R41.Pin_0
  N40: F5305.drain, H0.pin_8, IRF44_2.drain, D1.cathode
  N41: F5305_2.drain, H0.pin_9, IRF44.drain, D2.cathode
  N42: MCP2562.pin6, H0.pin_14
  N43: MCP2562.pin7, H0.pin_15
  N44: MCP2562.pin8, R8.Pin_0
  N45: Disengage.cathode, H0.pin_22, R42.Pin_0
  N46: Disengage.anode, R33.Pin_0
  N47: H0.pin_5, R16.Pin_1
  N48: H0.pin_6, TC4427.OUT_A
  N49: H0.pin_7, R12.Pin_1
  N50: H0.pin_18, H0.pin_19, F3.pin1, R39.Pin_1
  N51: H0.pin_20, R3.Pin_1
  N52: H0.pin_21, R2.Pin_1
  N53: TC4427.OUT_B, R12.Pin_0
  N54: TC4427.VDD, F2.pin1, R36.Pin_1
  N55: C1.1, D15.COM, ADS1115.AIN0, R43.Pin_0
  N56: R1.Pin_0, R35.Pin_1, C4.0, D16.COM, ADS1115.AIN3
  N57: D16.C2, ADS1115.VCC, J0.Pin_0, C6.1, D17.C2, D18.C2, D19.C2
  N58: C3.0, IC1.7, ADS1115.AIN2
  N59: R2.Pin_0, R25.Pin_1, R43.Pin_1
  N60: R3.Pin_0, R26.Pin_1, R44.Pin_1
  N61: D15.C2, D14.C2, ADS1115.AVDD

notes:
  Rev H
  Copyright Reuben Rissler 2023
  License GPLv3 - PCB design
  A- A0 A1 A2 A3 A+
  SCL
  SDA
  GND
  VIN
  ADDR
  ALRT

custom parts:
  Fuse PCB mount: A PCB mount fuse with 200 mil spacing.
  N-channel mosfet: A TO-92 N-channel mosfet
  ESP32-38PinWide: Generic 38-Pin ESP32 with wide format (only access to one side of pins on a breadboard) based on Stephen Lilley's HiLetgo ESP-WROOM-32 ESP32 ESP-32S Development Board.
  Rectifier Diode 600mil: A standard 3amp rectifier diode
  DTM13-12PA-12PB-R008: DTM13-12PA-12PB-R008 connector.
  TC4427: A 1.5 amp high side mosfet driver useful for driving positive loads from a microcontroller
  Voltage Regulator - 5V: 5V DC Voltage Regulator
  Adafruit ADS1115 16-Bit ADC: For microcontrollers without an analog-to-digital converter or when you want a higher-precision ADC, the ADS1115 provides 16-bit precision at 860 samples/second over I2C. The chip can be configured as 4 single-ended input channels, or two differential channels. As a nice bonus, it even includes a programmable gain amplifier, up to x16, to help boost up smaller single/differential signals to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
