# Fritzing sketch Power control compact Rev A (saved by Fritzing 1.0.1rc)
circuit board: 6.2cm x 8.25cm
breadboards: 1

parts:
  J1 = DTM13-12PA-R008 [package=THT]
  D1 = Rectifier Diode [part_number=1N4001 package="300 mil [THT]"]
  7805 = Voltage Regulator - 5V [package="DPak [SMD]"]
  LED2 = LED - 5mm [color="Red (633nm)" current=0.030 package="5 mm [THT]"]
  TINY45 = attiny85 [package=dip]
  D2 = Rectifier Diode [part_number=1N4001 package="300 mil [THT]"]
  D3 = Rectifier Diode [part_number=1N4001 package="300 mil [THT]"]
  OMRON = OMRON PCB Power Relay – G5LE [part_number="G5LE-1\n" package=THT]
  C1 = Electrolytic Capacitor [capacitance=0.1mF voltage=6.3V package="100 mil [THT, electrolytic]"]
  C2 = Electrolytic Capacitor [capacitance=1µF voltage=35V package="100 mil [THT, electrolytic]"]
  R1 = Resistor [tolerance=±5% power=0.25 resistance=330 package=THT]
  R3 = Resistor [tolerance=±5% power=0.25 resistance=4.7k package=THT]
  R9 = Resistor [tolerance=±5% power=0.25 resistance=10k package=THT]
  TC4427 = TC4427 [part_number=TC4427 package="DIP (Dual Inline) [THT]"]
  D4 = Rectifier Diode [part_number=1N4001 package="300 mil [THT]"]
  LM2585 = LM2585 [part_number=LM2585 package=TO263-5L]
  D5 = Rectifier Diode 600mil [part_number=1N5400 package="600 mil [THT]"]
  R5 = Resistor [tolerance=±5% power=0.25W resistance=220 package=THT]
  R6 = Resistor [tolerance=±5% power=0.25W resistance=220 package=THT]
  C7 = Ceramic Capacitor [capacitance=100nF voltage=35V package="100 mil [THT, multilayer]"]
  C10 = Electrolytic Capacitor [package="300 mil [THT, electrolytic]"]
  D8 = Rectifier Diode 600mil [part_number=1N5400 package="600 mil [THT]"]
  L1 = Inductor [mpn=2311-H-RC package="[THT]"]
  R10 = Resistor [tolerance=±5% power=0.25W resistance=220 package=THT]
  C8 = Ceramic Capacitor [capacitance=100nF voltage=35V package="100 mil [THT, multilayer]"]
  C3 = Electrolytic Capacitor [capacitance=1µF voltage=35V package="100 mil [THT, electrolytic]"]
  C9 = Ceramic Capacitor [capacitance=100nF voltage=35V package="100 mil [THT, multilayer]"]

nets:
  N1: J1.pin_1, J1.pin_2, D5.cathode, R6.Pin_1, C10.+
  N2: J1.pin_3, J1.pin_4, OMRON.C, TC4427.VDD, D4.anode, D8.anode
  N3: J1.pin_5, OMRON.A
  N4: J1.pin_6, D1.anode
  GND: J1.pin_7, J1.pin_8, J1.pin_9, 7805.GND, LED2.cathode, TINY45.Pin_4, D3.anode, OMRON.COIL1, C1.-, C2.-, R3.Pin_1, TC4427.GND
  N5: J1.pin_10, J1.pin_11, J1.pin_12, LM2585.Pin_3, LM2585.Tab, R5.Pin_1, C7.0, C10.-, C8.1, C3.-, C9.1
  N6: D1.cathode, D2.cathode, D3.cathode, OMRON.COIL2
  N7: 7805.input_voltage, C2.+, R9.Pin_0, D4.cathode
  N8: 7805.output_voltage, TINY45.Pin_1, TINY45.Pin_8, C1.+
  N9: LED2.anode, R1.Pin_1
  N10: TINY45.Pin_5, R3.Pin_0, R9.Pin_1
  N11: TINY45.Pin_6, R1.Pin_0
  N12: TINY45.Pin_7, TC4427.IN_A
  N13: D2.anode, TC4427.OUT_A
  N14: LM2585.Pin_1, R10.Pin_0
  N15: LM2585.Pin_2, R5.Pin_0, R6.Pin_0, C7.1
  N16: LM2585.Pin_4, D5.anode, L1.pin_0
  N17: LM2585.Pin_5, D8.cathode, L1.pin_1, C3.+, C9.0
  N18: R10.Pin_1, C8.0

notes:
  License GPLv3 - PCB design
  Rev A
  Ign 12V timed  19V
  Copyright Reuben Rissler 2024

custom parts:
  DTM13-12PA-R008: DTM13-12PA-R008 connector.
  TC4427: A 1.5 amp high side mosfet driver useful for driving positive loads from a microcontroller
  LM2585: LM2585 3A 100KHz 60V Buck DC to DC in TO2635L package. Allthough the specifications of the LM2575 (1A) and LM2576 (3A) are far from impressive today, they are still acceptable in many situations. The main advantage of the LM2575/LM2576 is that it is available from many vendors and therefore low-cost and easy to find. Many vendors offer more advanced regulators that are pinout compatible with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
  Rectifier Diode 600mil: A standard 3amp rectifier diode
  Electrolytic Capacitor: 1000µF electrolytic capacitor
  Inductor: Inductor ferrite core 68uH 7.7A
