# Fritzing sketch Power control compact Rev B (saved by Fritzing 1.0.1rc)
circuit board: 6.2cm x 8.25cm
breadboards: 1

parts:
  J1 = DTM13-12PA-R008 [package=THT]
  D1 = Rectifier Diode [part_number=1N4001 package="300 mil [THT]"]
  7805 = Voltage Regulator - 5V [package="DPak [SMD]"]
  LED2 = LED - 5mm [color="Red (633nm)" current=0.030 package="5 mm [THT]"]
  TINY45 = attiny85 [package=dip]
  D4 = Rectifier Diode [part_number=1N4001 package="300 mil [THT]"]
  OMRON = OMRON PCB Power Relay – G5LE [part_number="G5LE-1\n" package=THT]
  C1 = Electrolytic Capacitor [capacitance=0.1mF voltage=6.3V package="100 mil [THT, electrolytic]"]
  C2 = Electrolytic Capacitor [capacitance=1µF voltage=35V package="100 mil [THT, electrolytic]"]
  R1 = Resistor [tolerance=±5% power=0.25 resistance=330 package=THT]
  R3 = Resistor [tolerance=±5% power=0.25 resistance=4.7k package=THT]
  R8 = Resistor [tolerance=±5% power=0.25 resistance=10k package=THT]
  TC4427 = TC4427 [part_number=TC4427 package="DIP (Dual Inline) [THT]"]
  D2 = Rectifier Diode [part_number=1N4001 package="300 mil [THT]"]
  R5 = Resistor [tolerance=±5% power=0.25W resistance=33k package=THT]
  R6 = Resistor [tolerance=±5% power=0.25W resistance=390k package=THT]
  C7 = Ceramic Capacitor [capacitance=100nF voltage=35V package="100 mil [THT, multilayer]"]
  D6 = Rectifier Diode 600mil [part_number=1N5400 package="600 mil [THT]"]
  C4 = Electrolytic Capacitor [capacitance=0.47mF voltage=35V package="200 mil [THT, electrolytic]"]
  Max1771 = mystery part, 8 pins [chip_label=? mpn=MAX1771]
  C9 = Ceramic Capacitor [capacitance=100nF voltage=35V package="100 mil [THT, multilayer]"]
  Q1 = Basic FET N-Channel [package="DPak [SMD]"]
  L1 = Inductor [mpn=2311-H-RC package="[THT]"]
  C3 = Electrolytic Capacitor [capacitance=0.47mF voltage=35V package="200 mil [THT, electrolytic]"]
  R15 = Resistor [tolerance=±5% resistance=40m power=0.25W package="2512 [SMD]"]
  C8 = Ceramic Capacitor [capacitance=100nF voltage=35V package="100 mil [THT, multilayer]"]
  D3 = Rectifier Diode [part_number=1N4001 package="300 mil [THT]"]
  R10 = Resistor [tolerance=±5% power=0.25 resistance=10k package=THT]
  R11 = Resistor [tolerance=±5% power=0.25 resistance=10k package=THT]

nets:
  N1: J1.pin_1, J1.pin_2, R6.Pin_1, C7.0, D6.cathode, C3.+
  N2: J1.pin_3, J1.pin_4, OMRON.A, D3.anode
  N3: J1.pin_5, D1.cathode, 7805.input_voltage, C2.+, D2.cathode
  N4: J1.pin_6, D1.anode, R8.Pin_0
  GND: J1.pin_7, J1.pin_8, J1.pin_9, 7805.GND, LED2.cathode, TINY45.Pin_4, D4.anode, OMRON.COIL1, C1.-, C2.-, R3.Pin_1, TC4427.GND, R10.Pin_1, R11.Pin_1
  N5: J1.pin_10, J1.pin_11, J1.pin_12, R5.Pin_1, C4.-, Max1771.pin4, Max1771.pin6, Max1771.pin7, C9.1, C3.-, R15.Pin_0, C8.0
  N6: 7805.output_voltage, TINY45.Pin_1, TINY45.Pin_8, C1.+
  N7: LED2.anode, R1.Pin_1
  N8: TINY45.Pin_3, TC4427.IN_B, R10.Pin_0
  N9: TINY45.Pin_5, R3.Pin_0, R8.Pin_1
  N10: TINY45.Pin_6, R1.Pin_0
  N11: TINY45.Pin_7, TC4427.IN_A, R11.Pin_0
  N12: D4.cathode, OMRON.COIL2, TC4427.OUT_A
  N13: OMRON.C, C4.+, Max1771.pin2, L1.pin_1, C8.1
  N14: TC4427.OUT_B, D2.anode
  N15: TC4427.VDD, D3.cathode
  N16: R5.Pin_0, R6.Pin_0, C7.1, Max1771.pin3
  N17: D6.anode, Q1.drain, L1.pin_0
  N18: Max1771.pin1, Q1.Gate
  N19: Max1771.pin5, C9.0
  N20: Max1771.pin8, Q1.source, R15.Pin_1

notes:
  License GPLv3 - PCB design
  Ign Rtr Battery   19V
  Copyright Reuben Rissler 2025
  Rev B
  Logic Gnd |  PS Gnd

custom parts:
  DTM13-12PA-R008: DTM13-12PA-R008 connector.
  TC4427: A 1.5 amp high side mosfet driver useful for driving positive loads from a microcontroller
  Rectifier Diode 600mil: A standard 3amp rectifier diode
  Inductor: Inductor ferrite core 68uH 7.7A
