# Fritzing sketch Power distribution Rev A (saved by Fritzing 0.9.9b)
circuit board: 17.4cm x 7.43cm
breadboards: 1

parts:
  T9AS5D22-12 = RELAY [package=relay-t9a]
  + = Quick connect terminal - 0.25" [package=THT]
  +_2 = Quick connect terminal - 0.25" [package=THT]
  +_3 = Quick connect terminal - 0.25" [package=THT]
  - = Quick connect terminal - 0.25" [package=THT]
  D2 = Rectifier Diode [part_number=1N4001 package="300 mil [THT]"]
  -5V+ = screw terminal, 2 pins
  D3 = Rectifier Diode [part_number=1N4001 package="300 mil [THT]"]
  OMRON1 = OMRON PCB Power Relay – G5LE [part_number="G5LE-1\n" package=THT]
  D4 = Rectifier Diode [part_number=1N4001 package="300 mil [THT]"]
  78E05 = Voltage Regulator - 5V [package="TO220 [THT]"]
  C1 = Electrolytic Capacitor [capacitance=1µF voltage=35V package="100 mil [THT, electrolytic]"]
  C2 = Electrolytic Capacitor [capacitance=0.1mF voltage=6.3V package="100 mil [THT, electrolytic]"]
  D5 = Rectifier Diode [part_number=1N4001 package="300 mil [THT]"]
  R1 = Resistor [tolerance=±5% power=0.25 resistance=10k package=THT]
  TC4427 = TC4427 [part_number=TC4427 package="DIP (Dual Inline) [THT]"]
  D6 = Rectifier Diode [part_number=1N4001 package="300 mil [THT]"]
  Fuse1 = Fuseholder [part_number=3557-2]
  -_2 = Quick connect terminal - 0.25" [package=THT]
  -_3 = Quick connect terminal - 0.25" [package=THT]
  -_4 = Quick connect terminal - 0.25" [package=THT]
  -_5 = Quick connect terminal - 0.25" [package=THT]
  -_6 = Quick connect terminal - 0.25" [package=THT]
  -_7 = Quick connect terminal - 0.25" [package=THT]
  -_8 = Quick connect terminal - 0.25" [package=THT]
  +_4 = Quick connect terminal - 0.25" [package=THT]
  +_5 = Quick connect terminal - 0.25" [package=THT]
  +_6 = Quick connect terminal - 0.25" [package=THT]
  +_7 = Quick connect terminal - 0.25" [package=THT]
  +_8 = Quick connect terminal - 0.25" [package=THT]
  +_9 = Quick connect terminal - 0.25" [package=THT]
  +_10 = Quick connect terminal - 0.25" [package=THT]
  Fuse2 = Fuseholder [part_number=3557-2]
  Fuse3 = Fuseholder [part_number=3557-2]
  Fuse4 = Fuseholder [part_number=3557-2]
  Fuse5 = Fuseholder [part_number=3557-2]
  Fuse6 = Fuseholder [part_number=3557-2]
  Fuse7 = Fuseholder [part_number=3557-2]
  Fuse8 = Fuseholder [part_number=3557-2]
  Fuse9 = Fuseholder [part_number=3557-2]
  TINY45 = attiny85 [package=dip]
  D5_2 = Rectifier Diode [part_number=1N4001 package="300 mil [THT]"]
  LED1 = LED - 5mm [color="Red (633nm)" current=0.030 package="5 mm [THT]"]
  R2 = Resistor [tolerance=±5% power=0.25 resistance=330 package=THT]

nets:
  GND: T9AS5D22-12.COIL1, -.pin1, -.pin2, D2.anode, -5V+.pin1, OMRON1.COIL1, D4.anode, 78E05.GND, C1.-, C2.-, TC4427.GND, -_2.pin1, -_2.pin2, -_3.pin1, -_3.pin2, -_4.pin1, -_4.pin2, -_5.pin1, -_5.pin2, -_6.pin1, -_6.pin2, -_7.pin1, -_7.pin2, -_8.pin1, -_8.pin2, TINY45.Pin_4, LED1.cathode
  N1: T9AS5D22-12.COIL2, D2.cathode, D6.cathode
  N2: T9AS5D22-12.MAIN, OMRON1.C
  N3: T9AS5D22-12.NO, D3.anode, R1.Pin_0, Fuse1.Connector2, Fuse1.Connector4, Fuse2.Connector2, Fuse2.Connector4, Fuse3.Connector2, Fuse3.Connector4, Fuse4.Connector2, Fuse4.Connector4, Fuse5.Connector2, Fuse5.Connector4, Fuse6.Connector2, Fuse6.Connector4, Fuse7.Connector2, Fuse7.Connector4, Fuse8.Connector2, Fuse8.Connector4
  N4: +.pin1, +.pin2, Fuse1.Connector1, Fuse1.Connector3
  N5: +_2.pin1, +_2.pin2, +_3.pin1, +_3.pin2, Fuse9.Connector2, Fuse9.Connector4
  N6: -5V+.pin2, 78E05.output_voltage, C2.+, TINY45.Pin_1, TINY45.Pin_8
  N7: D3.cathode, OMRON1.COIL2, D4.cathode, D5_2.cathode
  N8: OMRON1.A, D5.anode, TC4427.VDD, Fuse9.Connector1, Fuse9.Connector3
  N9: 78E05.input_voltage, C1.+, D5.cathode
  N10: R1.Pin_1, TINY45.Pin_5
  N11: TC4427.IN_A, TINY45.Pin_7
  N12: TC4427.OUT_A, D5_2.anode
  N13: +_4.pin1, +_4.pin2, Fuse2.Connector1, Fuse2.Connector3
  N14: +_5.pin1, +_5.pin2, Fuse3.Connector1, Fuse3.Connector3
  N15: +_6.pin1, +_6.pin2, Fuse4.Connector1, Fuse4.Connector3
  N16: +_7.pin1, +_7.pin2, Fuse5.Connector1, Fuse5.Connector3
  N17: +_8.pin1, +_8.pin2, Fuse6.Connector1, Fuse6.Connector3
  N18: +_9.pin1, +_9.pin2, Fuse7.Connector1, Fuse7.Connector3
  N19: +_10.pin1, +_10.pin2, Fuse8.Connector1, Fuse8.Connector3
  N20: TINY45.Pin_6, R2.Pin_0
  N21: LED1.anode, R2.Pin_1

notes:
  BAT-
  IGN
  BAT+
  |--off delay--|
  5A max
  power fuses 10A max
  Rev A
  Copyright Reuben Rissler license GPLv3

custom parts:
  RELAY: SPDT relay TE T9AP/S
  Quick connect terminal - 0.25": Disconnect terminal
  Voltage Regulator - 5V: 5V DC Voltage Regulator
  TC4427: A 1.5 amp high side mosfet driver useful for driving positive loads from a microcontroller
  Fuseholder: Device used to protect against excessive current.
