# Fritzing sketch Section control Rev A (saved by Fritzing 0.9.3b)
circuit board: 18cm x 9.5cm
breadboards: 1

parts:
  ESP32 = ESP32-38PinWide [part_number=ESP32-38PinWide]
  QL1 = Basic FET P-Channel [package="DPak [SMD]"]
  QL2 = Basic FET P-Channel [package="DPak [SMD]"]
  QL3 = Basic FET P-Channel [package="DPak [SMD]"]
  QL4 = Basic FET P-Channel [package="DPak [SMD]"]
  QL5 = Basic FET P-Channel [package="DPak [SMD]"]
  QL7 = Basic FET P-Channel [package="DPak [SMD]"]
  QL8 = Basic FET P-Channel [package="DPak [SMD]"]
  QL9 = Basic FET P-Channel [package="DPak [SMD]"]
  QL10 = Basic FET P-Channel [package="DPak [SMD]"]
  QL11 = Basic FET P-Channel [package="DPak [SMD]"]
  QL12 = Basic FET P-Channel [package="DPak [SMD]"]
  QL13 = Basic FET P-Channel [package="DPak [SMD]"]
  QL14 = Basic FET P-Channel [package="DPak [SMD]"]
  QL15 = Basic FET P-Channel [package="DPak [SMD]"]
  QL6 = Basic FET P-Channel [package="DPak [SMD]"]
  QL16 = Basic FET P-Channel [package="DPak [SMD]"]
  D1 = Rectifier Diode [part_number=1N4001 package="300 mil [THT]"]
  D2 = Rectifier Diode [part_number=1N4001 package="300 mil [THT]"]
  D3 = Rectifier Diode [part_number=1N4001 package="300 mil [THT]"]
  D4 = Rectifier Diode [part_number=1N4001 package="300 mil [THT]"]
  D5 = Rectifier Diode [part_number=1N4001 package="300 mil [THT]"]
  D6 = Rectifier Diode [part_number=1N4001 package="300 mil [THT]"]
  D7 = Rectifier Diode [part_number=1N4001 package="300 mil [THT]"]
  D8 = Rectifier Diode [part_number=1N4001 package="300 mil [THT]"]
  D9 = Rectifier Diode [part_number=1N4001 package="300 mil [THT]"]
  D10 = Rectifier Diode [part_number=1N4001 package="300 mil [THT]"]
  D11 = Rectifier Diode [part_number=1N4001 package="300 mil [THT]"]
  D12 = Rectifier Diode [part_number=1N4001 package="300 mil [THT]"]
  D13 = Rectifier Diode [part_number=1N4001 package="300 mil [THT]"]
  D14 = Rectifier Diode [part_number=1N4001 package="300 mil [THT]"]
  D15 = Rectifier Diode [part_number=1N4001 package="300 mil [THT]"]
  D16 = Rectifier Diode [part_number=1N4001 package="300 mil [THT]"]
  U5 = RELAY [package=relay-t9a]
  D17 = Rectifier Diode [part_number=1N4001 package="300 mil [THT]"]
  D18 = Rectifier Diode [part_number=1N4001 package="300 mil [THT]"]
  D19 = Rectifier Diode [part_number=1N4001 package="300 mil [THT]"]
  C1 = Electrolytic Capacitor [capacitance=1µF package="100 mil [THT, electrolytic]"]
  C2 = Electrolytic Capacitor [capacitance=1µF package="100 mil [THT, electrolytic]"]
  R17 = Resistor [tolerance=±5% resistance=220 package=THT]
  R18 = Resistor [tolerance=±5% resistance=1k package=THT]
  R19 = Resistor [tolerance=±5% resistance=1k package=THT]
  R20 = Resistor [tolerance=±5% resistance=1k package=THT]
  R21 = Resistor [tolerance=±5% resistance=1k package=THT]
  R22 = Resistor [tolerance=±5% resistance=1k package=THT]
  R23 = Resistor [tolerance=±5% resistance=1k package=THT]
  R24 = Resistor [tolerance=±5% resistance=1k package=THT]
  R25 = Resistor [tolerance=±5% resistance=1k package=THT]
  R26 = Resistor [tolerance=±5% resistance=1k package=THT]
  R27 = Resistor [tolerance=±5% resistance=1k package=THT]
  R28 = Resistor [tolerance=±5% resistance=1k package=THT]
  R29 = Resistor [tolerance=±5% resistance=1k package=THT]
  R30 = Resistor [tolerance=±5% resistance=1k package=THT]
  R31 = Resistor [tolerance=±5% resistance=1k package=THT]
  R32 = Resistor [tolerance=±5% resistance=1k package=THT]
  F1 = Fuse PCB mount [package=THT]
  F2 = Fuse PCB mount [package=THT]
  F3 = Fuse PCB mount [package=THT]
  F4 = Fuse PCB mount [package=THT]
  F5 = Fuse PCB mount [package=THT]
  F6 = Fuse PCB mount [package=THT]
  F7 = Fuse PCB mount [package=THT]
  F8 = Fuse PCB mount [package=THT]
  F9 = Fuse PCB mount [package=THT]
  F10 = Fuse PCB mount [package=THT]
  F11 = Fuse PCB mount [package=THT]
  F12 = Fuse PCB mount [package=THT]
  F13 = Fuse PCB mount [package=THT]
  F14 = Fuse PCB mount [package=THT]
  F15 = Fuse PCB mount [package=THT]
  F16 = Fuse PCB mount [package=THT]
  R33 = Resistor [tolerance=±5% resistance=220 package=THT]
  LED1 = LED - 5mm [color="Green (555nm)" current=20m package="5 mm [THT]"]
  LED2 = LED - 5mm [color="Green (555nm)" current=20m package="5 mm [THT]"]
  LED3 = LED - 5mm [color="Green (555nm)" current=20m package="5 mm [THT]"]
  LED4 = LED - 5mm [color="Green (555nm)" current=20m package="5 mm [THT]"]
  LED5 = LED - 5mm [color="Green (555nm)" current=20m package="5 mm [THT]"]
  LED6 = LED - 5mm [color="Green (555nm)" current=20m package="5 mm [THT]"]
  LED7 = LED - 5mm [color="Green (555nm)" current=20m package="5 mm [THT]"]
  LED8 = LED - 5mm [color="Green (555nm)" current=20m package="5 mm [THT]"]
  LED9 = LED - 5mm [color="Green (555nm)" current=20m package="5 mm [THT]"]
  LED10 = LED - 5mm [color="Green (555nm)" current=20m package="5 mm [THT]"]
  LED11 = LED - 5mm [color="Green (555nm)" current=20m package="5 mm [THT]"]
  LED12 = LED - 5mm [color="Green (555nm)" current=20m package="5 mm [THT]"]
  LED13 = LED - 5mm [color="Green (555nm)" current=20m package="5 mm [THT]"]
  LED14 = LED - 5mm [color="Green (555nm)" current=20m package="5 mm [THT]"]
  LED15 = LED - 5mm [color="Green (555nm)" current=20m package="5 mm [THT]"]
  LED16 = LED - 5mm [color="Green (555nm)" current=20m package="5 mm [THT]"]
  R34 = Resistor [tolerance=±5% resistance=220 package=THT]
  R35 = Resistor [tolerance=±5% resistance=220 package=THT]
  R36 = Resistor [tolerance=±5% resistance=220 package=THT]
  R37 = Resistor [tolerance=±5% resistance=220 package=THT]
  R38 = Resistor [tolerance=±5% resistance=220 package=THT]
  R39 = Resistor [tolerance=±5% resistance=220 package=THT]
  R40 = Resistor [tolerance=±5% resistance=220 package=THT]
  R41 = Resistor [tolerance=±5% resistance=220 package=THT]
  R42 = Resistor [tolerance=±5% resistance=220 package=THT]
  R43 = Resistor [tolerance=±5% resistance=220 package=THT]
  R44 = Resistor [tolerance=±5% resistance=220 package=THT]
  R45 = Resistor [tolerance=±5% resistance=220 package=THT]
  R46 = Resistor [tolerance=±5% resistance=220 package=THT]
  R47 = Resistor [tolerance=±5% resistance=220 package=THT]
  R48 = Resistor [tolerance=±5% resistance=220 package=THT]
  S15 = SPDT Switch
  S14 = SPDT Switch
  S18 = SPDT Switch
  S1 = SPDT Switch
  S3 = SPDT Switch
  S12 = SPDT Switch
  S5 = SPDT Switch
  S7 = SPDT Switch
  S9 = SPDT Switch
  S17 = SPDT Switch
  S13 = SPDT Switch
  S6 = SPDT Switch
  S11 = SPDT Switch
  S8 = SPDT Switch
  S16 = SPDT Switch
  S10 = SPDT Switch
  S4 = SPDT Switch
  S2 = SPDT Switch
  LED17 = LED - 5mm [color="Green (555nm)" current=20m package="5 mm [THT]"]
  R49 = Resistor [tolerance=±5% resistance=220 package=THT]
  WiFi = LED - 5mm [color="Yellow (595nm)" package="5 mm [THT]"]
  R50 = Resistor [tolerance=±5% resistance=100 package=THT]
  U6 = Voltage Regulator - 5V [package="TO220 [THT]"]
  D20 = Rectifier Diode [part_number=1N4001 package="300 mil [THT]"]

nets:
  N1: ESP32.GPIO34, S18.O
  N2: ESP32.GPIO35, S18.S
  N3: ESP32.GPIO32, R50.Pin_1
  N4: ESP32.GPIO27, QL13.Gate, R29.Pin_0
  N5: ESP32.GPIO14, QL14.Gate, R30.Pin_0
  N6: ESP32.GPIO12, QL15.Gate, R31.Pin_0
  GND: ESP32.GND, D18.cathode, C1.-, C2.-, R17.Pin_0, R18.Pin_0, R19.Pin_0, R20.Pin_0, R21.Pin_0, R22.Pin_0, R23.Pin_0, R24.Pin_0, R25.Pin_0, R26.Pin_0, R27.Pin_0, R28.Pin_0, R29.Pin_1, R30.Pin_1, R31.Pin_1, R32.Pin_1, S18.P, S17.S, WiFi.cathode, U6.GND
  N7: ESP32.GPIO13, QL16.Gate, R32.Pin_0
  N8: ESP32.VIN, C2.+, U6.output_voltage
  N9: ESP32.GPIO15, QL12.Gate, R28.Pin_1
  N10: ESP32.GPIO2, QL11.Gate, R27.Pin_1
  N11: ESP32.GPIO0, QL10.Gate, R26.Pin_1
  N12: ESP32.GPIO4, QL9.Gate, R25.Pin_1
  N13: ESP32.GPIO16, QL8.Gate, R24.Pin_1
  N14: ESP32.GPIO17, QL7.Gate, R23.Pin_1
  N15: ESP32.GPIO5, QL6.Gate, R22.Pin_1
  N16: ESP32.GPIO18, QL5.Gate, R21.Pin_1
  N17: ESP32.GPIO19, QL4.Gate, R20.Pin_1
  N18: ESP32.GPIO21, QL3.Gate, R19.Pin_1
  N19: ESP32.GPIO22, QL2.Gate, R18.Pin_1
  N20: ESP32.GPIO23, QL1.Gate, R17.Pin_1
  N21: QL1.drain, D1.anode, F1.pin1, S1.P, S1.S
  N22: QL1.source, QL2.source, QL3.source, QL4.source, QL5.source, QL7.source, QL8.source, QL9.source, QL10.source, QL11.source, QL12.source, QL13.source, QL14.source, QL15.source, QL6.source, QL16.source, U5.MAIN, S15.O, S14.O, S1.O, S3.O, S12.O, S5.O, S7.O, S9.O, S13.O, S6.O, S11.O, S8.O, S16.O, S10.O, S4.O, S2.O, LED17.cathode
  N23: QL2.drain, D2.anode, F2.pin1, S2.P, S2.S
  N24: QL3.drain, D3.anode, F3.pin1, S3.P, S3.S
  N25: QL4.drain, D4.anode, F4.pin1, S4.P, S4.S
  N26: QL5.drain, D5.anode, F5.pin1, S5.P, S5.S
  N27: QL7.drain, D7.anode, F7.pin1, S7.P, S7.S
  N28: QL8.drain, D8.anode, F8.pin1, S8.P, S8.S
  N29: QL9.drain, D9.anode, F9.pin1, S9.P, S9.S
  N30: QL10.drain, D10.anode, F10.pin1, S10.P, S10.S
  N31: QL11.drain, D11.anode, F11.pin1, S11.P, S11.S
  N32: QL12.drain, D12.anode, F12.pin1, S12.P, S12.S
  N33: QL13.drain, D13.anode, F13.pin1, S13.P, S13.S
  N34: QL14.drain, D14.anode, F14.pin1, S14.P, S14.S
  N35: QL15.drain, D15.anode, F15.pin1, S15.P, S15.S
  N36: QL6.drain, D6.anode, F6.pin1, S6.P, S6.S
  N37: QL16.drain, D16.anode, F16.pin1, S16.P, S16.S
  N38: D1.cathode, D2.cathode, D3.cathode, D4.cathode, D5.cathode, D6.cathode, D7.cathode, D8.cathode, D9.cathode, D10.cathode, D11.cathode, D12.cathode, D13.cathode, D14.cathode, D15.cathode, D16.cathode, LED1.anode, LED2.anode, LED3.anode, LED4.anode, LED5.anode, LED6.anode, LED7.anode, LED8.anode, LED9.anode, LED10.anode, LED11.anode, LED12.anode, LED13.anode, LED14.anode, LED15.anode, LED16.anode, D20.anode
  N39: U5.COIL1, D19.cathode, C1.+, R49.Pin_0, U6.input_voltage, D20.cathode
  N40: U5.COIL2, D18.anode, D19.anode, S17.O
  N41: U5.NO, D17.cathode
  N42: D17.anode, S17.P
  N43: F1.pin2, R33.Pin_0
  N44: F2.pin2, R34.Pin_0
  N45: F3.pin2, R35.Pin_0
  N46: F4.pin2, R36.Pin_0
  N47: F5.pin2, R37.Pin_0
  N48: F6.pin2, R38.Pin_0
  N49: F7.pin2, R39.Pin_0
  N50: F8.pin2, R40.Pin_0
  N51: F9.pin2, R41.Pin_0
  N52: F10.pin2, R42.Pin_0
  N53: F11.pin2, R43.Pin_0
  N54: F12.pin2, R44.Pin_0
  N55: F13.pin2, R45.Pin_0
  N56: F14.pin2, R46.Pin_0
  N57: F15.pin2, R47.Pin_0
  N58: F16.pin2, R48.Pin_0
  N59: R33.Pin_1, LED1.cathode
  N60: LED2.cathode, R34.Pin_1
  N61: LED3.cathode, R35.Pin_1
  N62: LED4.cathode, R36.Pin_1
  N63: LED5.cathode, R37.Pin_1
  N64: LED6.cathode, R38.Pin_1
  N65: LED7.cathode, R39.Pin_1
  N66: LED8.cathode, R40.Pin_1
  N67: LED9.cathode, R41.Pin_1
  N68: LED10.cathode, R42.Pin_1
  N69: LED11.cathode, R43.Pin_1
  N70: LED12.cathode, R44.Pin_1
  N71: LED13.cathode, R45.Pin_1
  N72: LED14.cathode, R46.Pin_1
  N73: LED15.cathode, R47.Pin_1
  N74: LED16.cathode, R48.Pin_1
  N75: LED17.anode, R49.Pin_1
  N76: WiFi.anode, R50.Pin_0

notes:
  -
  +
  Rev A
  Copyright Silicon Reparation 2021
  License GPLv3 PCB design

custom parts:
  ESP32-38PinWide: Generic 38-Pin ESP32 with wide format (only access to one side of pins on a breadboard) based on Stephen Lilley's HiLetgo ESP-WROOM-32 ESP32 ESP-32S Development Board.
  RELAY: SPST 30A relay
  Fuse PCB mount: A PCB mount fuse with 200 mil spacing.
  SPDT Switch: SPDT Switch Mini toggle switch
