# Fritzing sketch Section control Rev B (saved by Fritzing 0.9.9b)
circuit board: 20.5001cm x 11.7cm
breadboards: 1

parts:
  S1 = SPDT Switch
  F2 = Fuse PCB mount [package=THT]
  LED1 = LED - 5mm [color="Green (555nm)" current=20m package="5 mm [THT]"]
  D2 = Rectifier Diode [part_number=1N4001 package="300 mil [THT]"]
  R1 = Resistor [tolerance=±5% resistance=560 power=0.25 package=THT]
  D1 = Rectifier Diode [part_number=1N4001 package="300 mil [THT]"]
  F1 = Fuse PCB mount [package=THT]
  R9 = RELAY [package=relay-t9a]
  C1 = Electrolytic Capacitor [capacitance=10µF voltage=20V package="100 mil [THT, electrolytic]"]
  C2 = Electrolytic Capacitor [capacitance=10µF package="100 mil [THT, electrolytic]"]
  RY1 = SPDT relay [part_number=RT package=THT]
  D17 = Rectifier Diode [part_number=1N4001 package="Melf DO-214 AC [SMD]"]
  D18 = Rectifier Diode [part_number=1N4001 package="Melf DO-214 AC [SMD]"]
  J1 = screw terminal, 2 pins
  RY2 = SPDT relay [part_number=RT package=THT]
  LED2 = LED - 5mm [color="Green (555nm)" current=20m package="5 mm [THT]"]
  R2 = Resistor [tolerance=±5% resistance=560 power=0.25 package=THT]
  D3 = Rectifier Diode [part_number=1N4001 package="300 mil [THT]"]
  D4 = Rectifier Diode [part_number=1N4001 package="300 mil [THT]"]
  S2 = SPDT Switch
  F3 = Fuse PCB mount [package=THT]
  F4 = Fuse PCB mount [package=THT]
  J2 = screw terminal, 2 pins
  D19 = Rectifier Diode [part_number=1N4001 package="Melf DO-214 AC [SMD]"]
  RY3 = SPDT relay [part_number=RT package=THT]
  LED3 = LED - 5mm [color="Green (555nm)" current=20m package="5 mm [THT]"]
  R3 = Resistor [tolerance=±5% resistance=560 power=0.25 package=THT]
  D5 = Rectifier Diode [part_number=1N4001 package="300 mil [THT]"]
  D6 = Rectifier Diode [part_number=1N4001 package="300 mil [THT]"]
  S3 = SPDT Switch
  F5 = Fuse PCB mount [package=THT]
  F6 = Fuse PCB mount [package=THT]
  J3 = screw terminal, 2 pins
  RY4 = SPDT relay [part_number=RT package=THT]
  LED4 = LED - 5mm [color="Green (555nm)" current=20m package="5 mm [THT]"]
  R4 = Resistor [tolerance=±5% resistance=560 power=0.25 package=THT]
  D7 = Rectifier Diode [part_number=1N4001 package="300 mil [THT]"]
  D8 = Rectifier Diode [part_number=1N4001 package="300 mil [THT]"]
  S4 = SPDT Switch
  F7 = Fuse PCB mount [package=THT]
  F8 = Fuse PCB mount [package=THT]
  J4 = screw terminal, 2 pins
  RY5 = SPDT relay [part_number=RT package=THT]
  LED5 = LED - 5mm [color="Green (555nm)" current=20m package="5 mm [THT]"]
  R5 = Resistor [tolerance=±5% resistance=560 power=0.25 package=THT]
  D9 = Rectifier Diode [part_number=1N4001 package="300 mil [THT]"]
  D10 = Rectifier Diode [part_number=1N4001 package="300 mil [THT]"]
  S5 = SPDT Switch
  F9 = Fuse PCB mount [package=THT]
  F10 = Fuse PCB mount [package=THT]
  J5 = screw terminal, 2 pins
  RY6 = SPDT relay [part_number=RT package=THT]
  LED6 = LED - 5mm [color="Green (555nm)" current=20m package="5 mm [THT]"]
  R6 = Resistor [tolerance=±5% resistance=560 power=0.25 package=THT]
  D11 = Rectifier Diode [part_number=1N4001 package="300 mil [THT]"]
  D12 = Rectifier Diode [part_number=1N4001 package="300 mil [THT]"]
  S6 = SPDT Switch
  F11 = Fuse PCB mount [package=THT]
  F12 = Fuse PCB mount [package=THT]
  J6 = screw terminal, 2 pins
  RY7 = SPDT relay [part_number=RT package=THT]
  LED7 = LED - 5mm [color="Green (555nm)" current=20m package="5 mm [THT]"]
  R7 = Resistor [tolerance=±5% resistance=560 power=0.25 package=THT]
  D13 = Rectifier Diode [part_number=1N4001 package="300 mil [THT]"]
  D14 = Rectifier Diode [part_number=1N4001 package="300 mil [THT]"]
  S7 = SPDT Switch
  F13 = Fuse PCB mount [package=THT]
  F14 = Fuse PCB mount [package=THT]
  J7 = screw terminal, 2 pins
  RY8 = SPDT relay [part_number=RT package=THT]
  LED8 = LED - 5mm [color="Green (555nm)" current=20m package="5 mm [THT]"]
  R8 = Resistor [tolerance=±5% resistance=560 power=0.25 package=THT]
  D15 = Rectifier Diode [part_number=1N4001 package="300 mil [THT]"]
  D16 = Rectifier Diode [part_number=1N4001 package="300 mil [THT]"]
  S8 = SPDT Switch
  F15 = Fuse PCB mount [package=THT]
  F16 = Fuse PCB mount [package=THT]
  J8 = screw terminal, 2 pins
  D22 = Rectifier Diode [part_number=1N4001 package="Melf DO-214 AC [SMD]"]
  D24 = Rectifier Diode [part_number=1N4001 package="Melf DO-214 AC [SMD]"]
  D26 = Rectifier Diode [part_number=1N4001 package="Melf DO-214 AC [SMD]"]
  D28 = Rectifier Diode [part_number=1N4001 package="Melf DO-214 AC [SMD]"]
  D30 = Rectifier Diode [part_number=1N4001 package="Melf DO-214 AC [SMD]"]
  D32 = Rectifier Diode [part_number=1N4001 package="Melf DO-214 AC [SMD]"]
  D20 = Rectifier Diode [part_number=1N4001 package="Melf DO-214 AC [SMD]"]
  D21 = Rectifier Diode [part_number=1N4001 package="Melf DO-214 AC [SMD]"]
  D23 = Rectifier Diode [part_number=1N4001 package="Melf DO-214 AC [SMD]"]
  D25 = Rectifier Diode [part_number=1N4001 package="Melf DO-214 AC [SMD]"]
  D27 = Rectifier Diode [part_number=1N4001 package="Melf DO-214 AC [SMD]"]
  D29 = Rectifier Diode [part_number=1N4001 package="Melf DO-214 AC [SMD]"]
  D31 = Rectifier Diode [part_number=1N4001 package="Melf DO-214 AC [SMD]"]
  DOGL1 = DOGL128 [part_number="EA DOGL128E-6"]
  R10 = RELAY [package=relay-t9a]
  S10 = SPDT Switch
  D33 = Rectifier Diode [part_number=1N4001 package="300 mil [THT]"]
  F1_2 = female pin header, 2 pins [form="♀ (female)"]
  D34 = Rectifier Diode [part_number=1N4001 package="300 mil [THT]"]
  D35 = Rectifier Diode [part_number=1N4001 package="300 mil [THT]"]
  D36 = Rectifier Diode [part_number=1N4001 package="300 mil [THT]"]
  D37 = Rectifier Diode [part_number=1N4001 package="300 mil [THT]"]
  S9 = SPDT Switch
  U7 = Voltage Regulator - 5V [package="TO220 [THT]"]
  C1_2 = Ceramic Capacitor [capacitance=1µF package="100 mil [THT, multilayer]"]
  C2_2 = Ceramic Capacitor [capacitance=1µF package="100 mil [THT, multilayer]"]
  C3 = Ceramic Capacitor [capacitance=1µF package="100 mil [THT, multilayer]"]
  C4 = Ceramic Capacitor [capacitance=1µF package="100 mil [THT, multilayer]"]
  C5 = Ceramic Capacitor [capacitance=1µF package="100 mil [THT, multilayer]"]
  R13 = Resistor [tolerance=±5% resistance=220 power=0.25 package=THT]
  D38 = Rectifier Diode [part_number=1N4001 package="300 mil [THT]"]
  R14 = Resistor [tolerance=±5% resistance=220 power=0.25 package=THT]
  D39 = Rectifier Diode [part_number=1N4001 package="300 mil [THT]"]
  ULN2803 = IC, DIP package, 18 pins [chip_label=IC]
  U8 = ESP32-38PinWide [part_number=ESP32-38PinWide]
  ‎TB67H410 = Motor driver [part_number=TB67H410 package=THT]
  R15 = Resistor [tolerance=±5% resistance=220 package="2512 [SMD]"]
  D40 = Rectifier Diode [part_number=1N4001 package="Melf DO-214 AC [SMD]"]
  D41 = Rectifier Diode [part_number=1N4001 package="Melf DO-214 AC [SMD]"]
  F1_3 = female pin header, 2 pins [form="♀ (female)"]
  R17 = Resistor [tolerance=±5% power=0.25 resistance=220 package=THT]
  R18 = Resistor [tolerance=±5% power=0.25 resistance=220 package=THT]
  R19 = Resistor [tolerance=±5% power=0.25 resistance=1k package=THT]
  R20 = Resistor [tolerance=±5% power=0.25 resistance=1k package=THT]
  R21 = Resistor [tolerance=±5% power=0.25 resistance=1k package=THT]
  RA1 = mystery part, 9 pins [chip_label=?]
  D42 = Rectifier Diode [part_number=1N4001 package="300 mil [THT]"]
  F17 = Resettable Fuse PTC [package=ptc]
  R22 = Resistor [tolerance=±5% power=0.25 resistance=1k package=THT]
  R16 = Resistor [tolerance=±5% power=0.25 resistance=6.8k package=THT]
  C10 = Ceramic Capacitor [capacitance=27pF voltage=35V package="100 mil [THT, multilayer]"]
  C6 = Electrolytic Capacitor [capacitance=0.1mF voltage=35V package="100 mil [THT, electrolytic]"]
  C7 = Ceramic Capacitor [capacitance=100nF voltage=35V package="100 mil [THT, multilayer]"]
  C8 = Ceramic Capacitor [capacitance=100nF voltage=35V package="100 mil [THT, multilayer]"]
  C9 = Ceramic Capacitor [capacitance=100nF voltage=35V package="100 mil [THT, multilayer]"]
  R10_2 = Resistor [tolerance=±5% power=0.25 resistance=47 package=THT]
  R11 = Resistor [tolerance=±5% power=0.25 resistance=47 package=THT]
  R12 = Resistor [tolerance=±5% power=0.25 resistance=47 package=THT]
  J0 = Resistor [tolerance=±5% power=0.25 resistance=47 package=THT]
  J9 = Screw terminal - 2 pins [package=THT]
  J10 = screw terminal, 3 pins
  U9 = mystery part, 16 pins [chip_label=?]

nets:
  N1: S1.O, F1.pin1, RY1.1NC
  N2: S1.P, D18.cathode
  N3: S1.S, F2.pin1, RY1.1NO
  N4: F2.pin2, LED1.anode, D2.cathode, J1.pin2, U9.pin1
  N5: LED1.cathode, R1.Pin_1
  GND: D2.anode, R1.Pin_0, D1.anode, R9.COIL2, C1.-, C2.-, R2.Pin_0, D3.anode, D4.anode, R3.Pin_0, D5.anode, D6.anode, R4.Pin_0, D7.anode, D8.anode, R5.Pin_0, D9.anode, D10.anode, R6.Pin_0, D11.anode, D12.anode, R7.Pin_0, D13.anode, D14.anode, R8.Pin_0, D15.anode, D16.anode, DOGL1.VSS, R10.COIL2, D36.anode, D37.anode, S9.P, U7.GND, C1_2.1, C2_2.1, C3.1, C4.1, C5.1, D38.anode, D39.anode, ULN2803.pin9, U8.GND, ‎TB67H410.GND, ‎TB67H410.PWMB, ‎TB67H410.INB1, ‎TB67H410.INB2, R19.Pin_1, R20.Pin_1, R21.Pin_1, RA1.pin1, C10.0, C6.-, C7.0, C8.0, C9.0, J0.Pin_0, J10.pin1
  N6: D1.cathode, F1.pin2, J1.pin1
  N7: R9.COIL1, S10.O, D35.anode, D36.cathode
  N8: R9.MAIN, R10.MAIN, F1_2.pin2
  N9: R9.NO, D17.anode, D19.anode, D21.anode, D23.anode, D25.anode, D27.anode, D29.anode, D31.anode, ULN2803.pin10, D40.anode
  N10: C1.+, D34.cathode, D35.cathode, U7.input_voltage, R13.Pin_0, F17.2
  VIN: C2.+, U7.output_voltage, U8.VIN, ‎TB67H410.VCC, ‎TB67H410.HBMODE, ‎TB67H410.TBLKAB, R16.Pin_0, C9.1, R10_2.Pin_0, R11.Pin_0, R12.Pin_0
  N11: RY1.A1, ULN2803.pin11
  N12: RY1.1COM, RY1.A2, D17.cathode
  N13: D18.anode, D22.anode, D24.anode, D26.anode, D28.anode, D30.anode, D32.anode, D20.anode, R10.NO, D41.anode
  N14: RY2.A1, ULN2803.pin12
  N15: RY2.1NC, S2.O, F3.pin1
  N16: RY2.1COM, RY2.A2, D19.cathode
  N17: RY2.1NO, S2.S, F4.pin1
  N18: LED2.cathode, R2.Pin_1
  N19: LED2.anode, D4.cathode, F4.pin2, J2.pin2, U9.pin2
  N20: D3.cathode, F3.pin2, J2.pin1
  N21: S2.P, D20.cathode
  N22: RY3.A1, ULN2803.pin13
  N23: RY3.1NC, S3.O, F5.pin1
  N24: RY3.1COM, RY3.A2, D21.cathode
  N25: RY3.1NO, S3.S, F6.pin1
  N26: LED3.cathode, R3.Pin_1
  N27: LED3.anode, D6.cathode, F6.pin2, J3.pin2, U9.pin3
  N28: D5.cathode, F5.pin2, J3.pin1
  N29: S3.P, D22.cathode
  N30: RY4.A1, ULN2803.pin14
  N31: RY4.1NC, S4.O, F7.pin1
  N32: RY4.1COM, RY4.A2, D23.cathode
  N33: RY4.1NO, S4.S, F8.pin1
  N34: LED4.cathode, R4.Pin_1
  N35: LED4.anode, D8.cathode, F8.pin2, J4.pin2, U9.pin4
  N36: D7.cathode, F7.pin2, J4.pin1
  N37: S4.P, D24.cathode
  N38: RY5.A1, ULN2803.pin15
  N39: RY5.1NC, S5.O, F9.pin1
  N40: RY5.1COM, RY5.A2, D25.cathode
  N41: RY5.1NO, S5.S, F10.pin1
  N42: LED5.cathode, R5.Pin_1
  N43: LED5.anode, D10.cathode, F10.pin2, J5.pin2, U9.pin5
  N44: D9.cathode, F9.pin2, J5.pin1
  N45: S5.P, D26.cathode
  N46: RY6.A1, ULN2803.pin16
  N47: RY6.1NC, S6.O, F11.pin1
  N48: RY6.1COM, RY6.A2, D27.cathode
  N49: RY6.1NO, S6.S, F12.pin1
  N50: LED6.cathode, R6.Pin_1
  N51: LED6.anode, D12.cathode, F12.pin2, J6.pin2, U9.pin6
  N52: D11.cathode, F11.pin2, J6.pin1
  N53: S6.P, D28.cathode
  N54: RY7.A1, ULN2803.pin17
  N55: RY7.1NC, S7.O, F13.pin1
  N56: RY7.1COM, RY7.A2, D29.cathode
  N57: RY7.1NO, S7.S, F14.pin1
  N58: LED7.cathode, R7.Pin_1
  N59: LED7.anode, D14.cathode, F14.pin2, J7.pin2, U9.pin7
  N60: D13.cathode, F13.pin2, J7.pin1
  N61: S7.P, D30.cathode
  N62: RY8.A1, ULN2803.pin18
  N63: RY8.1NC, S8.O, F15.pin1
  N64: RY8.1COM, RY8.A2, D31.cathode
  N65: RY8.1NO, S8.S, F16.pin1
  N66: LED8.cathode, R8.Pin_1
  N67: LED8.anode, D16.cathode, F16.pin2, J8.pin2, U9.pin8
  N68: D15.cathode, F15.pin2, J8.pin1
  N69: S8.P, D32.cathode
  N70: DOGL1.A1, R12.Pin_1
  N71: DOGL1.A2, R11.Pin_1
  N72: DOGL1.A3, R10_2.Pin_1
  N73: DOGL1.C1, DOGL1.C2, DOGL1.C3, J0.Pin_1
  N74: DOGL1.V0, C1_2.0
  N75: DOGL1.V1, C2_2.0
  N76: DOGL1.V2, C3.0
  N77: DOGL1.V3, C4.0
  N78: DOGL1.V4, C5.0
  N79: DOGL1.VOUT, R13.Pin_1, D38.cathode
  N80: DOGL1.VDD2, DOGL1.VDD, U8.3.3, ‎TB67H410.VREF, R17.Pin_0, R18.Pin_0, R22.Pin_0, C8.1
  N81: DOGL1.SI, U8.GPIO23
  N82: DOGL1.SCL, U8.GPIO18
  N83: DOGL1.A0, U8.GPIO5
  N84: DOGL1.RST, U8.GPIO4
  N85: DOGL1.CS1B, U8.GPIO2
  N86: R10.COIL1, S10.S, D34.anode, D37.cathode, R14.Pin_0
  N87: S10.P, D33.cathode
  N88: D33.anode, F1_2.pin1
  N89: S9.O, U8.GPIO21, R17.Pin_1
  N90: S9.S, U8.GPIO19, R18.Pin_1
  N91: R14.Pin_1, D39.cathode, U8.GPIO36
  N92: ULN2803.pin1, U8.GPIO13, RA1.pin9, U9.pin9
  N93: ULN2803.pin2, U8.GPIO12, RA1.pin8, U9.pin10
  N94: ULN2803.pin3, U8.GPIO14, RA1.pin7, U9.pin11
  N95: ULN2803.pin4, U8.GPIO27, RA1.pin6, U9.pin12
  N96: ULN2803.pin5, U8.GPIO26, RA1.pin5, U9.pin13
  N97: ULN2803.pin6, U8.GPIO25, RA1.pin4, U9.pin14
  N98: ULN2803.pin7, U8.GPIO33, RA1.pin3, U9.pin15
  N99: ULN2803.pin8, U8.GPIO32, RA1.pin2, U9.pin16
  N100: U8.GPIO15, ‎TB67H410.PWMA, R21.Pin_0
  N101: U8.GPIO16, ‎TB67H410.INA2, R20.Pin_0
  N102: U8.GPIO17, ‎TB67H410.INA1, R19.Pin_0
  N103: U8.GPIO22, D42.anode, R22.Pin_1
  N104: ‎TB67H410.OUTB-, ‎TB67H410.OUTB+, J9.pin1
  N105: ‎TB67H410.RSB, ‎TB67H410.RSA, R15.Pin_1
  N106: ‎TB67H410.VM, R15.Pin_0, F1_3.pin1, C6.+, C7.1
  N107: ‎TB67H410.OSCM, R16.Pin_1, C10.1
  N108: ‎TB67H410.OUTA+, ‎TB67H410.OUTA-, J9.pin2
  N109: D40.cathode, D41.cathode, F1_3.pin2
  N110: D42.cathode, J10.pin2
  N111: F17.1, J10.pin3

notes:
  Rev B
  Copyright Silicon Reparation 2022
  License GPLv3 PCB design
  +
  -

custom parts:
  SPDT Switch: SPDT Switch Mini toggle switch
  Fuse PCB mount: A PCB mount fuse with 200 mil spacing.
  RELAY: SPST 30A relay
  SPDT relay: A SPDT 8A relay
  Rectifier Diode: A DO-214AB smd rectifier diode
  DOGL128: A graphic display with an LED backlight
  Voltage Regulator - 5V: 5V DC Voltage Regulator
  ESP32-38PinWide: Generic 38-Pin ESP32 with wide format made by Espressif. This part uses SVG elements from various sources on the web, thanks to all.
  Motor driver: A quad half bridge driver capable of driving single or dual DC motors bidirectionally. With 24 pins on a 300mil inline pin header footprint. It can drive up to two 2.5A motors or one 5A motor.
