# Fritzing sketch Section control Rev C (saved by Fritzing 0.9.9b)
circuit board: 20.5001cm x 11.7cm
breadboards: 1

parts:
  S1 = SPDT Switch
  F2 = Fuse PCB mount [package=THT]
  LED1 = LED - 5mm [color="Green (555nm)" current=20m package="5 mm [THT]"]
  D2 = Rectifier Diode [part_number=1N4001 package="300 mil [THT]"]
  R1 = Resistor [tolerance=±5% resistance=1k power=0.25 package=THT]
  D1 = Rectifier Diode [part_number=1N4001 package="300 mil [THT]"]
  F1 = Fuse PCB mount [package=THT]
  R9 = RELAY [package=relay-t9a]
  C1 = Electrolytic Capacitor [capacitance=10µF voltage=20V package="100 mil [THT, electrolytic]"]
  C2 = Electrolytic Capacitor [capacitance=10µF voltage=35V package="100 mil [THT, electrolytic]"]
  RY1 = SPDT relay [part_number=RT package=THT]
  D17 = Rectifier Diode [part_number=1N4001 package="Melf DO-214 AC [SMD]"]
  D18 = Rectifier Diode [part_number=1N4001 package="Melf DO-214 AC [SMD]"]
  J1 = screw terminal, 2 pins
  RY2 = SPDT relay [part_number=RT package=THT]
  LED2 = LED - 5mm [color="Green (555nm)" current=20m package="5 mm [THT]"]
  R2 = Resistor [tolerance=±5% resistance=1k power=0.25 package=THT]
  D3 = Rectifier Diode [part_number=1N4001 package="300 mil [THT]"]
  D4 = Rectifier Diode [part_number=1N4001 package="300 mil [THT]"]
  S2 = SPDT Switch
  F3 = Fuse PCB mount [package=THT]
  F4 = Fuse PCB mount [package=THT]
  J2 = screw terminal, 2 pins
  D19 = Rectifier Diode [part_number=1N4001 package="Melf DO-214 AC [SMD]"]
  RY3 = SPDT relay [part_number=RT package=THT]
  LED3 = LED - 5mm [color="Green (555nm)" current=20m package="5 mm [THT]"]
  R3 = Resistor [tolerance=±5% resistance=1k power=0.25 package=THT]
  D5 = Rectifier Diode [part_number=1N4001 package="300 mil [THT]"]
  D6 = Rectifier Diode [part_number=1N4001 package="300 mil [THT]"]
  S3 = SPDT Switch
  F5 = Fuse PCB mount [package=THT]
  F6 = Fuse PCB mount [package=THT]
  J3 = screw terminal, 2 pins
  RY4 = SPDT relay [part_number=RT package=THT]
  LED4 = LED - 5mm [color="Green (555nm)" current=20m package="5 mm [THT]"]
  R4 = Resistor [tolerance=±5% resistance=1k power=0.25 package=THT]
  D7 = Rectifier Diode [part_number=1N4001 package="300 mil [THT]"]
  D8 = Rectifier Diode [part_number=1N4001 package="300 mil [THT]"]
  S4 = SPDT Switch
  F7 = Fuse PCB mount [package=THT]
  F8 = Fuse PCB mount [package=THT]
  J4 = screw terminal, 2 pins
  RY5 = SPDT relay [part_number=RT package=THT]
  LED5 = LED - 5mm [color="Green (555nm)" current=20m package="5 mm [THT]"]
  R5 = Resistor [tolerance=±5% resistance=1k power=0.25 package=THT]
  D9 = Rectifier Diode [part_number=1N4001 package="300 mil [THT]"]
  D10 = Rectifier Diode [part_number=1N4001 package="300 mil [THT]"]
  S5 = SPDT Switch
  F9 = Fuse PCB mount [package=THT]
  F10 = Fuse PCB mount [package=THT]
  J5 = screw terminal, 2 pins
  RY6 = SPDT relay [part_number=RT package=THT]
  LED6 = LED - 5mm [color="Green (555nm)" current=20m package="5 mm [THT]"]
  R6 = Resistor [tolerance=±5% resistance=1k power=0.25 package=THT]
  D11 = Rectifier Diode [part_number=1N4001 package="300 mil [THT]"]
  D12 = Rectifier Diode [part_number=1N4001 package="300 mil [THT]"]
  S6 = SPDT Switch
  F11 = Fuse PCB mount [package=THT]
  F12 = Fuse PCB mount [package=THT]
  J6 = screw terminal, 2 pins
  RY7 = SPDT relay [part_number=RT package=THT]
  LED7 = LED - 5mm [color="Green (555nm)" current=20m package="5 mm [THT]"]
  R7 = Resistor [tolerance=±5% resistance=1k power=0.25 package=THT]
  D13 = Rectifier Diode [part_number=1N4001 package="300 mil [THT]"]
  D14 = Rectifier Diode [part_number=1N4001 package="300 mil [THT]"]
  S7 = SPDT Switch
  F13 = Fuse PCB mount [package=THT]
  F14 = Fuse PCB mount [package=THT]
  J7 = screw terminal, 2 pins
  RY8 = SPDT relay [part_number=RT package=THT]
  LED8 = LED - 5mm [color="Green (555nm)" current=20m package="5 mm [THT]"]
  R8 = Resistor [tolerance=±5% resistance=1k power=0.25 package=THT]
  D15 = Rectifier Diode [part_number=1N4001 package="300 mil [THT]"]
  D16 = Rectifier Diode [part_number=1N4001 package="300 mil [THT]"]
  S8 = SPDT Switch
  F15 = Fuse PCB mount [package=THT]
  F16 = Fuse PCB mount [package=THT]
  J8 = screw terminal, 2 pins
  D22 = Rectifier Diode [part_number=1N4001 package="Melf DO-214 AC [SMD]"]
  D24 = Rectifier Diode [part_number=1N4001 package="Melf DO-214 AC [SMD]"]
  D26 = Rectifier Diode [part_number=1N4001 package="Melf DO-214 AC [SMD]"]
  D28 = Rectifier Diode [part_number=1N4001 package="Melf DO-214 AC [SMD]"]
  D30 = Rectifier Diode [part_number=1N4001 package="Melf DO-214 AC [SMD]"]
  D32 = Rectifier Diode [part_number=1N4001 package="Melf DO-214 AC [SMD]"]
  D20 = Rectifier Diode [part_number=1N4001 package="Melf DO-214 AC [SMD]"]
  D21 = Rectifier Diode [part_number=1N4001 package="Melf DO-214 AC [SMD]"]
  D23 = Rectifier Diode [part_number=1N4001 package="Melf DO-214 AC [SMD]"]
  D25 = Rectifier Diode [part_number=1N4001 package="Melf DO-214 AC [SMD]"]
  D27 = Rectifier Diode [part_number=1N4001 package="Melf DO-214 AC [SMD]"]
  D29 = Rectifier Diode [part_number=1N4001 package="Melf DO-214 AC [SMD]"]
  D31 = Rectifier Diode [part_number=1N4001 package="Melf DO-214 AC [SMD]"]
  R10 = RELAY [package=relay-t9a]
  S10 = SPDT Switch
  F1_2 = female pin header, 2 pins [form="♀ (female)"]
  D34 = Rectifier Diode [part_number=1N4001 package="300 mil [THT]"]
  D35 = Rectifier Diode [part_number=1N4001 package="300 mil [THT]"]
  D37 = Rectifier Diode [part_number=1N4001 package="300 mil [THT]"]
  D36 = Rectifier Diode [part_number=1N4001 package="300 mil [THT]"]
  S9 = SPDT Switch
  U7 = Voltage Regulator - 5V [package="TO220 [THT]"]
  C1_2 = Ceramic Capacitor [capacitance=1µF package="100 mil [THT, multilayer]"]
  C2_2 = Ceramic Capacitor [capacitance=1µF package="100 mil [THT, multilayer]"]
  C3 = Ceramic Capacitor [capacitance=1µF package="100 mil [THT, multilayer]"]
  C4 = Ceramic Capacitor [capacitance=1µF package="100 mil [THT, multilayer]"]
  C5 = Ceramic Capacitor [capacitance=1µF package="100 mil [THT, multilayer]"]
  R13 = Resistor [tolerance=±5% resistance=220 power=0.5W package=THT]
  D50 = Rectifier Diode [part_number=1N4001 package="300 mil [THT]"]
  U8 = ESP32-38PinWide [part_number=ESP32-38PinWide]
  ‎TB67H410 = Motor driver [part_number=TB67H410 package=THT]
  R15 = Resistor [tolerance=±5% resistance=220 package="2512 [SMD]"]
  D40 = Rectifier Diode [part_number=1N4001 package="Melf DO-214 AC [SMD]"]
  D41 = Rectifier Diode [part_number=1N4001 package="Melf DO-214 AC [SMD]"]
  F1_3 = female pin header, 2 pins [form="♀ (female)"]
  R30 = Resistor [tolerance=±5% power=0.25 resistance=10k package=THT]
  R31 = Resistor [tolerance=±5% power=0.25 resistance=10k package=THT]
  R9_2 = Resistor [tolerance=±5% power=0.25 resistance=1k package=THT]
  R10_2 = Resistor [tolerance=±5% power=0.25 resistance=1k package=THT]
  R11 = Resistor [tolerance=±5% power=0.25 resistance=1k package=THT]
  D38 = Rectifier Diode [part_number=1N4001 package="300 mil [THT]"]
  F17 = Resettable Fuse PTC [package=ptc]
  R12 = Resistor [tolerance=±5% power=0.25 resistance=1k package=THT]
  R16 = Resistor [tolerance=±5% power=0.25 resistance=6.8k package=THT]
  C10 = Ceramic Capacitor [capacitance=27pF voltage=35V package="100 mil [THT, multilayer]"]
  C6 = Electrolytic Capacitor [capacitance=0.1mF voltage=35V package="100 mil [THT, electrolytic]"]
  C8 = Ceramic Capacitor [capacitance=100nF voltage=35V package="100 mil [THT, multilayer]"]
  R27 = Resistor [tolerance=±5% power=0.25 resistance=47 package=THT]
  R26 = Resistor [tolerance=±5% power=0.25 resistance=47 package=THT]
  R25 = Resistor [tolerance=±5% power=0.25 resistance=47 package=THT]
  J0 = Resistor [tolerance=±5% power=0.25 resistance=47 package=THT]
  J5_2 = Screw terminal - 2 pins [package=THT]
  12V_Sig_GND = screw terminal, 3 pins
  Wifi = LED - 5mm [color="Blue (505nm)" current=0.030 package="5 mm [THT]"]
  R24 = Resistor [tolerance=±5% power=0.25 resistance=4.7k package=THT]
  - = mystery part, 9 pins [chip_label=?]
  IC3 = SO16 [chip_label=IC package=SO]
  MCP23017 = MCP23017 [package=THT]
  C11 = Ceramic Capacitor [capacitance=100nF voltage=35V package="100 mil [THT, multilayer]"]
  ADS1115 = Adafruit ADS1115 16Bit I2C ADC [part_number="Adafruit #1085"]
  12V_A0_A1_GND = screw terminal, 4 pins
  C12 = Ceramic Capacitor [capacitance=100nF voltage=35V package="100 mil [THT, multilayer]"]
  C13 = Ceramic Capacitor [capacitance=100nF voltage=35V package="100 mil [THT, multilayer]"]
  C14 = Ceramic Capacitor [capacitance=100nF voltage=35V package="100 mil [THT, multilayer]"]
  R15_2 = Resistor [tolerance=±5% power=0.25 resistance=1.5k package=THT]
  R16_2 = Resistor [tolerance=±5% power=0.25 resistance=1.5k package=THT]
  J1_2 = Screw terminal - 3 pins [package=THT]
  D33 = Rectifier Diode [part_number=1N4001 package="300 mil [THT]"]
  CNY17 = mystery part, 6 pins [chip_label=?]
  R32 = Resistor [tolerance=±5% power=0.25 resistance=10k package=THT]
  TBD62084 = SOIC - 18 pins [part_number=TBD62084 package=SOIC-18]
  IC5 = SO18W [chip_label=IC package=SO(w)]
  DOGL1 = DOGL128 [part_number="EA DOGL128E-6"]
  1_2_3_4_5_6 = female pin header, 6 pins [form="♀ (female)"]
  D42 = Rectifier Diode [part_number=1N4001 package="300 mil [THT]"]
  J2_2 = screw terminal, 3 pins

nets:
  N1: S1.O, F1.pin1, RY1.1NC
  N2: S1.P, D18.cathode
  N3: S1.S, F2.pin1, RY1.1NO
  N4: F2.pin2, LED1.anode, D2.cathode, J1.pin2, IC3.9
  N5: LED1.cathode, R1.Pin_1
  GND: D2.anode, R1.Pin_0, D1.anode, R9.COIL2, C1.-, C2.-, R2.Pin_0, D3.anode, D4.anode, R3.Pin_0, D5.anode, D6.anode, R4.Pin_0, D7.anode, D8.anode, R5.Pin_0, D9.anode, D10.anode, R6.Pin_0, D11.anode, D12.anode, R7.Pin_0, D13.anode, D14.anode, R8.Pin_0, D15.anode, D16.anode, R10.COIL2, D37.anode, D36.anode, S9.P, U7.GND, C1_2.1, C2_2.1, C3.1, C4.1, C5.1, D50.anode, U8.GND, ‎TB67H410.GND, ‎TB67H410.PWMB, ‎TB67H410.INB1, ‎TB67H410.INB2, R9_2.Pin_1, R10_2.Pin_1, R11.Pin_1, C10.0, C6.-, C8.0, J0.Pin_0, 12V_Sig_GND.pin1, Wifi.cathode, -.pin1, MCP23017.V-, MCP23017.A0, MCP23017.A1, MCP23017.A2, C11.0, ADS1115.GND, 12V_A0_A1_GND.pin4, C12.1, C13.0, C14.1, R15_2.Pin_1, R16_2.Pin_1, CNY17.pin2, CNY17.pin4, TBD62084.GND, IC5.9, DOGL1.VSS, 1_2_3_4_5_6.pin1, 1_2_3_4_5_6.pin2, J2_2.pin1, J2_2.pin2
  N6: D1.cathode, F1.pin2, J1.pin1
  N7: R9.COIL1, D37.cathode
  N8: R9.MAIN, R10.MAIN, J1_2.pin1, J1_2.pin2, J1_2.pin3
  N9: R9.NO, D17.anode, D19.anode, D21.anode, D23.anode, D25.anode, D27.anode, D29.anode, D31.anode, D40.anode, TBD62084.VCC, IC5.10
  N10: C1.+, D34.cathode, D35.cathode, U7.input_voltage, R13.Pin_0, F17.2, D42.anode
  VIN: C2.+, U7.output_voltage, U8.VIN, ‎TB67H410.VCC, ‎TB67H410.HBMODE, ‎TB67H410.TBLKAB, R16.Pin_0, C8.1, R27.Pin_0, R26.Pin_0, R25.Pin_0, MCP23017.V+, C11.1, ADS1115.VDD, 1_2_3_4_5_6.pin6
  N11: RY1.A1, TBD62084.OUT1, IC5.18
  N12: RY1.1COM, RY1.A2, D17.cathode
  N13: D18.anode, D22.anode, D24.anode, D26.anode, D28.anode, D30.anode, D32.anode, D20.anode, R10.NO, D41.anode
  N14: RY2.A1, TBD62084.OUT2, IC5.17
  N15: RY2.1NC, S2.O, F3.pin1
  N16: RY2.1COM, RY2.A2, D19.cathode
  N17: RY2.1NO, S2.S, F4.pin1
  N18: LED2.cathode, R2.Pin_1
  N19: LED2.anode, D4.cathode, F4.pin2, J2.pin2, IC3.10
  N20: D3.cathode, F3.pin2, J2.pin1
  N21: S2.P, D20.cathode
  N22: RY3.A1, TBD62084.OUT3, IC5.16
  N23: RY3.1NC, S3.O, F5.pin1
  N24: RY3.1COM, RY3.A2, D21.cathode
  N25: RY3.1NO, S3.S, F6.pin1
  N26: LED3.cathode, R3.Pin_1
  N27: LED3.anode, D6.cathode, F6.pin2, J3.pin2, IC3.11
  N28: D5.cathode, F5.pin2, J3.pin1
  N29: S3.P, D22.cathode
  N30: RY4.A1, TBD62084.OUT4, IC5.15
  N31: RY4.1NC, S4.O, F7.pin1
  N32: RY4.1COM, RY4.A2, D23.cathode
  N33: RY4.1NO, S4.S, F8.pin1
  N34: LED4.cathode, R4.Pin_1
  N35: LED4.anode, D8.cathode, F8.pin2, J4.pin2, IC3.12
  N36: D7.cathode, F7.pin2, J4.pin1
  N37: S4.P, D24.cathode
  N38: RY5.A1, TBD62084.OUT5, IC5.14
  N39: RY5.1NC, S5.O, F9.pin1
  N40: RY5.1COM, RY5.A2, D25.cathode
  N41: RY5.1NO, S5.S, F10.pin1
  N42: LED5.cathode, R5.Pin_1
  N43: LED5.anode, D10.cathode, F10.pin2, J5.pin2, IC3.13
  N44: D9.cathode, F9.pin2, J5.pin1
  N45: S5.P, D26.cathode
  N46: RY6.A1, TBD62084.OUT6, IC5.13
  N47: RY6.1NC, S6.O, F11.pin1
  N48: RY6.1COM, RY6.A2, D27.cathode
  N49: RY6.1NO, S6.S, F12.pin1
  N50: LED6.cathode, R6.Pin_1
  N51: LED6.anode, D12.cathode, F12.pin2, J6.pin2, IC3.14
  N52: D11.cathode, F11.pin2, J6.pin1
  N53: S6.P, D28.cathode
  N54: RY7.A1, TBD62084.OUT7, IC5.12
  N55: RY7.1NC, S7.O, F13.pin1
  N56: RY7.1COM, RY7.A2, D29.cathode
  N57: RY7.1NO, S7.S, F14.pin1
  N58: LED7.cathode, R7.Pin_1
  N59: LED7.anode, D14.cathode, F14.pin2, J7.pin2, IC3.15
  N60: D13.cathode, F13.pin2, J7.pin1
  N61: S7.P, D30.cathode
  N62: RY8.A1, TBD62084.OUT8, IC5.11
  N63: RY8.1NC, S8.O, F15.pin1
  N64: RY8.1COM, RY8.A2, D31.cathode
  N65: RY8.1NO, S8.S, F16.pin1
  N66: LED8.cathode, R8.Pin_1
  N67: LED8.anode, D16.cathode, F16.pin2, J8.pin2, IC3.16
  N68: D15.cathode, F15.pin2, J8.pin1
  N69: S8.P, D32.cathode
  N70: R10.COIL1, S10.S, D34.anode, D36.cathode, CNY17.pin1
  N71: S10.O, D35.anode
  N72: S10.P, D33.cathode
  N73: F1_2.pin1, D33.anode
  N74: F1_2.pin2, J2_2.pin3
  N75: S9.O, U8.GPIO33, R30.Pin_1
  N76: S9.S, U8.GPIO32, R31.Pin_1
  N77: C1_2.0, DOGL1.V0
  N78: C2_2.0, DOGL1.V1
  N79: C3.0, DOGL1.V2
  N80: C4.0, DOGL1.V3
  N81: C5.0, DOGL1.V4
  N82: R13.Pin_1, D50.cathode, DOGL1.VOUT
  N83: U8.3.3, ‎TB67H410.VREF, R30.Pin_0, R31.Pin_0, R12.Pin_0, DOGL1.VDD2, DOGL1.VDD
  N84: U8.GPIO36, CNY17.pin5
  N85: U8.GPIO39, R32.Pin_1
  N86: U8.GPIO25, 1_2_3_4_5_6.pin3
  N87: U8.GPIO26, 1_2_3_4_5_6.pin4
  N88: U8.GPIO27, 1_2_3_4_5_6.pin5
  N89: U8.GPIO13, R24.Pin_0
  N90: U8.GPIO15, ‎TB67H410.PWMA, R11.Pin_0
  N91: U8.GPIO2, DOGL1.CS1B
  N92: U8.GPIO4, DOGL1.RST
  N93: U8.GPIO16, ‎TB67H410.INA2, R10_2.Pin_0
  N94: U8.GPIO17, ‎TB67H410.INA1, R9_2.Pin_0
  N95: U8.GPIO5, DOGL1.A0
  N96: U8.GPIO18, DOGL1.SCL
  N97: U8.GPIO21, MCP23017.SDA, ADS1115.SDA, R16_2.Pin_0
  N98: U8.GPIO22, MCP23017.SCL, ADS1115.SCL, R15_2.Pin_0
  N99: U8.GPIO23, DOGL1.SI
  N100: ‎TB67H410.OUTB-, ‎TB67H410.OUTB+, J5_2.pin1
  N101: ‎TB67H410.RSB, ‎TB67H410.RSA, R15.Pin_1
  N102: ‎TB67H410.VM, R15.Pin_0, F1_3.pin1, C6.+
  N103: ‎TB67H410.OSCM, R16.Pin_1, C10.1
  N104: ‎TB67H410.OUTA+, ‎TB67H410.OUTA-, J5_2.pin2
  N105: D40.cathode, D41.cathode, F1_3.pin2
  N106: D38.cathode, 12V_Sig_GND.pin2
  N107: D38.anode, R12.Pin_1, R32.Pin_0
  N108: F17.1, 12V_Sig_GND.pin3
  N109: R27.Pin_1, DOGL1.A3
  N110: R26.Pin_1, DOGL1.A2
  N111: R25.Pin_1, DOGL1.A1
  N112: J0.Pin_1, DOGL1.C1, DOGL1.C2, DOGL1.C3
  N113: Wifi.anode, R24.Pin_1
  N114: -.pin2, IC3.1, MCP23017.MCP_D15
  N115: -.pin3, IC3.2, MCP23017.MCP_D14
  N116: -.pin4, IC3.3, MCP23017.MCP_D13
  N117: -.pin5, IC3.4, MCP23017.MCP_D12
  N118: -.pin6, IC3.5, MCP23017.MCP_D11
  N119: -.pin7, IC3.6, MCP23017.MCP_D10
  N120: -.pin8, IC3.7, MCP23017.MCP_D9
  N121: -.pin9, IC3.8, MCP23017.MCP_D8
  N122: MCP23017.MCP_D0, TBD62084.IN1, IC5.1
  N123: MCP23017.MCP_D1, TBD62084.IN2, IC5.2
  N124: MCP23017.MCP_D2, TBD62084.IN3, IC5.3
  N125: MCP23017.MCP_D3, TBD62084.IN4, IC5.4
  N126: MCP23017.MCP_D4, TBD62084.IN5, IC5.5
  N127: MCP23017.MCP_D5, TBD62084.IN6, IC5.6
  N128: MCP23017.MCP_D6, TBD62084.IN7, IC5.7
  N129: MCP23017.MCP_D7, TBD62084.IN8, IC5.8
  N130: ADS1115.AIN1, 12V_A0_A1_GND.pin3, C13.1
  N131: ADS1115.AIN0, 12V_A0_A1_GND.pin2, C12.0
  N132: 12V_A0_A1_GND.pin1, C14.0, D42.cathode

notes:
  Rev C
  Copyright Reuben Rissler 2023
  License GPLv3 PCB design
  +
  - - +
  NONC

custom parts:
  SPDT Switch: SPDT Switch Mini toggle switch
  Fuse PCB mount: A PCB mount fuse with 200 mil spacing.
  RELAY: SPST 30A relay
  SPDT relay: A SPDT 8A relay
  Rectifier Diode: A DO-214AB smd rectifier diode
  Voltage Regulator - 5V: 5V DC Voltage Regulator
  ESP32-38PinWide: Generic 38-Pin ESP32 with wide format made by Espressif. This part uses SVG elements from various sources on the web, thanks to all.
  Motor driver: A quad half bridge driver capable of driving single or dual DC motors bidirectionally. With 24 pins on a 300mil inline pin header footprint. It can drive up to two 2.5A motors or one 5A motor.
  MCP23017: A 16 bit I2C port expander.
  Adafruit ADS1115 16Bit I2C ADC: For microcontrollers without an analog-to-digital converter or when you want a higher-precision ADC, the ADS1115 provides 16-bit precision at 860 samples/second over I2C. The chip can be configured as 4 single-ended input channels, or two differential channels. As a nice bonus, it even includes a programmable gain amplifier, up to x16, to help boost up smaller single/differential signals to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
  Screw terminal - 3 pins: Wire clamp terminal with 3 pins
  SOIC - 18 pins: 8 channel transistor array
  DOGL128: A graphic display with an LED backlight
