# Fritzing sketch Section control Rev E (saved by Fritzing 0.9.9b)
circuit board: 20.5001cm x 11.7cm
breadboards: 1

parts:
  S1 = SPDT Switch
  F2 = Fuse PCB mount [package=THT]
  LED1 = LED - 5mm [color="Green (555nm)" current=20m package="5 mm [THT]"]
  D2 = Rectifier Diode [part_number=1N4001 package="300 mil [THT]"]
  R1 = Resistor [tolerance=±5% resistance=1k power=0.25 package=THT]
  D1 = Rectifier Diode [part_number=1N4001 package="300 mil [THT]"]
  F1 = Fuse PCB mount [package=THT]
  RY9 = RELAY [package=relay-t9a]
  C1 = Electrolytic Capacitor [capacitance=10µF voltage=20V package="100 mil [THT, electrolytic]"]
  C2 = Electrolytic Capacitor [capacitance=10µF voltage=35V package="100 mil [THT, electrolytic]"]
  D17 = Rectifier Diode [part_number=1N4001 package="Melf DO-214 AC [SMD]"]
  D18 = Rectifier Diode [part_number=1N4001 package="Melf DO-214 AC [SMD]"]
  J1 = screw terminal, 2 pins
  LED2 = LED - 5mm [color="Green (555nm)" current=20m package="5 mm [THT]"]
  R2 = Resistor [tolerance=±5% resistance=1k power=0.25 package=THT]
  D3 = Rectifier Diode [part_number=1N4001 package="300 mil [THT]"]
  D4 = Rectifier Diode [part_number=1N4001 package="300 mil [THT]"]
  S2 = SPDT Switch
  F3 = Fuse PCB mount [package=THT]
  F4 = Fuse PCB mount [package=THT]
  J2 = screw terminal, 2 pins
  D19 = Rectifier Diode [part_number=1N4001 package="Melf DO-214 AC [SMD]"]
  LED3 = LED - 5mm [color="Green (555nm)" current=20m package="5 mm [THT]"]
  R3 = Resistor [tolerance=±5% resistance=1k power=0.25 package=THT]
  D5 = Rectifier Diode [part_number=1N4001 package="300 mil [THT]"]
  D6 = Rectifier Diode [part_number=1N4001 package="300 mil [THT]"]
  S3 = SPDT Switch
  F5 = Fuse PCB mount [package=THT]
  F6 = Fuse PCB mount [package=THT]
  J3 = screw terminal, 2 pins
  LED4 = LED - 5mm [color="Green (555nm)" current=20m package="5 mm [THT]"]
  R4 = Resistor [tolerance=±5% resistance=1k power=0.25 package=THT]
  D7 = Rectifier Diode [part_number=1N4001 package="300 mil [THT]"]
  D8 = Rectifier Diode [part_number=1N4001 package="300 mil [THT]"]
  S4 = SPDT Switch
  F7 = Fuse PCB mount [package=THT]
  F8 = Fuse PCB mount [package=THT]
  J4 = screw terminal, 2 pins
  LED5 = LED - 5mm [color="Green (555nm)" current=20m package="5 mm [THT]"]
  R5 = Resistor [tolerance=±5% resistance=1k power=0.25 package=THT]
  D9 = Rectifier Diode [part_number=1N4001 package="300 mil [THT]"]
  D10 = Rectifier Diode [part_number=1N4001 package="300 mil [THT]"]
  S5 = SPDT Switch
  F9 = Fuse PCB mount [package=THT]
  F10 = Fuse PCB mount [package=THT]
  J5 = screw terminal, 2 pins
  LED6 = LED - 5mm [color="Green (555nm)" current=20m package="5 mm [THT]"]
  R6 = Resistor [tolerance=±5% resistance=1k power=0.25 package=THT]
  D11 = Rectifier Diode [part_number=1N4001 package="300 mil [THT]"]
  D12 = Rectifier Diode [part_number=1N4001 package="300 mil [THT]"]
  S6 = SPDT Switch
  F11 = Fuse PCB mount [package=THT]
  F12 = Fuse PCB mount [package=THT]
  J6 = screw terminal, 2 pins
  LED7 = LED - 5mm [color="Green (555nm)" current=20m package="5 mm [THT]"]
  R7 = Resistor [tolerance=±5% resistance=1k power=0.25 package=THT]
  D13 = Rectifier Diode [part_number=1N4001 package="300 mil [THT]"]
  D14 = Rectifier Diode [part_number=1N4001 package="300 mil [THT]"]
  S7 = SPDT Switch
  F13 = Fuse PCB mount [package=THT]
  F14 = Fuse PCB mount [package=THT]
  J7 = screw terminal, 2 pins
  LED8 = LED - 5mm [color="Green (555nm)" current=20m package="5 mm [THT]"]
  R8 = Resistor [tolerance=±5% resistance=1k power=0.25 package=THT]
  D15 = Rectifier Diode [part_number=1N4001 package="300 mil [THT]"]
  D16 = Rectifier Diode [part_number=1N4001 package="300 mil [THT]"]
  S8 = SPDT Switch
  F15 = Fuse PCB mount [package=THT]
  F16 = Fuse PCB mount [package=THT]
  J8 = screw terminal, 2 pins
  D22 = Rectifier Diode [part_number=1N4001 package="Melf DO-214 AC [SMD]"]
  D24 = Rectifier Diode [part_number=1N4001 package="Melf DO-214 AC [SMD]"]
  D26 = Rectifier Diode [part_number=1N4001 package="Melf DO-214 AC [SMD]"]
  D28 = Rectifier Diode [part_number=1N4001 package="Melf DO-214 AC [SMD]"]
  D30 = Rectifier Diode [part_number=1N4001 package="Melf DO-214 AC [SMD]"]
  D32 = Rectifier Diode [part_number=1N4001 package="Melf DO-214 AC [SMD]"]
  D20 = Rectifier Diode [part_number=1N4001 package="Melf DO-214 AC [SMD]"]
  D21 = Rectifier Diode [part_number=1N4001 package="Melf DO-214 AC [SMD]"]
  D23 = Rectifier Diode [part_number=1N4001 package="Melf DO-214 AC [SMD]"]
  D25 = Rectifier Diode [part_number=1N4001 package="Melf DO-214 AC [SMD]"]
  D27 = Rectifier Diode [part_number=1N4001 package="Melf DO-214 AC [SMD]"]
  D29 = Rectifier Diode [part_number=1N4001 package="Melf DO-214 AC [SMD]"]
  D31 = Rectifier Diode [part_number=1N4001 package="Melf DO-214 AC [SMD]"]
  RY10 = RELAY [package=relay-t9a]
  S10 = SPDT Switch
  F1_2 = female pin header, 2 pins [form="♀ (female)"]
  S9 = SPDT Switch
  U7 = Voltage Regulator - 5V [package="TO220 [THT]"]
  C1_2 = Ceramic Capacitor [capacitance=1µF voltage=35V package="100 mil [THT, multilayer]"]
  C2_2 = Ceramic Capacitor [capacitance=1µF voltage=35V package="100 mil [THT, multilayer]"]
  C3 = Ceramic Capacitor [capacitance=1µF voltage=35V package="100 mil [THT, multilayer]"]
  C4 = Ceramic Capacitor [capacitance=1µF voltage=35V package="100 mil [THT, multilayer]"]
  C5 = Ceramic Capacitor [capacitance=1µF voltage=35V package="100 mil [THT, multilayer]"]
  ESP32 = ESP32-38PinWide [part_number=ESP32-38PinWide]
  ‎TB67H410 = Motor driver [part_number=TB67H410 package=THT]
  R30 = Resistor [tolerance=±5% resistance=0.20 package="2512 [SMD]"]
  D40 = Rectifier Diode [part_number=1N4001 package="Melf DO-214 AC [SMD]"]
  D41 = Rectifier Diode [part_number=1N4001 package="Melf DO-214 AC [SMD]"]
  R18 = Resistor [tolerance=±5% power=0.25 resistance=1k package=THT]
  R19 = Resistor [tolerance=±5% power=0.25 resistance=1k package=THT]
  R9 = Resistor [tolerance=±5% power=0.25 resistance=1k package=THT]
  R10 = Resistor [tolerance=±5% power=0.25 resistance=1k package=THT]
  R11 = Resistor [tolerance=±5% power=0.25 resistance=1k package=THT]
  F17 = Resettable Fuse PTC [package=ptc]
  R43 = Resistor [tolerance=±5% power=0.25 resistance=6.8k package=THT]
  C10 = Ceramic Capacitor [capacitance=27pF voltage=35V package="100 mil [THT, multilayer]"]
  C6 = Electrolytic Capacitor [capacitance=0.1mF voltage=35V package="100 mil [THT, electrolytic]"]
  C8 = Ceramic Capacitor [capacitance=100nF voltage=35V package="100 mil [THT, multilayer]"]
  R27 = Resistor [tolerance=±5% power=0.25 resistance=47 package=THT]
  R26 = Resistor [tolerance=±5% power=0.25 resistance=47 package=THT]
  R25 = Resistor [tolerance=±5% power=0.25 resistance=47 package=THT]
  J0 = Resistor [tolerance=±5% power=0.25 resistance=47 package=THT]
  J5_2 = Screw terminal - 2 pins [package=THT]
  12V_Sig_Gnd = screw terminal, 3 pins
  Wifi = LED - 5mm [color="Blue (505nm)" current=0.030 package="5 mm [THT]"]
  - = mystery part, 9 pins [chip_label=?]
  IC3 = SO16 [chip_label=IC package=SO]
  MCP23017 = MCP23017 [package=THT]
  C11 = Ceramic Capacitor [capacitance=100nF voltage=35V package="100 mil [THT, multilayer]"]
  12V_A0_A1_GND = screw terminal, 4 pins
  C12 = Ceramic Capacitor [capacitance=100nF voltage=35V package="100 mil [THT, multilayer]"]
  C13 = Ceramic Capacitor [capacitance=100nF voltage=35V package="100 mil [THT, multilayer]"]
  C14 = Ceramic Capacitor [capacitance=100nF voltage=35V package="100 mil [THT, multilayer]"]
  R35 = Resistor [tolerance=±5% power=0.25 resistance=1.5k package=THT]
  R36 = Resistor [tolerance=±5% power=0.25 resistance=1.5k package=THT]
  J1_2 = Screw terminal - 3 pins [package=THT]
  TBD62084 = SOIC - 18 pins [part_number=TBD62084 package=SOIC-18]
  IC5 = SO18W [chip_label=IC package=SO(w)]
  DOGL1 = DOGL128 [part_number="EA DOGL128E-6"]
  R20 = Resistor [tolerance=±5% power=0.25 resistance=1k package=THT]
  R13 = Resistor [tolerance=±5% power=0.25 resistance=1k package=THT]
  R29 = Resistor [tolerance=±5% power=0.5W resistance=220 package=THT]
  ADS1115 = Adafruit ADS1115 16-Bit ADC [part_number=1085]
  RY1 = SPDT relay [part_number=RT package=THT]
  D33 = Rectifier Diode [part_number=1N4001 package="300 mil [THT]"]
  D34 = Rectifier Diode [part_number=1N4001 package="300 mil [THT]"]
  D35 = Rectifier Diode [part_number=1N4001 package="300 mil [THT]"]
  D36 = Rectifier Diode [part_number=1N4001 package="300 mil [THT]"]
  D37 = Rectifier Diode [part_number=1N4001 package="300 mil [THT]"]
  Z50 = Rectifier Diode [part_number=1N4742 package="300 mil [THT]"]
  D42 = Rectifier Diode [part_number=1N4001 package="300 mil [THT]"]
  F18 = female pin header, 2 pins [form="♀ (female)"]
  R47 = Resistor [tolerance=±5% power=0.25 resistance=10k package=THT]
  R46 = Resistor [tolerance=±5% power=0.25 resistance=10k package=THT]
  RY2 = SPDT relay [part_number=RT package=THT]
  RY3 = SPDT relay [part_number=RT package=THT]
  RY4 = SPDT relay [part_number=RT package=THT]
  RY5 = SPDT relay [part_number=RT package=THT]
  RY6 = SPDT relay [part_number=RT package=THT]
  RY7 = SPDT relay [part_number=RT package=THT]
  RY8 = SPDT relay [part_number=RT package=THT]
  J10 = Generic double row female header - 6 pins [form="♀ (female)" package=THT]
  R15 = Resistor [tolerance=±5% power=0.25 resistance=1k package=THT]
  R16 = Resistor [tolerance=±5% power=0.25 resistance=1k package=THT]
  R17 = Resistor [tolerance=±5% power=0.25 resistance=1k package=THT]
  R38 = Resistor [tolerance=±5% power=0.25 resistance=1.5k package=THT]
  R39 = Resistor [tolerance=±5% power=0.25 resistance=1.5k package=THT]
  R40 = Resistor [tolerance=±5% power=0.25 resistance=1.5k package=THT]
  R41 = Resistor [tolerance=±5% power=0.25 resistance=1.5k package=THT]
  D51 = BAV99 [package=sot23]
  R45 = Resistor [tolerance=±5% power=0.25 resistance=10k package=THT]
  C15 = Electrolytic Capacitor [capacitance=0.1mF voltage=6.3V package="100 mil [THT, electrolytic]"]
  D52 = BAV99 [package=sot23]
  Pwr = LED - 5mm [color="Red (633nm)" current=0.030 package="5 mm [THT]"]
  Sig = LED - 5mm [color="Yellow (592nm)" current=0.030 package="5 mm [THT]"]
  R51 = Resistor [tolerance=±5% power=0.25 resistance=1.2k package=THT]
  R50 = Resistor [tolerance=±5% power=0.25 resistance=1.2k package=THT]

nets:
  N1: S1.O, F1.pin1, RY1.1NC
  N2: S1.P, D18.cathode
  N3: S1.S, F2.pin1, RY1.1NO
  N4: F2.pin2, LED1.anode, D2.cathode, J1.pin2, IC3.9
  N5: LED1.cathode, R1.Pin_1
  GND: D2.anode, R1.Pin_0, D1.anode, RY9.COIL2, C1.-, C2.-, R2.Pin_0, D3.anode, D4.anode, R3.Pin_0, D5.anode, D6.anode, R4.Pin_0, D7.anode, D8.anode, R5.Pin_0, D9.anode, D10.anode, R6.Pin_0, D11.anode, D12.anode, R7.Pin_0, D13.anode, D14.anode, R8.Pin_0, D15.anode, D16.anode, RY10.COIL2, S9.P, U7.GND, C1_2.1, C2_2.1, C3.1, C4.1, C5.1, ESP32.GND, ‎TB67H410.GND, ‎TB67H410.PWMB, ‎TB67H410.INB1, ‎TB67H410.INB2, R9.Pin_1, R10.Pin_1, R11.Pin_1, C10.0, C6.-, C8.0, 12V_Sig_Gnd.pin1, Wifi.cathode, -.pin1, MCP23017.V-, MCP23017.A0, MCP23017.A1, MCP23017.A2, C11.0, 12V_A0_A1_GND.pin4, C12.1, C13.0, C14.1, J1_2.pin1, TBD62084.GND, IC5.9, DOGL1.VSS, ADS1115.GND, D36.anode, D37.anode, Z50.anode, R47.Pin_0, J10.pin1, J10.pin2, R40.Pin_1, R41.Pin_1, D51.A1, C15.-, D52.A1
  N6: D1.cathode, F1.pin2, J1.pin1
  N7: RY9.COIL1, S10.O, D35.anode, D37.cathode
  N8: RY9.MAIN, RY10.MAIN, J1_2.pin2
  N9: RY9.NO, D17.anode, D19.anode, D21.anode, D23.anode, D25.anode, D27.anode, D29.anode, D31.anode, D40.anode, TBD62084.VCC, IC5.10
  N10: C1.+, U7.input_voltage, F17.2, R29.Pin_0, D34.cathode, D35.cathode, F18.pin1
  VIN: C2.+, U7.output_voltage, ESP32.VIN, ‎TB67H410.VCC, ‎TB67H410.HBMODE, ‎TB67H410.TBLKAB, R43.Pin_0, C8.1, R27.Pin_0, R26.Pin_0, R25.Pin_0, J10.pin6
  N11: D17.cathode, RY1.1COM, RY1.A2
  N12: D18.anode, D22.anode, D24.anode, D26.anode, D28.anode, D30.anode, D32.anode, D20.anode, RY10.NO, D41.anode
  N13: LED2.cathode, R2.Pin_1
  N14: LED2.anode, D4.cathode, F4.pin2, J2.pin2, IC3.10
  N15: D3.cathode, F3.pin2, J2.pin1
  N16: S2.O, F3.pin1, RY2.1NC
  N17: S2.P, D20.cathode
  N18: S2.S, F4.pin1, RY2.1NO
  N19: D19.cathode, RY2.1COM, RY2.A2
  N20: LED3.cathode, R3.Pin_1
  N21: LED3.anode, D6.cathode, F6.pin2, J3.pin2, IC3.11
  N22: D5.cathode, F5.pin2, J3.pin1
  N23: S3.O, F5.pin1, RY3.1NC
  N24: S3.P, D22.cathode
  N25: S3.S, F6.pin1, RY3.1NO
  N26: LED4.cathode, R4.Pin_1
  N27: LED4.anode, D8.cathode, F8.pin2, J4.pin2, IC3.12
  N28: D7.cathode, F7.pin2, J4.pin1
  N29: S4.O, F7.pin1, RY4.1NC
  N30: S4.P, D24.cathode
  N31: S4.S, F8.pin1, RY4.1NO
  N32: LED5.cathode, R5.Pin_1
  N33: LED5.anode, D10.cathode, F10.pin2, J5.pin2, IC3.13
  N34: D9.cathode, F9.pin2, J5.pin1
  N35: S5.O, F9.pin1, RY5.1NC
  N36: S5.P, D26.cathode
  N37: S5.S, F10.pin1, RY5.1NO
  N38: LED6.cathode, R6.Pin_1
  N39: LED6.anode, D12.cathode, F12.pin2, J6.pin2, IC3.14
  N40: D11.cathode, F11.pin2, J6.pin1
  N41: S6.O, F11.pin1, RY6.1NC
  N42: S6.P, D28.cathode
  N43: S6.S, F12.pin1, RY6.1NO
  N44: LED7.cathode, R7.Pin_1
  N45: LED7.anode, D14.cathode, F14.pin2, J7.pin2, IC3.15
  N46: D13.cathode, F13.pin2, J7.pin1
  N47: S7.O, F13.pin1, RY7.1NC
  N48: S7.P, D30.cathode
  N49: S7.S, F14.pin1, RY7.1NO
  N50: LED8.cathode, R8.Pin_1
  N51: LED8.anode, D16.cathode, F16.pin2, J8.pin2, IC3.16
  N52: D15.cathode, F15.pin2, J8.pin1
  N53: S8.O, F15.pin1, RY8.1NC
  N54: S8.P, D32.cathode
  N55: S8.S, F16.pin1, RY8.1NO
  N56: D21.cathode, RY3.1COM, RY3.A2
  N57: D23.cathode, RY4.1COM, RY4.A2
  N58: D25.cathode, RY5.1COM, RY5.A2
  N59: D27.cathode, RY6.1COM, RY6.A2
  N60: D29.cathode, RY7.1COM, RY7.A2
  N61: D31.cathode, RY8.1COM, RY8.A2
  N62: RY10.COIL1, S10.S, D34.anode, D36.cathode, R46.Pin_0
  N63: S10.P, D33.cathode
  N64: F1_2.pin1, D33.anode
  N65: F1_2.pin2, J1_2.pin3
  N66: S9.O, ESP32.GPIO32, R18.Pin_1
  N67: S9.S, ESP32.GPIO33, R19.Pin_1
  N68: C1_2.0, DOGL1.V0
  N69: C2_2.0, DOGL1.V1
  N70: C3.0, DOGL1.V2
  N71: C4.0, DOGL1.V3
  N72: C5.0, DOGL1.V4
  VDD: ESP32.3.3, ‎TB67H410.VREF, R18.Pin_0, R19.Pin_0, MCP23017.V+, MCP23017.RST, C11.1, R35.Pin_1, R36.Pin_1, DOGL1.VDD2, DOGL1.VDD, ADS1115.VCC, R15.Pin_1, R16.Pin_1, R17.Pin_1, D51.C2, C15.+, D52.C2
  N73: ESP32.GPIO36, R47.Pin_1, R46.Pin_1, D51.COM
  N74: ESP32.GPIO34, R45.Pin_1, D52.COM
  N75: ESP32.GPIO25, ‎TB67H410.PWMA, R9.Pin_0
  N76: ESP32.GPIO26, ‎TB67H410.INA2, R10.Pin_0
  N77: ESP32.GPIO27, ‎TB67H410.INA1, R11.Pin_0
  N78: ESP32.GPIO13, R13.Pin_0
  N79: ESP32.GPIO15, J10.pin3, R15.Pin_0
  N80: ESP32.GPIO2, DOGL1.CS1B
  N81: ESP32.GPIO4, DOGL1.RST
  N82: ESP32.GPIO16, J10.pin4, R16.Pin_0
  N83: ESP32.GPIO17, J10.pin5, R17.Pin_0
  N84: ESP32.GPIO5, DOGL1.A0
  N85: ESP32.GPIO18, DOGL1.SCL
  N86: ESP32.GPIO21, MCP23017.SDA, R35.Pin_0, ADS1115.SDA
  N87: ESP32.GPIO22, MCP23017.SCL, R36.Pin_0, ADS1115.SCL
  N88: ESP32.GPIO23, DOGL1.SI
  N89: ‎TB67H410.OUTB-, ‎TB67H410.OUTB+, J5_2.pin1
  N90: ‎TB67H410.RSB, ‎TB67H410.RSA, R30.Pin_1
  N91: ‎TB67H410.VM, R30.Pin_0, D40.cathode, D41.cathode, C6.+
  N92: ‎TB67H410.OSCM, R43.Pin_1, C10.1
  N93: ‎TB67H410.OUTA+, ‎TB67H410.OUTA-, J5_2.pin2
  N94: F17.1, 12V_Sig_Gnd.pin3, R20.Pin_0, Sig.anode, R51.Pin_1
  N95: R27.Pin_1, DOGL1.A3
  N96: R26.Pin_1, DOGL1.A2
  N97: R25.Pin_1, DOGL1.A1
  N98: J0.Pin_0, Pwr.cathode
  N99: J0.Pin_1, DOGL1.C1, DOGL1.C2, DOGL1.C3
  N100: 12V_Sig_Gnd.pin2, R20.Pin_1, R45.Pin_0, R50.Pin_1
  N101: Wifi.anode, R13.Pin_1
  N102: -.pin2, IC3.1, MCP23017.MCP_D15
  N103: -.pin3, IC3.2, MCP23017.MCP_D14
  N104: -.pin4, IC3.3, MCP23017.MCP_D13
  N105: -.pin5, IC3.4, MCP23017.MCP_D12
  N106: -.pin6, IC3.5, MCP23017.MCP_D11
  N107: -.pin7, IC3.6, MCP23017.MCP_D10
  N108: -.pin8, IC3.7, MCP23017.MCP_D9
  N109: -.pin9, IC3.8, MCP23017.MCP_D8
  N110: MCP23017.MCP_D0, TBD62084.IN1, IC5.1
  N111: MCP23017.MCP_D1, TBD62084.IN2, IC5.2
  N112: MCP23017.MCP_D2, TBD62084.IN3, IC5.3
  N113: MCP23017.MCP_D3, TBD62084.IN4, IC5.4
  N114: MCP23017.MCP_D4, TBD62084.IN5, IC5.5
  N115: MCP23017.MCP_D5, TBD62084.IN6, IC5.6
  N116: MCP23017.MCP_D6, TBD62084.IN7, IC5.7
  N117: MCP23017.MCP_D7, TBD62084.IN8, IC5.8
  N118: 12V_A0_A1_GND.pin1, C14.0, D42.cathode
  N119: 12V_A0_A1_GND.pin2, R38.Pin_1
  N120: 12V_A0_A1_GND.pin3, R39.Pin_1
  N121: C12.0, ADS1115.AIN1, R39.Pin_0, R41.Pin_0
  N122: C13.1, ADS1115.AIN0, R38.Pin_0, R40.Pin_0
  N123: TBD62084.OUT8, IC5.11, RY8.A1
  N124: TBD62084.OUT7, IC5.12, RY7.A1
  N125: TBD62084.OUT6, IC5.13, RY6.A1
  N126: TBD62084.OUT5, IC5.14, RY5.A1
  N127: TBD62084.OUT4, IC5.15, RY4.A1
  N128: TBD62084.OUT3, IC5.16, RY3.A1
  N129: TBD62084.OUT2, IC5.17, RY2.A1
  N130: TBD62084.OUT1, IC5.18, RY1.A1
  N131: DOGL1.VOUT, R29.Pin_1, Z50.cathode
  N132: D42.anode, F18.pin2
  N133: Pwr.anode, R51.Pin_0
  N134: Sig.cathode, R50.Pin_0

notes:
  Rev E
  Copyright Reuben Rissler 2023
  License GPLv3 PCB design
  +
  Bat+
  WH
  GY
  BR
  GN
  BU
  1
  Bat-
  Ign
  9
  2
  10
  11
  3
  4
  12
  5
  13
  14
  6
  15
  7
  16
  8
  YL
  OG
  PR

custom parts:
  SPDT Switch: SPDT Switch Mini toggle switch
  Fuse PCB mount: A PCB mount fuse with 200 mil spacing.
  RELAY: SPST 30A relay
  Rectifier Diode: A DO-214AB smd rectifier diode
  Voltage Regulator - 5V: 5V DC Voltage Regulator
  ESP32-38PinWide: Generic 38-Pin ESP32 with wide format made by Espressif. This part uses SVG elements from various sources on the web, thanks to all.
  Motor driver: A quad half bridge driver capable of driving single or dual DC motors bidirectionally. With 24 pins on a 300mil inline pin header footprint. It can drive up to two 2.5A motors or one 5A motor.
  MCP23017: A 16 bit I2C port expander.
  Screw terminal - 3 pins: Wire clamp terminal with 3 pins
  SOIC - 18 pins: 8 channel transistor array
  DOGL128: A graphic display with an LED backlight
  Adafruit ADS1115 16-Bit ADC: For microcontrollers without an analog-to-digital converter or when you want a higher-precision ADC, the ADS1115 provides 16-bit precision at 860 samples/second over I2C. The chip can be configured as 4 single-ended input channels, or two differential channels. As a nice bonus, it even includes a programmable gain amplifier, up to x16, to help boost up smaller single/differential signals to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
  SPDT relay: A SPDT 8A relay
  Generic double row female header - 6 pins: Generic double row staggered female header
